// Logisim project cpu28(2.25)_流水中断.circ as structural Verilog: 23 circuits, main circuit ◇单周期MIPS
module \单周期MIPS  (
  input  IR1,
  input  IR2,
  input  IR3,
  output RegWrite,
  output MemWrite,
  output [31:0] PC,
  output [31:0] IR,
  output [31:0] RDin,
  output [31:0] MDin,
  output [31:0] LedData
);

  wire and_1_out, and_4_out, and_5_out, and_6_out, BGTZ, CLK, comparator_1_eq, comparator_2_gt, display, Go,
       IR1_t, IR2_t, IR3_t, IRA, IRB, IRC, JAL, JMP, JR, MemToReg, mips_alu_1_equal, not_1_out, not_2_out,
       not_3_out, not_4_out, pause, RST, SB, SignedExt, SUBU, Syscall, W1, W2, W3, XOR,
       \单周期硬布线控制器_1_alu_src , \单周期硬布线控制器_1_beq , \单周期硬布线控制器_1_bne , \单周期硬布线控制器_1_regdst , \是否跳转 ;
  wire [1:0] bytechoose;
  wire [3:0] \单周期硬布线控制器_1_alu_op ;
  wire [4:0] bit_extender_3_out, multiplexer_4_out, multiplexer_6_out, multiplexer_8_out, multiplexer_10_out,
       multiplier_1_out;
  wire [7:0] demultiplexer_1_out0, demultiplexer_1_out1, demultiplexer_1_out2, demultiplexer_1_out3;
  wire [9:0] mips_alu_1_result;
  wire [15:0] \总周期数 , \无条件分支数 , \条件分支成功数 ;
  wire [27:0] adder_1_out_2;
  wire [31:0] adder_2_out, and_7_out, and_8_out, bit_extender_1_out, bit_extender_2_out, multiplexer_1_out,
       multiplexer_2_out, multiplexer_3_out, multiplexer_7_out, multiplexer_9_out, multiplexer_11_out,
       not_5_out, or_5_out, R1, R2, ram_1_data, shifter_1_out, shifter_2_out;
  wire [31:12] mips_alu_1_result_2;
  wire [31:28] adder_1_out;

  Clock #(.highDuration(1), .lowDuration(1)) clock_1 (.out(CLK));
  Button _1 (.out(IRA));
  Button _2 (.out(IRB));
  Button _3 (.out(IRC));
  Button \u_继续运行  (.out(Go));
  LED #(.active("true")) led_1 (.in(W1));
  LED #(.active("true")) led_2 (.in(W2));
  LED #(.active("true")) led_3 (.in(W3));
  Multiplexer #(.select(1), .width(32), .disabled("Z"), .enable("false")) multiplexer_1 (
    .in0({adder_1_out, IR[25:0], 2'b00}), .in1(R2), .out(multiplexer_1_out), .sel(JR));
  Multiplexer #(.select(1), .width(32), .disabled("Z"), .enable("true")) multiplexer_2 (
    .in0({adder_1_out, adder_1_out_2}), .in1(adder_2_out), .out(multiplexer_2_out), .sel(\是否跳转 ));  // open: en
  Hex_Digit_Display hex_digit_display_1 (.value(LedData[31:28]));  // open: dp
  Counter #(.width(16), .max('hffff), .ongoal("wrap"), .trigger("rising"), .behavior("old")) counter_1 (
    .count(not_2_out), .Q(\总周期数 ), .clk(CLK), .clr(RST));  // open: load, D, carry, preset
  Multiplexer #(.select(1), .width(32), .disabled("Z"), .enable("false")) multiplexer_3 (
    .in0(multiplexer_2_out), .in1(multiplexer_1_out), .out(multiplexer_3_out), .sel(JMP));
  Hex_Digit_Display hex_digit_display_2 (.value(LedData[27:24]));  // open: dp
  Hex_Digit_Display hex_digit_display_3 (.value(LedData[23:20]));  // open: dp
  not not_1 (not_1_out, Go);
  Register #(.width(32), .trigger("rising"), .Select("low")) u_PC (
    .D(multiplexer_3_out), .en(not_2_out), .Q(PC), .clk(CLK), .clr(RST));
  Hex_Digit_Display hex_digit_display_4 (.value(LedData[15:12]));  // open: dp
  Hex_Digit_Display hex_digit_display_5 (.value(LedData[19:16]));  // open: dp
  // Mips_Probe mips_probe_1: pin names not known; wires that end beside it: IR
  not not_2 (not_2_out, and_1_out);
  and and_1 (and_1_out, not_1_out, pause);
  Adder #(.width(32)) adder_1 (.a(PC), .b(32'h4), .out({adder_1_out, adder_1_out_2}));  // open: cin, cout
  Adder #(.width(32)) adder_2 (
    .a({adder_1_out, adder_1_out_2}), .b(shifter_1_out), .out(adder_2_out));  // open: cin, cout
  Hex_Digit_Display hex_digit_display_6 (.value(LedData[11:8]));  // open: dp
  Hex_Digit_Display hex_digit_display_7 (.value(LedData[7:4]));  // open: dp
  // Probe on \总周期数 
  Hex_Digit_Display hex_digit_display_8 (.value(LedData[3:0]));  // open: dp
  Comparator #(.width(32), .mode("twosComplement")) comparator_1 (
    .a(R1), .b(32'h22), .eq(comparator_1_eq));  // open: gt, lt
  ROM #(.addrWidth(10), .dataWidth(32), .Select("high")) rom_1 (.addr(PC[11:2]), .data(IR));
  not not_3 (not_3_out, comparator_1_eq);
  or or_1 (IR1_t, IR1, IRA);
  and and_2 (pause, Syscall, not_3_out);
  and and_3 (display, comparator_1_eq, Syscall);
  Register #(.width(32), .trigger("rising"), .Select("low")) register_1 (
    .D(R2), .en(display), .Q(LedData), .clk(CLK), .clr(RST));
  ps1 ps1_1 (
    .OP0(IR[26]), .OP1(IR[27]), .OP2(IR[28]), .OP3(IR[29]), .OP4(IR[30]), .OP5(IR[31]), .F0(IR[0]),
    .F1(IR[1]), .F2(IR[2]), .F3(IR[3]), .F4(IR[4]), .F5(IR[5]), .bgtz(BGTZ), .XOR(XOR), .SB(SB), .SUBU(SUBU));
  or or_2 (IR2_t, IR2, IRB);
  // Probe on IR
  \单周期硬布线控制器  \u_单周期硬布线控制器_1  (
    .Func(IR[5:0]), .OP(IR[31:26]), .ALU_OP(\单周期硬布线控制器_1_alu_op ), .MemToReg(MemToReg), .MemWrite(MemWrite),
    .ALU_SRC(\单周期硬布线控制器_1_alu_src ), .RegWrite(RegWrite), .SysCALL(Syscall), .SignedExt(SignedExt),
    .RegDst(\单周期硬布线控制器_1_regdst ), .JR(JR), .JMP(JMP), .Beq(\单周期硬布线控制器_1_beq ), .JAL(JAL),
    .Bne(\单周期硬布线控制器_1_bne ));
  Multiplexer #(.select(1), .width(5), .disabled("Z"), .enable("false")) multiplexer_4 (
    .in0(IR[25:21]), .in1(5'b00100), .out(multiplexer_4_out), .sel(Syscall));
  assign bit_extender_1_out = {{16{1'b0}}, IR[15:0]};  // Bit_Extender bit_extender_1
  assign bit_extender_2_out = {{16{IR[15]}}, IR[15:0]};  // Bit_Extender bit_extender_2
  Multiplexer #(.select(1), .width(32), .disabled("Z"), .enable("false")) multiplexer_5 (
    .in0(multiplexer_7_out), .in1({adder_1_out, adder_1_out_2}), .out(RDin), .sel(JAL));
  or or_3 (IR3_t, IR3, IRC);
  Multiplexer #(.select(1), .width(5), .disabled("Z"), .enable("true")) multiplexer_6 (
    .in0(IR[20:16]), .in1(IR[15:11]), .out(multiplexer_6_out), .sel(\单周期硬布线控制器_1_regdst ));  // open: en
  Multiplexer #(.select(1), .width(32), .disabled("Z"), .enable("false")) multiplexer_7 (
    .in0({mips_alu_1_result_2, mips_alu_1_result, bytechoose}), .in1(ram_1_data), .out(multiplexer_7_out),
    .sel(MemToReg));
  Multiplexer #(.select(1), .width(5), .disabled("Z"), .enable("false")) multiplexer_8 (
    .in0(multiplexer_6_out), .in1({5{1'b1}}), .out(multiplexer_8_out), .sel(JAL));
  Multiplexer #(.select(1), .width(32), .disabled("Z"), .enable("false")) multiplexer_9 (
    .in0(bit_extender_1_out), .in1(bit_extender_2_out), .out(multiplexer_9_out), .sel(SignedExt));
  Counter #(.width(16), .max('hffff), .ongoal("wrap"), .trigger("rising"), .behavior("old")) counter_2 (
    .count(JMP), .Q(\无条件分支数 ), .clk(CLK), .clr(RST));  // open: load, D, carry, preset
  Multiplexer #(.select(1), .width(5), .disabled("Z"), .enable("false")) multiplexer_10 (
    .in0(IR[20:16]), .in1(5'b00010), .out(multiplexer_10_out), .sel(Syscall));
  MIPS_Regifile mips_regifile_1 (
    .Din(RDin), .Clk(CLK), .R1(R1), .R2(R2), .WE(RegWrite), .W_num(multiplexer_8_out),
    .R1_num(multiplexer_10_out), .R2_num(multiplexer_4_out));
  or or_4 (\是否跳转 , and_5_out, and_4_out, and_6_out);
  and and_4 (and_4_out, not_4_out, \单周期硬布线控制器_1_bne );
  and and_5 (and_5_out, \单周期硬布线控制器_1_beq , mips_alu_1_equal);
  not not_4 (not_4_out, mips_alu_1_equal);
  Shifter #(.width(32), .shift("ll")) shifter_1 (.in(bit_extender_2_out), .\dist (5'b00010), .out(shifter_1_out));
  Multiplexer #(.select(1), .width(32), .disabled("Z"), .enable("false")) multiplexer_11 (
    .in0(R1), .in1(multiplexer_9_out), .out(multiplexer_11_out), .sel(\单周期硬布线控制器_1_alu_src ));
  Counter #(.width(16), .max('hffff), .ongoal("wrap"), .trigger("rising"), .behavior("old")) counter_3 (
    .count(\是否跳转 ), .Q(\条件分支成功数 ), .clk(CLK), .clr(RST));  // open: load, D, carry, preset
  and and_6 (and_6_out, BGTZ, comparator_2_gt);
  MIPS_ALU mips_alu_1 (
    .X(R2), .Y(multiplexer_11_out), .AluOP(\单周期硬布线控制器_1_alu_op ), .Equal(mips_alu_1_equal),
    .Result({mips_alu_1_result_2, mips_alu_1_result, bytechoose}), .shamt(IR[10:6]));  // open: Result_2
  assign and_7_out = R1 & 32'hff;  // AND_Gate and_7, 32 bits wide
  assign bit_extender_3_out = {{3{1'b0}}, bytechoose};  // Bit_Extender bit_extender_3
  Demultiplexer #(.select(2), .width(8), .tristate("false"), .disabled("Z"), .enable("false")) demultiplexer_1 (
    .out0(demultiplexer_1_out0), .out1(demultiplexer_1_out1), .out2(demultiplexer_1_out2),
    .out3(demultiplexer_1_out3), .in({8{1'b1}}), .sel(bytechoose));
  Comparator #(.width(32), .mode("twosComplement")) comparator_2 (
    .a(R2), .b({32{1'b0}}), .gt(comparator_2_gt));  // open: eq, lt
  Shifter #(.width(32), .shift("ll")) shifter_2 (.in(and_7_out), .\dist (multiplier_1_out), .out(shifter_2_out));
  Multiplier #(.width(5)) multiplier_1 (
    .a(5'b01000), .b(bit_extender_3_out), .out(multiplier_1_out));  // open: cin, cout
  assign or_5_out = shifter_2_out | and_8_out;  // OR_Gate or_5, 32 bits wide
  assign and_8_out = ram_1_data & not_5_out;  // AND_Gate and_8, 32 bits wide
  assign not_5_out = ~{demultiplexer_1_out3, demultiplexer_1_out2, demultiplexer_1_out1, demultiplexer_1_out0};  // NOT_Gate not_5, 32 bits wide
  Multiplexer #(.select(1), .width(32), .disabled("Z"), .enable("false")) multiplexer_12 (
    .in0(R1), .in1(or_5_out), .out(MDin), .sel(SB));
  RAM #(.addrWidth(10), .dataWidth(32), .bus("separate"), .Select("high")) ram_1 (
    .addr(mips_alu_1_result), .din(MDin), .data(ram_1_data), .str(MemWrite), .clk(CLK), .ld(1'b1), .clr(RST));  // open: sel

  // Other names for the same wires on the sheet: Func[5:0] = IR[5:0]; OP[5:0] = IR[31:26]

  // Notes on the sheet:
  //   中断源
  //   J、JAL
  //   JR
  //   中断等待指示
  //   总复位信号应将除ROM以外所有存储组件全部清零
  //   数码管输出
  //   beq和bne跳转的话，在pc+1的基础上加上偏移量
  //   新增加的指令：SUBU、XOR、SB、BGTZ
  //   数码管输出应该用寄存器锁存，否则显示数据只能一闪而过
  //   指令存储器
  //   contents of rom_1 (hex, n*v repeats v):
  //   20090000 200b0020 20110000 20120001 a1310000 112020 20020022 c 2328820 21290001 216bffff 1560fff8
  //   200b0008 20090000 8d310000 112020 20020022 c 21290004 216bffff 1560fff9 2002000a c
  //   指令字
  //   OP
  //   Func
  //   rs
  //   rt
  //   rd
  //   Beq
  //   JMP
  //   JR
  //   Bne
  //   OP
  //   JAL
  //   Func
  //   Syscall
  //   MemToReg
  //   MemWrite
  //   AluOP
  //   AluSrcB
  //   RegWrite
  //   RegDst
  //   ANDI、ORI
  //   ADDI、ADDIU、SLTI、LW、SW
  //   为方便自动评测，需要输出PC，IR，寄存器堆写如数据RDin
  //   RAM写使能MemWrite、RAM写入数据MDin等信号
  //   sw指令读入数据存储器中
endmodule

// 单周期硬布线控制器
module \单周期硬布线控制器  (
  input  [5:0] OP,
  input  [5:0] Func,
  output [3:0] ALU_OP,
  output MemToReg,
  output MemWrite,
  output ALU_SRC,
  output RegWrite,
  output SysCALL,
  output SignedExt,
  output RegDst,
  output Beq,
  output Bne,
  output JR,
  output JMP,
  output JAL
);

  \运算控制器自动生成  \u_运算控制器自动生成_1  (
    .OP0(OP[0]), .OP1(OP[1]), .OP2(OP[2]), .OP3(OP[3]), .OP4(OP[4]), .OP5(OP[5]), .F0(Func[0]), .F1(Func[1]),
    .F2(Func[2]), .F3(Func[3]), .F4(Func[4]), .F5(Func[5]), .S0(ALU_OP[0]), .S1(ALU_OP[1]), .S2(ALU_OP[2]),
    .S3(ALU_OP[3]));
  \控制信号自动生成  \u_控制信号自动生成_1  (
    .OP0(OP[0]), .OP1(OP[1]), .OP2(OP[2]), .OP3(OP[3]), .OP4(OP[4]), .OP5(OP[5]), .F0(Func[0]), .F1(Func[1]),
    .F2(Func[2]), .F3(Func[3]), .F4(Func[4]), .F5(Func[5]), .MemToReg(MemToReg), .MemWrite(MemWrite),
    .ALU_SRC(ALU_SRC), .RegWrite(RegWrite), .SysCALL(SysCALL), .SignedExt(SignedExt), .RegDst(RegDst),
    .BEQ(Beq), .BNE(Bne), .JR(JR), .JMP(JMP), .JAL(JAL));

  // Other names for the same wires on the sheet: OP_CODE[5:0] = OP

  // Notes on the sheet:
  //   运算器控制器，根据指令生成运算器功能选择信号
  //   控制信号生成，产生数据通路需要的其他控制信号
endmodule

// 运算器控制器
module \运算控制器自动生成  (
  input  OP0,
  input  OP1,
  input  OP2,
  input  OP3,
  input  OP4,
  input  OP5,
  input  F0,
  input  F1,
  input  F2,
  input  F3,
  input  F4,
  input  F5,
  output S0,
  output S1,
  output S2,
  output S3
);

  wire and_1_out, and_2_out, and_3_out, and_4_out, and_5_out, and_6_out, and_7_out, and_8_out, and_9_out,
       and_10_out, and_11_out, and_12_out, and_13_out, and_14_out, and_15_out, and_16_out, and_17_out,
       and_18_out, and_19_out, and_20_out, and_21_out, and_22_out, and_23_out, and_24_out, and_25_out,
       and_26_out, and_27_out, and_28_out, and_29_out, and_30_out, and_31_out, and_32_out, and_33_out,
       and_34_out, and_35_out, and_36_out, and_37_out, and_38_out, and_39_out, and_40_out, not_1_out,
       not_2_out, not_3_out, not_4_out, not_5_out, not_6_out, not_7_out, not_8_out, not_9_out, not_10_out,
       not_11_out, not_12_out, not_13_out, not_14_out, not_15_out, not_16_out, not_17_out, not_18_out,
       not_19_out, not_20_out, not_21_out, not_22_out, not_23_out, not_24_out, not_25_out, not_26_out,
       not_27_out, not_28_out, not_29_out, not_30_out, not_31_out, not_32_out, not_33_out, not_34_out,
       not_35_out, not_36_out, not_37_out, not_38_out, not_39_out, not_40_out, not_41_out, not_42_out,
       not_43_out, not_44_out, not_45_out, not_46_out, not_47_out, not_48_out, not_49_out, not_50_out,
       not_51_out, not_52_out, not_53_out, not_54_out, not_55_out, not_56_out, not_57_out, not_58_out,
       not_59_out, not_60_out, not_61_out, not_62_out, not_63_out, not_64_out, not_65_out, not_66_out,
       not_67_out, not_68_out, not_69_out, not_70_out, not_71_out, not_72_out, not_73_out, not_74_out,
       not_75_out, not_76_out, not_77_out, not_78_out, not_79_out, not_80_out, not_81_out, not_82_out,
       not_83_out, not_84_out, not_85_out, not_86_out, not_87_out, not_88_out, not_89_out, not_90_out,
       not_91_out, not_92_out, not_93_out, not_94_out, not_95_out, not_96_out, not_97_out, not_98_out,
       not_99_out, not_100_out, not_101_out, not_102_out, not_103_out, not_104_out, not_105_out, not_106_out,
       not_107_out, not_108_out, not_109_out, not_110_out, not_111_out, not_112_out, not_113_out,
       not_114_out, not_115_out, not_116_out, not_117_out, not_118_out, not_119_out, not_120_out,
       not_121_out, not_122_out, not_123_out, not_124_out, not_125_out, not_126_out, not_127_out,
       not_128_out, not_129_out, not_130_out, not_131_out, not_132_out, not_133_out, not_134_out,
       not_135_out, not_136_out, not_137_out, not_138_out, not_139_out, not_140_out, not_141_out,
       not_142_out, not_143_out, not_144_out, not_145_out, not_146_out, not_147_out, not_148_out,
       not_149_out, not_150_out, not_151_out, not_152_out, not_153_out, not_154_out, not_155_out,
       not_156_out, not_157_out, not_158_out, not_159_out, not_160_out, not_161_out, not_162_out,
       not_163_out, not_164_out, not_165_out, not_166_out, not_167_out, not_168_out, not_169_out,
       not_170_out, not_171_out, not_172_out, not_173_out, not_174_out, not_175_out, not_176_out,
       not_177_out, not_178_out, not_179_out, not_180_out, not_181_out, not_182_out, not_183_out,
       not_184_out, not_185_out, not_186_out, not_187_out, not_188_out, not_189_out, not_190_out,
       not_191_out, not_192_out, not_193_out, not_194_out, not_195_out, not_196_out, not_197_out,
       not_198_out, not_199_out, not_200_out, not_201_out, not_202_out, not_203_out, not_204_out,
       not_205_out, not_206_out, not_207_out, not_208_out, not_209_out, not_210_out, not_211_out,
       not_212_out, not_213_out, not_214_out, not_215_out, not_216_out, not_217_out, not_218_out,
       not_219_out, not_220_out, not_221_out, not_222_out, not_223_out, not_224_out, not_225_out,
       not_226_out, not_227_out, not_228_out, not_229_out, not_230_out, not_231_out, not_232_out,
       not_233_out, not_234_out, not_235_out, not_236_out, not_237_out, not_238_out, not_239_out,
       not_240_out, not_241_out, not_242_out, not_243_out, not_244_out, not_245_out, not_246_out,
       not_247_out, not_248_out, not_249_out, not_250_out, not_251_out, not_252_out, not_253_out,
       not_254_out, not_255_out, not_256_out, not_257_out, not_258_out, not_259_out, not_260_out,
       not_261_out, not_262_out, not_263_out, not_264_out, not_265_out, not_266_out, not_267_out,
       not_268_out, not_269_out, not_270_out, not_271_out, not_272_out, not_273_out, not_274_out,
       not_275_out, not_276_out, not_277_out, not_278_out, not_279_out, not_280_out;

  not not_1 (not_1_out, OP5);
  not not_2 (not_2_out, OP4);
  not not_3 (not_3_out, OP3);
  not not_4 (not_4_out, OP2);
  not not_5 (not_5_out, OP1);
  not not_6 (not_6_out, OP0);
  not not_7 (not_7_out, F5);
  not not_8 (not_8_out, F4);
  not not_9 (not_9_out, F3);
  not not_10 (not_10_out, F2);
  not not_11 (not_11_out, OP5);
  not not_12 (not_12_out, OP4);
  not not_13 (not_13_out, OP3);
  not not_14 (not_14_out, OP2);
  not not_15 (not_15_out, OP1);
  not not_16 (not_16_out, OP0);
  not not_17 (not_17_out, F4);
  not not_18 (not_18_out, F3);
  not not_19 (not_19_out, F2);
  not not_20 (not_20_out, F1);
  not not_21 (not_21_out, F0);
  not not_22 (not_22_out, OP5);
  not not_23 (not_23_out, OP4);
  not not_24 (not_24_out, OP3);
  not not_25 (not_25_out, OP2);
  not not_26 (not_26_out, OP1);
  not not_27 (not_27_out, OP0);
  not not_28 (not_28_out, F4);
  not not_29 (not_29_out, F3);
  not not_30 (not_30_out, F2);
  not not_31 (not_31_out, F1);
  not not_32 (not_32_out, OP5);
  not not_33 (not_33_out, OP4);
  not not_34 (not_34_out, OP3);
  not not_35 (not_35_out, OP2);
  not not_36 (not_36_out, OP1);
  not not_37 (not_37_out, OP0);
  not not_38 (not_38_out, F4);
  not not_39 (not_39_out, F3);
  not not_40 (not_40_out, F1);
  not not_41 (not_41_out, F0);
  not not_42 (not_42_out, OP5);
  not not_43 (not_43_out, OP4);
  not not_44 (not_44_out, OP3);
  not not_45 (not_45_out, OP2);
  not not_46 (not_46_out, OP1);
  not not_47 (not_47_out, OP0);
  not not_48 (not_48_out, F4);
  not not_49 (not_49_out, F2);
  not not_50 (not_50_out, F0);
  not not_51 (not_51_out, OP5);
  not not_52 (not_52_out, OP4);
  not not_53 (not_53_out, OP2);
  not not_54 (not_54_out, OP1);
  not not_55 (not_55_out, OP0);
  not not_56 (not_56_out, OP5);
  not not_57 (not_57_out, OP4);
  not not_58 (not_58_out, OP1);
  not not_59 (not_59_out, OP0);
  not not_60 (not_60_out, OP5);
  not not_61 (not_61_out, OP4);
  not not_62 (not_62_out, OP2);
  not not_63 (not_63_out, OP1);
  not not_64 (not_64_out, OP5);
  not not_65 (not_65_out, OP4);
  not not_66 (not_66_out, OP2);
  not not_67 (not_67_out, OP0);
  not not_68 (not_68_out, OP4);
  not not_69 (not_69_out, OP3);
  not not_70 (not_70_out, OP2);
  not not_71 (not_71_out, OP4);
  not not_72 (not_72_out, OP2);
  not not_73 (not_73_out, OP5);
  not not_74 (not_74_out, OP4);
  not not_75 (not_75_out, OP3);
  not not_76 (not_76_out, OP2);
  not not_77 (not_77_out, OP1);
  not not_78 (not_78_out, OP0);
  not not_79 (not_79_out, F4);
  not not_80 (not_80_out, F3);
  not not_81 (not_81_out, F0);
  not not_82 (not_82_out, OP4);
  not not_83 (not_83_out, OP2);
  not not_84 (not_84_out, OP1);
  not not_85 (not_85_out, OP0);
  not not_86 (not_86_out, OP5);
  not not_87 (not_87_out, OP4);
  not not_88 (not_88_out, OP3);
  not not_89 (not_89_out, OP2);
  not not_90 (not_90_out, OP1);
  not not_91 (not_91_out, OP0);
  not not_92 (not_92_out, F5);
  not not_93 (not_93_out, F4);
  not not_94 (not_94_out, F3);
  not not_95 (not_95_out, F2);
  not not_96 (not_96_out, F0);
  not not_97 (not_97_out, OP5);
  not not_98 (not_98_out, OP4);
  not not_99 (not_99_out, OP3);
  not not_100 (not_100_out, OP2);
  not not_101 (not_101_out, OP1);
  not not_102 (not_102_out, OP0);
  not not_103 (not_103_out, F4);
  not not_104 (not_104_out, F3);
  not not_105 (not_105_out, F2);
  not not_106 (not_106_out, F0);
  not not_107 (not_107_out, OP5);
  not not_108 (not_108_out, OP4);
  not not_109 (not_109_out, OP3);
  not not_110 (not_110_out, OP2);
  not not_111 (not_111_out, OP1);
  not not_112 (not_112_out, OP0);
  not not_113 (not_113_out, F4);
  not not_114 (not_114_out, F3);
  not not_115 (not_115_out, F1);
  not not_116 (not_116_out, F0);
  not not_117 (not_117_out, OP5);
  not not_118 (not_118_out, OP4);
  not not_119 (not_119_out, OP3);
  not not_120 (not_120_out, OP2);
  not not_121 (not_121_out, OP1);
  not not_122 (not_122_out, OP0);
  not not_123 (not_123_out, F4);
  not not_124 (not_124_out, F3);
  not not_125 (not_125_out, OP5);
  not not_126 (not_126_out, OP4);
  not not_127 (not_127_out, OP3);
  not not_128 (not_128_out, OP2);
  not not_129 (not_129_out, OP1);
  not not_130 (not_130_out, OP0);
  not not_131 (not_131_out, F4);
  not not_132 (not_132_out, F2);
  not not_133 (not_133_out, F0);
  not not_134 (not_134_out, OP5);
  not not_135 (not_135_out, OP4);
  not not_136 (not_136_out, OP1);
  not not_137 (not_137_out, OP0);
  not not_138 (not_138_out, OP5);
  not not_139 (not_139_out, OP4);
  not not_140 (not_140_out, OP2);
  not not_141 (not_141_out, OP0);
  not not_142 (not_142_out, OP5);
  not not_143 (not_143_out, OP4);
  not not_144 (not_144_out, OP3);
  not not_145 (not_145_out, OP2);
  not not_146 (not_146_out, OP1);
  not not_147 (not_147_out, OP0);
  not not_148 (not_148_out, F4);
  not not_149 (not_149_out, F3);
  not not_150 (not_150_out, F2);
  not not_151 (not_151_out, OP5);
  not not_152 (not_152_out, OP4);
  not not_153 (not_153_out, OP3);
  not not_154 (not_154_out, OP2);
  not not_155 (not_155_out, OP1);
  not not_156 (not_156_out, OP0);
  not not_157 (not_157_out, F4);
  not not_158 (not_158_out, F3);
  not not_159 (not_159_out, F2);
  not not_160 (not_160_out, F1);
  not not_161 (not_161_out, F0);
  not not_162 (not_162_out, OP5);
  not not_163 (not_163_out, OP4);
  not not_164 (not_164_out, OP3);
  not not_165 (not_165_out, OP2);
  not not_166 (not_166_out, OP1);
  not not_167 (not_167_out, OP0);
  not not_168 (not_168_out, F4);
  not not_169 (not_169_out, F3);
  not not_170 (not_170_out, F2);
  not not_171 (not_171_out, F1);
  not not_172 (not_172_out, OP5);
  not not_173 (not_173_out, OP4);
  not not_174 (not_174_out, OP3);
  not not_175 (not_175_out, OP2);
  not not_176 (not_176_out, OP1);
  not not_177 (not_177_out, OP0);
  not not_178 (not_178_out, F4);
  not not_179 (not_179_out, F3);
  not not_180 (not_180_out, F2);
  not not_181 (not_181_out, F0);
  not not_182 (not_182_out, OP5);
  not not_183 (not_183_out, OP4);
  not not_184 (not_184_out, OP3);
  not not_185 (not_185_out, OP2);
  not not_186 (not_186_out, OP1);
  not not_187 (not_187_out, OP0);
  not not_188 (not_188_out, F4);
  not not_189 (not_189_out, F3);
  not not_190 (not_190_out, F1);
  not not_191 (not_191_out, F0);
  not not_192 (not_192_out, OP5);
  not not_193 (not_193_out, OP4);
  not not_194 (not_194_out, OP3);
  not not_195 (not_195_out, OP2);
  not not_196 (not_196_out, OP1);
  not not_197 (not_197_out, OP0);
  not not_198 (not_198_out, F4);
  not not_199 (not_199_out, F2);
  not not_200 (not_200_out, OP5);
  not not_201 (not_201_out, OP4);
  not not_202 (not_202_out, OP2);
  not not_203 (not_203_out, OP1);
  not not_204 (not_204_out, OP0);
  not not_205 (not_205_out, OP5);
  not not_206 (not_206_out, OP4);
  not not_207 (not_207_out, OP1);
  not not_208 (not_208_out, OP0);
  not not_209 (not_209_out, OP5);
  not not_210 (not_210_out, OP4);
  not not_211 (not_211_out, OP2);
  not not_212 (not_212_out, OP1);
  not not_213 (not_213_out, OP4);
  not not_214 (not_214_out, OP3);
  not not_215 (not_215_out, OP2);
  not not_216 (not_216_out, OP4);
  not not_217 (not_217_out, OP2);
  not not_218 (not_218_out, OP5);
  not not_219 (not_219_out, OP4);
  not not_220 (not_220_out, OP3);
  not not_221 (not_221_out, OP2);
  not not_222 (not_222_out, OP1);
  not not_223 (not_223_out, OP0);
  not not_224 (not_224_out, F4);
  not not_225 (not_225_out, F3);
  not not_226 (not_226_out, F2);
  not not_227 (not_227_out, OP4);
  not not_228 (not_228_out, OP2);
  not not_229 (not_229_out, OP1);
  not not_230 (not_230_out, OP0);
  not not_231 (not_231_out, OP5);
  not not_232 (not_232_out, OP4);
  not not_233 (not_233_out, OP3);
  not not_234 (not_234_out, OP2);
  not not_235 (not_235_out, OP1);
  not not_236 (not_236_out, OP0);
  not not_237 (not_237_out, F4);
  not not_238 (not_238_out, F3);
  not not_239 (not_239_out, F1);
  not not_240 (not_240_out, OP5);
  not not_241 (not_241_out, OP4);
  not not_242 (not_242_out, OP3);
  not not_243 (not_243_out, OP2);
  not not_244 (not_244_out, OP1);
  not not_245 (not_245_out, OP0);
  not not_246 (not_246_out, F4);
  not not_247 (not_247_out, F3);
  not not_248 (not_248_out, OP5);
  not not_249 (not_249_out, OP4);
  not not_250 (not_250_out, OP3);
  not not_251 (not_251_out, OP2);
  not not_252 (not_252_out, OP1);
  not not_253 (not_253_out, OP0);
  not not_254 (not_254_out, F4);
  not not_255 (not_255_out, F2);
  not not_256 (not_256_out, F0);
  not not_257 (not_257_out, OP5);
  not not_258 (not_258_out, OP4);
  not not_259 (not_259_out, OP3);
  not not_260 (not_260_out, OP2);
  not not_261 (not_261_out, OP1);
  not not_262 (not_262_out, OP0);
  not not_263 (not_263_out, F4);
  not not_264 (not_264_out, F2);
  not not_265 (not_265_out, OP5);
  not not_266 (not_266_out, OP4);
  not not_267 (not_267_out, OP2);
  not not_268 (not_268_out, OP0);
  not not_269 (not_269_out, OP5);
  not not_270 (not_270_out, OP4);
  not not_271 (not_271_out, OP1);
  not not_272 (not_272_out, OP5);
  not not_273 (not_273_out, OP4);
  not not_274 (not_274_out, OP3);
  not not_275 (not_275_out, OP2);
  not not_276 (not_276_out, OP1);
  not not_277 (not_277_out, OP0);
  not not_278 (not_278_out, F4);
  not not_279 (not_279_out, F3);
  not not_280 (not_280_out, F0);
  and and_1 (and_1_out, not_1_out, not_2_out, not_3_out, not_4_out, not_5_out, not_6_out, not_7_out, not_8_out, not_9_out, not_10_out, F1, F0);
  and and_2 (and_2_out, not_11_out, not_12_out, not_13_out, not_14_out, not_15_out, not_16_out, F5, not_17_out, not_18_out, not_19_out, not_20_out, not_21_out);
  and and_3 (and_3_out, not_22_out, not_23_out, not_24_out, not_25_out, not_26_out, not_27_out, F5, not_28_out, not_29_out, not_30_out, not_31_out, F0);
  and and_4 (and_4_out, not_32_out, not_33_out, not_34_out, not_35_out, not_36_out, not_37_out, F5, not_38_out, not_39_out, F2, not_40_out, not_41_out);
  and and_5 (and_5_out, not_42_out, not_43_out, not_44_out, not_45_out, not_46_out, not_47_out, F5, not_48_out, F3, not_49_out, F1, not_50_out);
  and and_6 (and_6_out, not_51_out, not_52_out, OP3, not_53_out, not_54_out, not_55_out);
  and and_7 (and_7_out, not_56_out, not_57_out, OP3, OP2, not_58_out, not_59_out);
  and and_8 (and_8_out, not_60_out, not_61_out, OP3, not_62_out, not_63_out, OP0);
  and and_9 (and_9_out, not_64_out, not_65_out, OP3, not_66_out, OP1, not_67_out);
  and and_10 (and_10_out, OP5, not_68_out, not_69_out, not_70_out, OP1, OP0);
  and and_11 (and_11_out, OP5, not_71_out, OP3, not_72_out, OP1, OP0);
  and and_12 (and_12_out, not_73_out, not_74_out, not_75_out, not_76_out, not_77_out, not_78_out, F5, not_79_out, not_80_out, F2, F1, not_81_out);
  and and_13 (and_13_out, OP5, not_82_out, OP3, not_83_out, not_84_out, not_85_out);
  and and_14 (and_14_out, not_86_out, not_87_out, not_88_out, not_89_out, not_90_out, not_91_out, not_92_out, not_93_out, not_94_out, not_95_out, F1, not_96_out);
  and and_15 (and_15_out, not_97_out, not_98_out, not_99_out, not_100_out, not_101_out, not_102_out, F5, not_103_out, not_104_out, not_105_out, F1, not_106_out);
  and and_16 (and_16_out, not_107_out, not_108_out, not_109_out, not_110_out, not_111_out, not_112_out, F5, not_113_out, not_114_out, F2, not_115_out, not_116_out);
  and and_17 (and_17_out, not_117_out, not_118_out, not_119_out, not_120_out, not_121_out, not_122_out, F5, not_123_out, not_124_out, F2, F1, F0);
  and and_18 (and_18_out, not_125_out, not_126_out, not_127_out, not_128_out, not_129_out, not_130_out, F5, not_131_out, F3, not_132_out, F1, not_133_out);
  and and_19 (and_19_out, not_134_out, not_135_out, OP3, OP2, not_136_out, not_137_out);
  and and_20 (and_20_out, not_138_out, not_139_out, OP3, not_140_out, OP1, not_141_out);
  and and_21 (and_21_out, not_142_out, not_143_out, not_144_out, not_145_out, not_146_out, not_147_out, F5, not_148_out, not_149_out, not_150_out, F1, F0);
  and and_22 (and_22_out, not_151_out, not_152_out, not_153_out, not_154_out, not_155_out, not_156_out, F5, not_157_out, not_158_out, not_159_out, not_160_out, not_161_out);
  and and_23 (and_23_out, not_162_out, not_163_out, not_164_out, not_165_out, not_166_out, not_167_out, F5, not_168_out, not_169_out, not_170_out, not_171_out, F0);
  and and_24 (and_24_out, not_172_out, not_173_out, not_174_out, not_175_out, not_176_out, not_177_out, F5, not_178_out, not_179_out, not_180_out, F1, not_181_out);
  and and_25 (and_25_out, not_182_out, not_183_out, not_184_out, not_185_out, not_186_out, not_187_out, F5, not_188_out, not_189_out, F2, not_190_out, not_191_out);
  and and_26 (and_26_out, not_192_out, not_193_out, not_194_out, not_195_out, not_196_out, not_197_out, F5, not_198_out, F3, not_199_out, F1, F0);
  and and_27 (and_27_out, not_200_out, not_201_out, OP3, not_202_out, not_203_out, not_204_out);
  and and_28 (and_28_out, not_205_out, not_206_out, OP3, OP2, not_207_out, not_208_out);
  and and_29 (and_29_out, not_209_out, not_210_out, OP3, not_211_out, not_212_out, OP0);
  and and_30 (and_30_out, OP5, not_213_out, not_214_out, not_215_out, OP1, OP0);
  and and_31 (and_31_out, OP5, not_216_out, OP3, not_217_out, OP1, OP0);
  and and_32 (and_32_out, not_218_out, not_219_out, not_220_out, not_221_out, not_222_out, not_223_out, F5, not_224_out, not_225_out, not_226_out, F1, F0);
  and and_33 (and_33_out, OP5, not_227_out, OP3, not_228_out, not_229_out, not_230_out);
  and and_34 (and_34_out, not_231_out, not_232_out, not_233_out, not_234_out, not_235_out, not_236_out, F5, not_237_out, not_238_out, F2, not_239_out, F0);
  and and_35 (and_35_out, not_240_out, not_241_out, not_242_out, not_243_out, not_244_out, not_245_out, F5, not_246_out, not_247_out, F2, F1, F0);
  and and_36 (and_36_out, not_248_out, not_249_out, not_250_out, not_251_out, not_252_out, not_253_out, F5, not_254_out, F3, not_255_out, F1, not_256_out);
  and and_37 (and_37_out, not_257_out, not_258_out, not_259_out, not_260_out, not_261_out, not_262_out, F5, not_263_out, F3, not_264_out, F1, F0);
  and and_38 (and_38_out, not_265_out, not_266_out, OP3, not_267_out, OP1, not_268_out);
  and and_39 (and_39_out, not_269_out, not_270_out, OP3, OP2, not_271_out, OP0);
  and and_40 (and_40_out, not_272_out, not_273_out, not_274_out, not_275_out, not_276_out, not_277_out, F5, not_278_out, not_279_out, F2, F1, not_280_out);
  or or_1 (S1, and_14_out, and_15_out, and_16_out, and_17_out, and_18_out, and_19_out, and_20_out, and_21_out);
  or or_2 (S3, and_34_out, and_35_out, and_36_out, and_37_out, and_38_out, and_39_out, and_40_out);
  or or_3 (S0, and_1_out, and_2_out, and_3_out, and_4_out, and_5_out, and_6_out, and_7_out, and_8_out, and_9_out, and_10_out, and_11_out, and_12_out, and_13_out);
  or or_4 (S2, and_22_out, and_23_out, and_24_out, and_25_out, and_26_out, and_27_out, and_28_out, and_29_out, and_30_out, and_31_out, and_32_out, and_33_out);
endmodule

// 控制信号生成
module \控制信号自动生成  (
  input  OP0,
  input  OP1,
  input  OP2,
  input  OP3,
  input  OP4,
  input  OP5,
  input  F0,
  input  F1,
  input  F2,
  input  F3,
  input  F4,
  input  F5,
  output MemToReg,
  output MemWrite,
  output ALU_SRC,
  output RegWrite,
  output SysCALL,
  output SignedExt,
  output RegDst,
  output BEQ,
  output BNE,
  output JR,
  output JMP,
  output JAL
);

  wire and_2_out, and_3_out, and_4_out, and_5_out, and_6_out, and_7_out, and_8_out, and_9_out, and_10_out,
       and_11_out, and_12_out, and_13_out, and_14_out, and_15_out, and_17_out, and_18_out, and_19_out,
       and_20_out, and_21_out, and_22_out, and_23_out, and_24_out, and_25_out, and_26_out, and_30_out,
       and_31_out, not_1_out, not_2_out, not_3_out, not_4_out, not_5_out, not_6_out, not_7_out, not_8_out,
       not_9_out, not_10_out, not_11_out, not_12_out, not_13_out, not_14_out, not_15_out, not_16_out,
       not_17_out, not_18_out, not_19_out, not_20_out, not_21_out, not_22_out, not_23_out, not_24_out,
       not_25_out, not_26_out, not_27_out, not_28_out, not_29_out, not_30_out, not_31_out, not_32_out,
       not_33_out, not_34_out, not_35_out, not_36_out, not_37_out, not_38_out, not_39_out, not_40_out,
       not_41_out, not_42_out, not_43_out, not_44_out, not_45_out, not_46_out, not_47_out, not_48_out,
       not_49_out, not_50_out, not_51_out, not_52_out, not_53_out, not_54_out, not_55_out, not_56_out,
       not_57_out, not_58_out, not_59_out, not_60_out, not_61_out, not_62_out, not_63_out, not_64_out,
       not_65_out, not_66_out, not_67_out, not_68_out, not_69_out, not_70_out, not_71_out, not_72_out,
       not_73_out, not_74_out, not_75_out, not_76_out, not_77_out, not_78_out, not_79_out, not_80_out,
       not_81_out, not_82_out, not_83_out, not_84_out, not_85_out, not_86_out, not_87_out, not_88_out,
       not_89_out, not_90_out, not_91_out, not_92_out, not_93_out, not_94_out, not_95_out, not_96_out,
       not_97_out, not_98_out, not_99_out, not_100_out, not_101_out, not_102_out, not_103_out, not_104_out,
       not_105_out, not_106_out, not_107_out, not_108_out, not_109_out, not_110_out, not_111_out,
       not_112_out, not_113_out, not_114_out, not_115_out, not_116_out, not_117_out, not_118_out,
       not_119_out, not_120_out, not_121_out, not_122_out, not_123_out, not_124_out, not_125_out,
       not_126_out, not_127_out, not_128_out, not_129_out, not_130_out, not_131_out, not_132_out,
       not_133_out, not_134_out, not_135_out, not_136_out, not_137_out, not_138_out, not_139_out,
       not_140_out, not_141_out, not_142_out, not_143_out, not_144_out, not_145_out, not_146_out,
       not_147_out, not_148_out, not_149_out, not_150_out, not_151_out, not_152_out, not_153_out,
       not_154_out, not_155_out, not_156_out, not_157_out, not_158_out, not_159_out, not_160_out,
       not_161_out, not_162_out, not_163_out, not_164_out, not_165_out, not_166_out, not_167_out,
       not_168_out, not_169_out, not_170_out, not_171_out;

  not not_1 (not_1_out, OP2);
  not not_2 (not_2_out, OP3);
  not not_3 (not_3_out, OP4);
  not not_4 (not_4_out, OP0);
  not not_5 (not_5_out, OP1);
  not not_6 (not_6_out, OP2);
  not not_7 (not_7_out, OP4);
  not not_8 (not_8_out, OP2);
  not not_9 (not_9_out, OP4);
  not not_10 (not_10_out, OP0);
  not not_11 (not_11_out, OP1);
  not not_12 (not_12_out, OP2);
  not not_13 (not_13_out, OP4);
  not not_14 (not_14_out, OP0);
  not not_15 (not_15_out, OP2);
  not not_16 (not_16_out, OP4);
  not not_17 (not_17_out, OP5);
  not not_18 (not_18_out, OP1);
  not not_19 (not_19_out, OP4);
  not not_20 (not_20_out, OP5);
  not not_21 (not_21_out, OP2);
  not not_22 (not_22_out, OP4);
  not not_23 (not_23_out, OP3);
  not not_24 (not_24_out, OP4);
  not not_25 (not_25_out, OP5);
  not not_26 (not_26_out, OP0);
  not not_27 (not_27_out, OP1);
  not not_28 (not_28_out, OP2);
  not not_29 (not_29_out, OP4);
  not not_30 (not_30_out, OP5);
  not not_31 (not_31_out, F0);
  not not_32 (not_32_out, F2);
  not not_33 (not_33_out, F3);
  not not_34 (not_34_out, F4);
  not not_35 (not_35_out, OP0);
  not not_36 (not_36_out, OP1);
  not not_37 (not_37_out, OP2);
  not not_38 (not_38_out, OP4);
  not not_39 (not_39_out, OP5);
  not not_40 (not_40_out, F3);
  not not_41 (not_41_out, F4);
  not not_42 (not_42_out, OP0);
  not not_43 (not_43_out, OP1);
  not not_44 (not_44_out, OP2);
  not not_45 (not_45_out, OP4);
  not not_46 (not_46_out, OP5);
  not not_47 (not_47_out, F2);
  not not_48 (not_48_out, F3);
  not not_49 (not_49_out, F4);
  not not_50 (not_50_out, OP0);
  not not_51 (not_51_out, OP1);
  not not_52 (not_52_out, OP2);
  not not_53 (not_53_out, OP4);
  not not_54 (not_54_out, OP5);
  not not_55 (not_55_out, F2);
  not not_56 (not_56_out, F4);
  not not_57 (not_57_out, OP0);
  not not_58 (not_58_out, OP2);
  not not_59 (not_59_out, OP4);
  not not_60 (not_60_out, OP5);
  not not_61 (not_61_out, OP1);
  not not_62 (not_62_out, OP4);
  not not_63 (not_63_out, OP5);
  not not_64 (not_64_out, OP2);
  not not_65 (not_65_out, OP3);
  not not_66 (not_66_out, OP4);
  not not_67 (not_67_out, OP0);
  not not_68 (not_68_out, OP1);
  not not_69 (not_69_out, OP2);
  not not_70 (not_70_out, OP3);
  not not_71 (not_71_out, OP4);
  not not_72 (not_72_out, OP5);
  not not_73 (not_73_out, F0);
  not not_74 (not_74_out, F1);
  not not_75 (not_75_out, F4);
  not not_76 (not_76_out, F5);
  not not_77 (not_77_out, OP0);
  not not_78 (not_78_out, OP1);
  not not_79 (not_79_out, OP2);
  not not_80 (not_80_out, OP4);
  not not_81 (not_81_out, OP0);
  not not_82 (not_82_out, OP2);
  not not_83 (not_83_out, OP4);
  not not_84 (not_84_out, OP5);
  not not_85 (not_85_out, OP1);
  not not_86 (not_86_out, OP2);
  not not_87 (not_87_out, OP4);
  not not_88 (not_88_out, OP5);
  not not_89 (not_89_out, OP1);
  not not_90 (not_90_out, OP3);
  not not_91 (not_91_out, OP4);
  not not_92 (not_92_out, OP5);
  not not_93 (not_93_out, OP3);
  not not_94 (not_94_out, OP4);
  not not_95 (not_95_out, OP5);
  not not_96 (not_96_out, OP2);
  not not_97 (not_97_out, OP4);
  not not_98 (not_98_out, OP0);
  not not_99 (not_99_out, OP1);
  not not_100 (not_100_out, OP2);
  not not_101 (not_101_out, OP3);
  not not_102 (not_102_out, OP4);
  not not_103 (not_103_out, OP5);
  not not_104 (not_104_out, F0);
  not not_105 (not_105_out, F1);
  not not_106 (not_106_out, F2);
  not not_107 (not_107_out, F4);
  not not_108 (not_108_out, F5);
  not not_109 (not_109_out, OP0);
  not not_110 (not_110_out, OP1);
  not not_111 (not_111_out, OP2);
  not not_112 (not_112_out, OP3);
  not not_113 (not_113_out, OP4);
  not not_114 (not_114_out, OP5);
  not not_115 (not_115_out, F3);
  not not_116 (not_116_out, F4);
  not not_117 (not_117_out, OP0);
  not not_118 (not_118_out, OP1);
  not not_119 (not_119_out, OP2);
  not not_120 (not_120_out, OP3);
  not not_121 (not_121_out, OP4);
  not not_122 (not_122_out, OP5);
  not not_123 (not_123_out, F2);
  not not_124 (not_124_out, F3);
  not not_125 (not_125_out, F4);
  not not_126 (not_126_out, OP0);
  not not_127 (not_127_out, OP1);
  not not_128 (not_128_out, OP2);
  not not_129 (not_129_out, OP3);
  not not_130 (not_130_out, OP4);
  not not_131 (not_131_out, OP5);
  not not_132 (not_132_out, F2);
  not not_133 (not_133_out, F4);
  not not_134 (not_134_out, OP0);
  not not_135 (not_135_out, OP1);
  not not_136 (not_136_out, OP3);
  not not_137 (not_137_out, OP4);
  not not_138 (not_138_out, OP5);
  not not_139 (not_139_out, OP5);
  not not_140 (not_140_out, OP4);
  not not_141 (not_141_out, OP3);
  not not_142 (not_142_out, OP1);
  not not_143 (not_143_out, OP0);
  not not_144 (not_144_out, OP1);
  not not_145 (not_145_out, OP2);
  not not_146 (not_146_out, OP3);
  not not_147 (not_147_out, OP4);
  not not_148 (not_148_out, OP5);
  not not_149 (not_149_out, F0);
  not not_150 (not_150_out, F1);
  not not_151 (not_151_out, F2);
  not not_152 (not_152_out, F4);
  not not_153 (not_153_out, F5);
  not not_154 (not_154_out, OP0);
  not not_155 (not_155_out, OP2);
  not not_156 (not_156_out, OP3);
  not not_157 (not_157_out, OP4);
  not not_158 (not_158_out, OP5);
  not not_159 (not_159_out, F0);
  not not_160 (not_160_out, F1);
  not not_161 (not_161_out, F2);
  not not_162 (not_162_out, F4);
  not not_163 (not_163_out, F5);
  not not_164 (not_164_out, OP2);
  not not_165 (not_165_out, OP3);
  not not_166 (not_166_out, OP4);
  not not_167 (not_167_out, OP5);
  not not_168 (not_168_out, OP2);
  not not_169 (not_169_out, OP3);
  not not_170 (not_170_out, OP4);
  not not_171 (not_171_out, OP5);
  and and_1 (MemToReg, OP0, OP1, not_1_out, not_2_out, not_3_out, OP5);
  and and_2 (and_2_out, not_4_out, not_5_out, not_6_out, OP3, not_7_out, OP5);
  and and_3 (and_3_out, OP0, OP1, not_8_out, OP3, not_9_out, OP5);
  and and_4 (and_4_out, not_10_out, not_11_out, not_12_out, OP3, not_13_out);
  and and_5 (and_5_out, not_14_out, not_15_out, OP3, not_16_out, not_17_out);
  and and_6 (and_6_out, not_18_out, OP3, not_19_out, not_20_out);
  and and_7 (and_7_out, OP0, OP1, not_21_out, not_22_out, OP5);
  and and_8 (and_8_out, OP0, OP1, OP2, not_23_out, not_24_out, not_25_out);
  and and_9 (and_9_out, not_26_out, not_27_out, not_28_out, not_29_out, not_30_out, not_31_out, not_32_out, not_33_out, not_34_out);
  and and_10 (and_10_out, not_35_out, not_36_out, not_37_out, not_38_out, not_39_out, not_40_out, not_41_out, F5);
  and and_11 (and_11_out, not_42_out, not_43_out, not_44_out, not_45_out, not_46_out, F1, not_47_out, not_48_out, not_49_out);
  and and_12 (and_12_out, not_50_out, not_51_out, not_52_out, not_53_out, not_54_out, F1, not_55_out, not_56_out, F5);
  and and_13 (and_13_out, not_57_out, not_58_out, OP3, not_59_out, not_60_out);
  and and_14 (and_14_out, not_61_out, OP3, not_62_out, not_63_out);
  and and_15 (and_15_out, OP0, OP1, not_64_out, not_65_out, not_66_out);
  and and_16 (SysCALL, not_67_out, not_68_out, not_69_out, not_70_out, not_71_out, not_72_out, not_73_out, not_74_out, F2, F3, not_75_out, not_76_out);
  and and_17 (and_17_out, not_77_out, not_78_out, not_79_out, OP3, not_80_out);
  and and_18 (and_18_out, not_81_out, not_82_out, OP3, not_83_out, not_84_out);
  and and_19 (and_19_out, not_85_out, not_86_out, OP3, not_87_out, not_88_out);
  and and_20 (and_20_out, not_89_out, OP2, not_90_out, not_91_out, not_92_out);
  and and_21 (and_21_out, OP0, OP2, not_93_out, not_94_out, not_95_out);
  and and_22 (and_22_out, OP0, OP1, not_96_out, not_97_out, OP5);
  and and_23 (and_23_out, not_98_out, not_99_out, not_100_out, not_101_out, not_102_out, not_103_out, not_104_out, not_105_out, not_106_out, not_107_out, not_108_out);
  and and_24 (and_24_out, not_109_out, not_110_out, not_111_out, not_112_out, not_113_out, not_114_out, not_115_out, not_116_out, F5);
  and and_25 (and_25_out, not_117_out, not_118_out, not_119_out, not_120_out, not_121_out, not_122_out, F1, not_123_out, not_124_out, not_125_out);
  and and_26 (and_26_out, not_126_out, not_127_out, not_128_out, not_129_out, not_130_out, not_131_out, F1, not_132_out, not_133_out, F5);
  and and_27 (BEQ, not_134_out, not_135_out, OP2, not_136_out, not_137_out, not_138_out);
  and and_28 (BNE, not_139_out, not_140_out, not_141_out, OP2, not_142_out, OP0);
  and and_29 (JR, not_143_out, not_144_out, not_145_out, not_146_out, not_147_out, not_148_out, not_149_out, not_150_out, not_151_out, F3, not_152_out, not_153_out);
  and and_30 (and_30_out, not_154_out, not_155_out, not_156_out, not_157_out, not_158_out, not_159_out, not_160_out, not_161_out, F3, not_162_out, not_163_out);
  and and_31 (and_31_out, OP1, not_164_out, not_165_out, not_166_out, not_167_out);
  and and_32 (JAL, OP0, OP1, not_168_out, not_169_out, not_170_out, not_171_out);
  or or_1 (MemWrite, and_2_out, and_3_out);
  or or_2 (ALU_SRC, and_4_out, and_5_out, and_6_out, and_7_out, and_8_out);
  or or_3 (RegWrite, and_9_out, and_10_out, and_11_out, and_12_out, and_13_out, and_14_out, and_15_out);
  or or_4 (SignedExt, and_17_out, and_18_out, and_19_out, and_20_out, and_21_out, and_22_out);
  or or_5 (RegDst, and_23_out, and_24_out, and_25_out, and_26_out);
  or or_6 (JMP, and_30_out, and_31_out);
endmodule

// ALU
module MIPS_ALU (
  input  [4:0] shamt,
  input  [31:0] X,
  input  [31:0] Y,
  input  [3:0] AluOP,
  output Equal,
  output [31:0] Result,
  output [31:0] Result_2
);

  wire [0:0] comparator_1_lt, comparator_2_lt;
  wire [31:0] adder_1_out, AND_out, divider_1_out, divider_1_rem, multiplier_1_cout, multiplier_1_out,
       NOR_out, OR_out, shifter_1_out, shifter_2_out, shifter_3_out, subtractor_1_out, XOR_out;

  assign AND_out = X & Y;  // AND_Gate AND, 32 bits wide
  assign OR_out = X | Y;  // OR_Gate OR, 32 bits wide
  Shifter #(.width(32), .shift("ll")) shifter_1 (.in(Y), .\dist (shamt), .out(shifter_1_out));
  Shifter #(.width(32), .shift("ar")) shifter_2 (.in(Y), .\dist (shamt), .out(shifter_2_out));
  Shifter #(.width(32), .shift("lr")) shifter_3 (.in(Y), .\dist (shamt), .out(shifter_3_out));
  Multiplier #(.width(32)) multiplier_1 (.a(X), .b(Y), .out(multiplier_1_out), .cout(multiplier_1_cout));  // open: cin
  Divider #(.width(32)) divider_1 (.a(X), .b(Y), .out(divider_1_out), .rem(divider_1_rem));  // open: upper
  Adder #(.width(32)) adder_1 (.a(X), .b(Y), .out(adder_1_out));  // open: cin, cout
  Subtractor #(.width(32)) subtractor_1 (.a(X), .b(Y), .out(subtractor_1_out));  // open: bin, bout
  assign XOR_out = X ^ Y;  // XOR_Gate XOR, 32 bits wide
  assign NOR_out = ~(X | Y);  // NOR_Gate NOR, 32 bits wide
  Comparator #(.width(32), .mode("twosComplement")) comparator_1 (
    .a(X), .b(Y), .eq(Equal), .lt(comparator_1_lt[0]));  // open: gt
  Comparator #(.width(32), .mode("unsigned")) comparator_2 (.a(X), .b(Y), .lt(comparator_2_lt[0]));  // open: gt, eq
  Multiplexer #(.select(4), .width(32), .disabled("Z"), .enable("false")) multiplexer_1 (
    .in0(shifter_1_out), .in1(shifter_2_out), .in2(shifter_3_out), .in3(multiplier_1_out),
    .in4(divider_1_out), .in5(adder_1_out), .in6(subtractor_1_out), .in7(AND_out), .in8(OR_out),
    .in9(XOR_out), .in10(NOR_out), .in11({{31{1'b0}}, comparator_1_lt[0]}),
    .in12({{31{1'b0}}, comparator_2_lt[0]}), .in13({32{1'b0}}), .in14({32{1'b0}}), .in15({32{1'b0}}),
    .out(Result), .sel(AluOP));
  Multiplexer #(.select(4), .width(32), .disabled("Z"), .enable("false")) multiplexer_2 (
    .in0({32{1'b0}}), .in1({32{1'b0}}), .in2({32{1'b0}}), .in3(multiplier_1_cout), .in4(divider_1_rem),
    .in5({32{1'b0}}), .in6({32{1'b0}}), .in7({32{1'b0}}), .in8({32{1'b0}}), .in9({32{1'b0}}),
    .in10({32{1'b0}}), .in11({32{1'b0}}), .in12({32{1'b0}}), .in13({32{1'b0}}), .in14({32{1'b0}}),
    .in15({32{1'b0}}), .out(Result_2), .sel(AluOP));

  // Other names for the same wires on the sheet: Result2[31:0] = Result_2; S[3:0] = AluOP

  // Notes on the sheet:
  //   不要改变此引脚区域内容，也不要改变ALU封装形式
  //   输入引脚
  //   输出引脚
endmodule

module MIPS_Regifile (
  input  [31:0] Din,
  input  Clk,
  input  WE,
  input  [4:0] R1_num,
  input  [4:0] W_num,
  input  [4:0] R2_num,
  output [31:0] R1,
  output [31:0] R2
);

  // RegisterFile registerfile_1: pin names not known; wires that end beside it: Din, Clk, WE, W_num, R1_num, R2_num, R1, R2

  // Notes on the sheet:
  //   写入目标寄存器中
  //   rd:目标寄存器
  //   rt
  //   rs
endmodule

module \理想流水线  (
  output RegWrite,
  output MemWrite,
  output [31:0] IF_PC,
  output [31:0] ID_PC,
  output [31:0] EX_PC,
  output [31:0] M_PC,
  output [31:0] WB_PC,
  output [31:0] RDin,
  output [31:0] MDin,
  output [31:0] LedData
);

  wire AluSrcB, AluSrcB_EX, AluSrcB_MEM, and_1_out, and_4_out, and_5_out, and_6_out, Beq, Beq_EX, Beq_MEM,
       BGTZ, BGTZ_EX, Bne, Bne_EX, Bne_MEM, CLK, comparator_2_gt, display, enable_WB, enableEX, equal_22,
       equal_22_ex, equal_22_mem, equal_22_wb, ex_mem_1_enable_ex, Go, if_id_1_enable_out, IR1, IR2, IR3,
       JAL, JAL_Ex, JAL_MEM, JAL_WB, JMP, JMP_EX, JR, JR_EX, MemToBeg, MemToBeg_ex, MemToBeg_MEM,
       MemToBeg_WB, MemWrite_ex, MemWriteID, mips_alu_1_equal, not_1_out, not_2_out, not_3_out, not_4_out,
       or_1_out, or_2_out, pause, RegDst, RegDst_EX, RegDst_MEM, RegDst_WB, register_1_q, RegWrite_ex,
       RegWrite_MEM, RegWriteID, RST, SB, SB_EX, SB_MEM, SignedExt, SUBU, Syscall, Syscall_ex, Syscall_mem,
       Syscall_wb, W1, W2, W3, XOR, \是否跳转 ;
  wire [3:0] AluOP, AluOP_EX, AluOP_MEM;
  wire [4:0] bit_extender_3_out, multiplexer_4_out, multiplexer_5_out, multiplexer_6_out, multiplexer_8_out,
       multiplier_1_out, rd_ID_EX, rd_ID_MEM, rd_ID_WB, rt_ID_EX, rt_ID_MEM, rt_ID_WB, shamtEX;
  wire [5:0] Func;
  wire [7:0] demultiplexer_1_out0, demultiplexer_1_out1, demultiplexer_1_out2, demultiplexer_1_out3;
  wire [15:0] \LoadUse次数 , \总周期数 , \插入气泡数 , \无条件分支数 , \条件分支成功数 ;
  wire [27:0] adder_3_out;
  wire [31:0] adder_1_out, adder_2_out, and_7_out, and_8_out, Beq_Bne, bit_extender_1_out,
       bit_extender_2_out, EX_IR, ex_mem_1_r2_ex, IF_IR, IMMEX, IR_PC_MEM, IR_PC_WB, MEMDATA_MEM, MEMDATA_WB,
       multiplexer_1_out, multiplexer_2_out, multiplexer_3_out, multiplexer_7_out, multiplexer_10_out,
       multiplexer_11_out, not_5_out, or_4_out, R1_ID, R1EX, R2_ID, R2EX, RESULT, RESULT_MEM, RESULT_WB,
       shifter_1_out, shifter_2_out;
  wire [31:2] J_JAL;
  wire [31:6] ID_IR;

  Button \u_总复位  (.out(RST));
  Button _1 (.out(IR1));
  Button _2 (.out(IR2));
  Button _3 (.out(IR3));
  // Probe on \总周期数 
  Multiplexer #(.select(1), .width(32), .disabled("Z"), .enable("false")) multiplexer_1 (
    .in0(adder_1_out), .in1(Beq_Bne), .out(multiplexer_1_out), .sel(\是否跳转 ));
  Button \u_继续运行  (.out(Go));
  LED #(.active("true")) led_1 (.in(W1));
  LED #(.active("true")) led_2 (.in(W2));
  LED #(.active("true")) led_3 (.in(W3));
  // Probe on IF_PC[11:0]
  Multiplexer #(.select(1), .width(32), .disabled("Z"), .enable("false")) multiplexer_2 (
    .in0(multiplexer_1_out), .in1(multiplexer_3_out), .out(multiplexer_2_out), .sel(JMP_EX));
  Multiplexer #(.select(1), .width(32), .disabled("Z"), .enable("false")) multiplexer_3 (
    .in0({J_JAL, 2'b00}), .in1(R1EX), .out(multiplexer_3_out), .sel(JR_EX));
  Hex_Digit_Display hex_digit_display_1 (.value(LedData[31:28]));  // open: dp
  // Probe on IF_PC[11:0]
  // Mips_Probe mips_probe_1: pin names not known; wires that end beside it: IF_IR
  Comparator #(.width(32), .mode("twosComplement")) comparator_1 (
    .a(R1_ID), .b(32'h22), .eq(equal_22));  // open: gt, lt
  Hex_Digit_Display hex_digit_display_2 (.value(LedData[23:20]));  // open: dp
  Hex_Digit_Display hex_digit_display_3 (.value(LedData[27:24]));  // open: dp
  // Probe on ID_PC[11:0]
  // Mips_Probe mips_probe_2: pin names not known; wires that end beside it: {ID_IR, Func}
  Counter #(.width(16), .max('hffff), .ongoal("wrap"), .trigger("rising"), .behavior("old")) counter_1 (
    .count(not_3_out), .Q(\总周期数 ), .clk(CLK), .clr(RST));  // open: load, D, carry, preset
  Register #(.width(32), .trigger("rising"), .Select("low")) PC (
    .D(multiplexer_2_out), .en(not_3_out), .Q(IF_PC), .clk(CLK), .clr(RST));
  Hex_Digit_Display hex_digit_display_4 (.value(LedData[19:16]));  // open: dp
  Hex_Digit_Display hex_digit_display_5 (.value(LedData[15:12]));  // open: dp
  // Probe on ID_PC[11:0]
  and and_1 (and_1_out, not_1_out, pause);
  not not_1 (not_1_out, Go);
  and and_2 (pause, Syscall_wb, not_2_out);
  not not_2 (not_2_out, equal_22_wb);
  and and_3 (display, equal_22, Syscall);
  Hex_Digit_Display hex_digit_display_6 (.value(LedData[11:8]));  // open: dp
  Hex_Digit_Display hex_digit_display_7 (.value(LedData[7:4]));  // open: dp
  Clock #(.highDuration(1), .lowDuration(1)) clock_1 (.out(CLK));
  // Probe on EX_PC[11:0]
  // Mips_Probe mips_probe_3: pin names not known; wires that end beside it: EX_IR
  Hex_Digit_Display hex_digit_display_8 (.value(LedData[3:0]));  // open: dp
  // Probe on EX_PC[11:0]
  ROM #(.addrWidth(10), .dataWidth(32), .Select("high")) rom_1 (.addr(IF_PC[11:2]), .data(IF_IR));
  not not_3 (not_3_out, register_1_q);
  Register #(.width(1), .trigger("rising"), .Select("low")) register_1 (
    .D(Syscall_wb), .en(and_1_out), .Q(register_1_q), .clk(CLK), .clr(RST));
  // Probe on M_PC[11:0]
  // Probe on M_PC[11:0]
  // Mips_Probe mips_probe_4: pin names not known; wires that end beside it: IR_PC_MEM
  // Probe on \总周期数 
  // Probe on \无条件分支数 
  // Probe on \条件分支成功数 
  // Probe on \插入气泡数 
  // Probe on \LoadUse次数 
  or or_1 (or_1_out, RST, JMP_EX, \是否跳转 );
  ps1 ps1_1 (
    .OP0(ID_IR[26]), .OP1(ID_IR[27]), .OP2(ID_IR[28]), .OP3(ID_IR[29]), .OP4(ID_IR[30]), .OP5(ID_IR[31]),
    .F0(Func[0]), .F1(Func[1]), .F2(Func[2]), .F3(Func[3]), .F4(Func[4]), .F5(Func[5]), .bgtz(BGTZ),
    .XOR(XOR), .SB(SB), .SUBU(SUBU));
  // Probe on IF_PC[11:0]
  // Probe on WB_PC[11:0]
  // Probe on WB_PC[11:0]
  // Mips_Probe mips_probe_5: pin names not known; wires that end beside it: IR_PC_WB
  IF_ID if_id_1 (
    .IRin(IF_IR), .PCin(IF_PC), .IRout({ID_IR, Func}), .PCout(ID_PC), .enable_out(if_id_1_enable_out),
    .rst(or_1_out), .enable(not_3_out), .clk(CLK));  // open: clear
  // Probe on EX_PC[11:0]
  // Probe on ID_PC[11:0]
  Adder #(.width(32)) adder_1 (.a(IF_PC), .b(32'h4), .out(adder_1_out));  // open: cin, cout
  // Probe on M_PC[11:0]
  // Probe on WB_PC[11:0]
  \单周期硬布线控制器  \u_单周期硬布线控制器_1  (
    .Func(Func), .OP(ID_IR[31:26]), .ALU_OP(AluOP), .MemToReg(MemToBeg), .MemWrite(MemWriteID),
    .ALU_SRC(AluSrcB), .RegWrite(RegWriteID), .SysCALL(Syscall), .SignedExt(SignedExt), .RegDst(RegDst),
    .JR(JR), .JMP(JMP), .Beq(Beq), .JAL(JAL), .Bne(Bne));
  Multiplexer #(.select(1), .width(5), .disabled("Z"), .enable("false")) multiplexer_4 (
    .in0(ID_IR[25:21]), .in1(5'b00010), .out(multiplexer_4_out), .sel(Syscall));
  assign bit_extender_1_out = {{16{1'b0}}, {ID_IR[15:6], Func}};  // Bit_Extender bit_extender_1
  assign bit_extender_2_out = {{16{ID_IR[15]}}, {ID_IR[15:6], Func}};  // Bit_Extender bit_extender_2
  Register #(.width(32), .trigger("rising"), .Select("low")) register_2 (
    .D(R2_ID), .en(display), .Q(LedData), .clk(CLK), .clr(RST));
  Multiplexer #(.select(1), .width(5), .disabled("Z"), .enable("false")) multiplexer_5 (
    .in0(ID_IR[20:16]), .in1(5'b00100), .out(multiplexer_5_out), .sel(Syscall));
  Multiplexer #(.select(1), .width(5), .disabled("Z"), .enable("false")) multiplexer_6 (
    .in0(rt_ID_WB), .in1(rd_ID_WB), .out(multiplexer_6_out), .sel(RegDst_WB));
  Multiplexer #(.select(1), .width(32), .disabled("Z"), .enable("false")) multiplexer_7 (
    .in0(bit_extender_1_out), .in1(bit_extender_2_out), .out(multiplexer_7_out), .sel(SignedExt));
  Multiplexer #(.select(1), .width(5), .disabled("Z"), .enable("false")) multiplexer_8 (
    .in0(multiplexer_6_out), .in1({5{1'b1}}), .out(multiplexer_8_out), .sel(JAL_WB));
  Multiplexer #(.select(1), .width(32), .disabled("Z"), .enable("false")) multiplexer_9 (
    .in0(multiplexer_10_out), .in1(adder_2_out), .out(RDin), .sel(JAL_WB));
  Multiplexer #(.select(1), .width(32), .disabled("Z"), .enable("false")) multiplexer_10 (
    .in0(RESULT_WB), .in1(MEMDATA_WB), .out(multiplexer_10_out), .sel(MemToBeg_WB));
  MIPS_Regifile mips_regifile_1 (
    .Din(RDin), .Clk(CLK), .R1(R1_ID), .R2(R2_ID), .WE(RegWrite), .W_num(multiplexer_8_out),
    .R1_num(multiplexer_4_out), .R2_num(multiplexer_5_out));
  Adder #(.width(32)) adder_2 (.a(32'h4), .b(WB_PC), .out(adder_2_out));  // open: cin, cout
  Counter #(.width(16), .max('hffff), .ongoal("wrap"), .trigger("rising"), .behavior("old")) counter_2 (
    .count(JMP_EX), .Q(\无条件分支数 ), .clk(CLK), .clr(RST));  // open: load, D, carry, preset
  or or_2 (or_2_out, RST, JMP_EX, \是否跳转 );
  ID_EX id_ex_1 (
    .J_JAL_imm_ID({ID_IR[25:6], Func}), .rst(or_2_out), .JMP_ID(JMP), .JR_ID(JR), .Rt_ID(ID_IR[20:16]),
    .Rd_ID(ID_IR[15:11]), .RegDst(RegDst), .JAL(JAL), .RegWrite(RegWriteID), .MemToReg(MemToBeg),
    .MemWrite(MemWriteID), .ALU_OP(AluOP), .ALU_src(AluSrcB), .Bne(Bne), .Beq(Beq), .IR_ID({ID_IR, Func}),
    .PC_ID(ID_PC), .R1_ID(R1_ID), .R2_ID(R2_ID), .IMM_ID(multiplexer_7_out), .shamt__ID(ID_IR[10:6]),
    .enable(if_id_1_enable_out), .J_JAL_imm_EX(J_JAL[27:2]), .clk(CLK), .JMP_EX(JMP_EX), .JR_EX(JR_EX),
    .Rt_EX(rt_ID_EX), .Rd_EX(rd_ID_EX), .RegDst_EX(RegDst_EX), .JAL_EX(JAL_Ex), .RegWrite_EX(RegWrite_ex),
    .MemToReg_EX(MemToBeg_ex), .MemWrite_EX(MemWrite_ex), .ALU_OP_EX(AluOP_EX), .ALU_src_EX(AluSrcB_EX),
    .Bne_EX(Bne_EX), .Beq_EX(Beq_EX), .IR_EX(EX_IR), .PC_EX(EX_PC), .R1_EX(R1EX), .R2_EX(R2EX),
    .IMM_EX(IMMEX), .shamt_EX(shamtEX), .enable_EX(enableEX), .syscall(Syscall), .syscallex(Syscall_ex),
    .SB(SB), .SB_EX(SB_EX), .equal_22_ex(equal_22_ex), .equal_22(equal_22), .bglz(BGTZ), .bglz_ex(BGTZ_EX));  // open: clear, forward_To_R1, forward_to_r1_2, forward_To_R2, forward_to_r2_2, ERET, ERET_ex
  Adder #(.width(32)) adder_3 (.a(EX_PC), .b(32'h4), .out({J_JAL[31:28], adder_3_out}));  // open: cin, cout
  Shifter #(.width(32), .shift("ll")) shifter_1 (.in(IMMEX), .\dist (5'b00010), .out(shifter_1_out));
  Multiplexer #(.select(1), .width(32), .disabled("Z"), .enable("false")) multiplexer_11 (
    .in0(R2EX), .in1(IMMEX), .out(multiplexer_11_out), .sel(AluSrcB_EX));
  or or_3 (\是否跳转 , and_4_out, and_5_out, and_6_out);
  and and_4 (and_4_out, Beq_EX, mips_alu_1_equal);
  MIPS_ALU mips_alu_1 (
    .X(R1EX), .Y(multiplexer_11_out), .AluOP(AluOP_EX), .Equal(mips_alu_1_equal), .Result(RESULT),
    .shamt(shamtEX));  // open: Result_2
  Adder #(.width(32)) adder_4 (.a({J_JAL[31:28], adder_3_out}), .b(shifter_1_out), .out(Beq_Bne));  // open: cin, cout
  and and_5 (and_5_out, not_4_out, Bne_EX);
  not not_4 (not_4_out, mips_alu_1_equal);
  Counter #(.width(16), .max('hffff), .ongoal("wrap"), .trigger("rising"), .behavior("old")) counter_3 (
    .count(\是否跳转 ), .Q(\条件分支成功数 ), .clk(CLK), .clr(RST));  // open: load, D, carry, preset
  and and_6 (and_6_out, BGTZ_EX, comparator_2_gt);
  EX_MEM ex_mem_1 (
    .Rt_ID(rt_ID_EX), .Rd_ID(rd_ID_EX), .RegDst(RegDst_EX), .JAL(JAL_Ex), .RegWrite(RegWrite_ex),
    .MemToReg(MemToBeg_ex), .MemWrite(MemWrite_ex), .ALU_OP(AluOP_EX), .ALU_src(AluSrcB_EX), .Bne(Bne_EX),
    .Beq(Beq_EX), .IR_ID(EX_IR), .PC_ID(EX_PC), .ALUresult_ID(RESULT), .R2_ID(R2EX), .enable(enableEX),
    .clk(CLK), .Rt_EX(rt_ID_MEM), .Rd_EX(rd_ID_MEM), .RegDst_EX(RegDst_MEM), .JAL_EX(JAL_MEM),
    .RegWrite_EX(RegWrite_MEM), .MemToReg_EX(MemToBeg_MEM), .MemWrite_EX(MemWrite), .ALU_OP_EX(AluOP_MEM),
    .ALU_src_EX(AluSrcB_MEM), .Bne_EX(Bne_MEM), .Beq_EX(Beq_MEM), .IR_EX(IR_PC_MEM), .PC_EX(M_PC),
    .ALU_result_EX(RESULT_MEM), .R2_EX(ex_mem_1_r2_ex), .enable_EX(ex_mem_1_enable_ex), .syscall(Syscall_ex),
    .sys_prime_call_EX(Syscall_mem), .clear(RST), .SB(SB_EX), .SB_mem(SB_MEM), .equal_22(equal_22_ex),
    .equal_22_EX(equal_22_mem));  // open: led, led_EX, bglz, bglz_mem, eret, eret_mem
  assign bit_extender_3_out = {{3{1'b0}}, RESULT[1:0]};  // Bit_Extender bit_extender_3
  Demultiplexer #(.select(2), .width(8), .tristate("false"), .disabled("Z"), .enable("false")) demultiplexer_1 (
    .out0(demultiplexer_1_out0), .out1(demultiplexer_1_out1), .out2(demultiplexer_1_out2),
    .out3(demultiplexer_1_out3), .in({8{1'b1}}), .sel(RESULT[1:0]));
  Comparator #(.width(32), .mode("twosComplement")) comparator_2 (
    .a(R1EX), .b({32{1'b0}}), .gt(comparator_2_gt));  // open: eq, lt
  assign and_7_out = ex_mem_1_r2_ex & 32'hff;  // AND_Gate and_7, 32 bits wide
  Multiplier #(.width(5)) multiplier_1 (
    .a(5'b01000), .b(bit_extender_3_out), .out(multiplier_1_out));  // open: cin, cout
  Shifter #(.width(32), .shift("ll")) shifter_2 (.in(and_7_out), .\dist (multiplier_1_out), .out(shifter_2_out));
  assign and_8_out = MEMDATA_MEM & not_5_out;  // AND_Gate and_8, 32 bits wide
  assign not_5_out = ~{demultiplexer_1_out3, demultiplexer_1_out2, demultiplexer_1_out1, demultiplexer_1_out0};  // NOT_Gate not_5, 32 bits wide
  RAM #(.addrWidth(10), .dataWidth(32), .bus("separate"), .Select("high")) ram_1 (
    .addr(RESULT_MEM[11:2]), .din(MDin), .data(MEMDATA_MEM), .str(MemWrite), .clk(CLK), .ld(1'b1), .clr(RST));  // open: sel
  Multiplexer #(.select(1), .width(32), .disabled("Z"), .enable("false")) multiplexer_12 (
    .in0(ex_mem_1_r2_ex), .in1(or_4_out), .out(MDin), .sel(SB_MEM));
  assign or_4_out = shifter_2_out | and_8_out;  // OR_Gate or_4, 32 bits wide
  MEM_WB mem_wb_1 (
    .Rt_ID(rt_ID_MEM), .Rd_ID(rd_ID_MEM), .RegDst(RegDst_MEM), .JAL(JAL_MEM), .RegWrite(RegWrite_MEM),
    .MemToReg(MemToBeg_MEM), .IR_ID(IR_PC_MEM), .PC_ID(M_PC), .alureslut(RESULT_MEM), .MemData(MEMDATA_MEM),
    .enable(ex_mem_1_enable_ex), .clk(CLK), .Rt_EX(rt_ID_WB), .Rd_EX(rd_ID_WB), .RegDst_EX(RegDst_WB),
    .JAL_EX(JAL_WB), .RegWrite_EX(RegWrite), .MemToReg_EX(MemToBeg_WB), .IR_EX(IR_PC_WB), .PC_EX(WB_PC),
    .ALUresult(RESULT_WB), .MemData_2(MEMDATA_WB), .enable_EX(enable_WB), .syscall(Syscall_mem),
    .syscall_EX(Syscall_wb), .clear(RST), .equal_22(equal_22_mem), .equal_22_EX(equal_22_wb));  // open: pause_wb, pause, led, led_wb, SB_WB_2, SB, eret, SB_WB

  // Other names for the same wires on the sheet: ID_IR[5:0] = Func; IR_PC[31:0] = {ID_IR, Func};
  //   J_JAL_imm_ID[25:0] = {ID_IR[25:6], Func}; rd_ID[4:0] = ID_IR[15:11]; rt_ID[4:0] = ID_IR[20:16];
  //   rs_ID[4:0] = ID_IR[25:21]; OP[5:0] = ID_IR[31:26]; IR_PC_EX[31:0] = EX_IR; J_JAL_imm_ID_EX[25:0] = J_JAL[27:2];
  //   MEM_IR[31:0] = IR_PC_MEM; MEM_PC[31:0] = M_PC; MemWrite_MEM = MemWrite; PC[31:0] = IF_PC;
  //   RegWrite_WB = RegWrite; WB_IR[31:0] = IR_PC_WB

  // Notes on the sheet:
  //   中断源
  //   时空图监测，可删除
  //   中断等待指示
  //   数码管输出
  //   指令存储器
  //   contents of rom_1 (hex, n*v repeats v):
  //   2011000f 112020 20020022 c 2231ffff 1e20fffb 2002000a c
  //   OP
  //   Func
  //   rs
  //   rt
  //   rd
  //   流水调试日志用
  //   JMP
  //   JR
  //   OP
  //   Func
  //   Beq
  //   Bne
  //   MemToReg
  //   MemWrite
  //   AluOP
  //   AluSrcB
  //   RegWrite
  //   JAL
  //   RegDst
  //   Syscall
  //   为方便自动评测，需要输出流水线各段保存的PC值，注意是PC不是PC+4，另外ID段寄存器写入信息，Mem段内存写入信息也要输出
endmodule

module \气泡流水线  (
  output RegWrite,
  output MemWrite,
  output [31:0] IF_PC,
  output [31:0] ID_PC,
  output [31:0] EX_PC,
  output [31:0] M_PC,
  output [31:0] WB_PC,
  output [31:0] RDin,
  output [31:0] MDin,
  output [31:0] LedData
);

  wire AluSrcB, AluSrcB_EX, AluSrcB_MEM, and_1_out, and_4_out, and_5_out, and_6_out, and_7_out, Beq, Beq_EX,
       Beq_MEM, BGTZ, BGTZ_EX, Bne, Bne_EX, Bne_MEM, CLK, clock_1_out, clock_2_out, comparator_1_eq,
       comparator_1_lt, comparator_3_gt, d_ff_1_q, display, enable_WB, enableEX, equal_22, equal_22_ex,
       equal_22_mem, equal_22_wb, ex_mem_1_enable_ex, Go, IR1, IR2, IR3, JAL, JAL_Ex, JAL_MEM, JAL_WB, JMP,
       JMP_EX, JR, JR_EX, MemToBeg, MemToBeg_ex, MemToBeg_MEM, MemToBeg_WB, MemWrite_ex, MemWriteID,
       mips_alu_1_equal, nand_1_out, not_1_out, not_2_out, not_3_out, not_4_out, not_5_out, or_1_out,
       or_2_out, or_3_out, or_4_out, or_5_out, pause, RegDst, RegDst_EX, RegDst_MEM, RegDst_WB, register_1_q,
       RegWrite_ex, RegWrite_MEM, RegWriteID, RST, SB, SB_EX, SB_MEM, SB_WB, SignedExt, SUBU, Syscall,
       Syscall_ex, Syscall_mem, Syscall_wb, W1, W2, W3, XOR, \数据相关 , \是否跳转 ;
  wire [3:0] AluOP, AluOP_EX, AluOP_MEM;
  wire [4:0] bit_extender_3_out, multiplexer_7_out, multiplexer_8_out, multiplexer_12_out,
       multiplexer_13_out, multiplexer_14_out, multiplexer_15_out, multiplier_1_out, R1_ID, R2_ID, rd_ID_EX,
       rd_ID_MEM, rd_ID_WB, rt_ID_EX, rt_ID_MEM, rt_ID_WB, shamtEX;
  wire [5:0] Func;
  wire [7:0] demultiplexer_1_out0, demultiplexer_1_out1, demultiplexer_1_out2, demultiplexer_1_out3;
  wire [12:0] CNT_num;
  wire [15:0] \LoadUse次数 , \总周期数 , \插入气泡数 , \无条件分支数 , \条件分支成功数 ;
  wire [27:0] adder_3_out;
  wire [31:0] adder_1_out, adder_2_out, and_8_out, and_9_out, Beq_Bne, bit_extender_1_out,
       bit_extender_2_out, EX_IR, ex_mem_1_r2_ex, IF_IR, IMMEX, IR_PC_MEM, IR_PC_WB, MEMDATA_MEM, MEMDATA_WB,
       multiplexer_1_out, multiplexer_2_out, multiplexer_3_out, multiplexer_6_out, multiplexer_10_out,
       multiplexer_11_out, not_6_out, or_7_out, R1_ID_t, R1EX, R2_ID_t, R2EX, RESULT, RESULT_MEM, RESULT_WB,
       shifter_1_out, shifter_2_out;
  wire [31:2] J_JAL;
  wire [31:6] ID_IR;

  Multiplexer #(.select(1), .width(32), .disabled("Z"), .enable("false")) multiplexer_1 (
    .in0(multiplexer_3_out), .in1(multiplexer_2_out), .out(multiplexer_1_out), .sel(JMP_EX));
  Multiplexer #(.select(1), .width(32), .disabled("Z"), .enable("false")) multiplexer_2 (
    .in0({J_JAL, 2'b00}), .in1(R1EX), .out(multiplexer_2_out), .sel(JR_EX));
  Multiplexer #(.select(1), .width(32), .disabled("Z"), .enable("false")) multiplexer_3 (
    .in0(adder_1_out), .in1(Beq_Bne), .out(multiplexer_3_out), .sel(\是否跳转 ));
  Button \u_总复位  (.out(RST));
  Button _1 (.out(IR1));
  Button _2 (.out(IR2));
  Button _3 (.out(IR3));
  // Probe on \总周期数 
  D_Flip_Flop #(.trigger("high"), .Pre_Clr_Positions("LEGACY"), .NegatePresetClear("false"), .enable("true"), .NewFFLayout("false")) d_ff_1 (.Q(d_ff_1_q));  // open: clk, D, Qn, preset, en, reset
  // Probe on 13'h1c9
  Button \u_继续运行  (.out(Go));
  LED #(.active("true")) led_1 (.in(W1));
  LED #(.active("true")) led_2 (.in(W2));
  LED #(.active("true")) led_3 (.in(W3));
  // Probe on IF_PC[11:0]
  // Mips_Probe mips_probe_1: pin names not known; wires that end beside it: IF_IR
  Comparator #(.width(13), .mode("twosComplement")) comparator_1 (
    .a(CNT_num), .b(13'h1c9), .eq(comparator_1_eq), .lt(comparator_1_lt));  // open: gt
  Clock #(.highDuration(1), .lowDuration(1)) clock_1 (.out(clock_1_out));
  Hex_Digit_Display hex_digit_display_1 (.value(LedData[27:24]));  // open: dp
  Hex_Digit_Display hex_digit_display_2 (.value(LedData[31:28]));  // open: dp
  // Probe on IF_PC[11:0]
  and and_1 (and_1_out, not_3_out, not_1_out);
  Register #(.width(32), .trigger("rising"), .Select("low")) PC (
    .D(multiplexer_1_out), .en(and_1_out), .Q(IF_PC), .clk(CLK), .clr(RST));
  Comparator #(.width(32), .mode("twosComplement")) comparator_2 (
    .a(R1_ID_t), .b(32'h22), .eq(equal_22));  // open: gt, lt
  Counter #(.width(13), .max('h1fff), .ongoal("stay"), .trigger("rising"), .behavior("old")) counter_1 (
    .count(comparator_1_lt), .Q(CNT_num), .clk(clock_1_out));  // open: load, D, carry, clr, preset
  Hex_Digit_Display hex_digit_display_3 (.value(LedData[23:20]));  // open: dp
  Hex_Digit_Display hex_digit_display_4 (.value(LedData[19:16]));  // open: dp
  // Probe on ID_PC[11:0]
  // Probe on ID_PC[11:0]
  // Mips_Probe mips_probe_2: pin names not known; wires that end beside it: {ID_IR, Func}
  Counter #(.width(16), .max('hffff), .ongoal("wrap"), .trigger("rising"), .behavior("old")) counter_2 (
    .count(not_3_out), .Q(\总周期数 ), .clk(CLK), .clr(RST));  // open: load, D, carry, preset
  nand nand_1 (nand_1_out, d_ff_1_q, comparator_1_eq);
  Hex_Digit_Display hex_digit_display_5 (.value(LedData[15:12]));  // open: dp
  Hex_Digit_Display hex_digit_display_6 (.value(LedData[11:8]));  // open: dp
  not not_1 (not_1_out, \数据相关 );
  and and_2 (pause, Syscall_wb, not_2_out);
  not not_2 (not_2_out, equal_22_wb);
  and and_3 (display, equal_22, Syscall);
  assign CLK = nand_1_out ? clock_1_out : 1'bz;  // Controlled_Buffer controlled_buffer_1
  Pull_Resistor #(.pull(1)) pull_resistor_1 (.node(CLK));
  Hex_Digit_Display hex_digit_display_7 (.value(LedData[3:0]));  // open: dp
  Hex_Digit_Display hex_digit_display_8 (.value(LedData[7:4]));  // open: dp
  Clock #(.highDuration(1), .lowDuration(1)) clock_2 (.out(clock_2_out));
  // Probe on EX_PC[11:0]
  // Probe on EX_PC[11:0]
  // Mips_Probe mips_probe_3: pin names not known; wires that end beside it: clock_2_out, EX_IR, CLK
  Register #(.width(1), .trigger("rising"), .Select("low")) register_1 (
    .D(Syscall_wb), .en(pause), .Q(register_1_q), .clk(CLK), .clr(or_1_out));
  not not_3 (not_3_out, register_1_q);
  Register #(.width(32), .trigger("rising"), .Select("low")) register_2 (
    .D(R2_ID_t), .en(display), .Q(LedData), .clk(CLK), .clr(RST));
  ROM #(.addrWidth(10), .dataWidth(32), .Select("high")) rom_1 (.addr(IF_PC[11:2]), .data(IF_IR));
  not not_4 (not_4_out, \数据相关 );
  or or_1 (or_1_out, Go, RST);
  // Probe on M_PC[11:0]
  // Probe on M_PC[11:0]
  // Mips_Probe mips_probe_4: pin names not known; wires that end beside it: IR_PC_MEM
  or or_2 (or_2_out, JMP_EX, \是否跳转 );
  and and_4 (and_4_out, not_4_out, not_3_out);
  // Probe on \总周期数 
  // Probe on \无条件分支数 
  // Probe on \条件分支成功数 
  // Probe on \插入气泡数 
  // Probe on \LoadUse次数 
  // Probe on WB_PC[11:0]
  // Mips_Probe mips_probe_5: pin names not known; wires that end beside it: IR_PC_WB
  or or_3 (or_3_out, RST, or_2_out);
  ps1 ps1_1 (
    .OP0(ID_IR[26]), .OP1(ID_IR[27]), .OP2(ID_IR[28]), .OP3(ID_IR[29]), .OP4(ID_IR[30]), .OP5(ID_IR[31]),
    .F0(Func[0]), .F1(Func[1]), .F2(Func[2]), .F3(Func[3]), .F4(Func[4]), .F5(Func[5]), .bgtz(BGTZ),
    .XOR(XOR), .SB(SB), .SUBU(SUBU));
  // Probe on IF_PC[11:0]
  // Probe on WB_PC[11:0]
  IF_ID if_id_1 (
    .IRin(IF_IR), .PCin(IF_PC), .IRout({ID_IR, Func}), .PCout(ID_PC), .rst(or_3_out), .enable(and_4_out),
    .clk(CLK), .clear(RST));  // open: enable_out
  Adder #(.width(32)) adder_1 (.a(IF_PC), .b(32'h4), .out(adder_1_out));  // open: cin, cout
  // Probe on ID_PC[11:0]
  // Probe on EX_PC[11:0]
  // Probe on WB_PC[11:0]
  // Probe on M_PC[11:0]
  assign bit_extender_1_out = {{16{1'b0}}, {ID_IR[15:6], Func}};  // Bit_Extender bit_extender_1
  assign bit_extender_2_out = {{16{ID_IR[15]}}, {ID_IR[15:6], Func}};  // Bit_Extender bit_extender_2
  \单周期硬布线控制器  \u_单周期硬布线控制器_1  (
    .Func(Func), .OP(ID_IR[31:26]), .ALU_OP(AluOP), .MemToReg(MemToBeg), .MemWrite(MemWriteID),
    .ALU_SRC(AluSrcB), .RegWrite(RegWriteID), .SysCALL(Syscall), .SignedExt(SignedExt), .RegDst(RegDst),
    .JR(JR), .JMP(JMP), .Beq(Beq), .JAL(JAL), .Bne(Bne));
  Multiplexer #(.select(1), .width(5), .disabled("Z"), .enable("false")) multiplexer_4 (
    .in0(ID_IR[25:21]), .in1(5'b00010), .out(R1_ID), .sel(Syscall));
  Multiplexer #(.select(1), .width(5), .disabled("Z"), .enable("false")) multiplexer_5 (
    .in0(ID_IR[20:16]), .in1(5'b00100), .out(R2_ID), .sel(Syscall));
  Multiplexer #(.select(1), .width(32), .disabled("Z"), .enable("false")) multiplexer_6 (
    .in0(bit_extender_1_out), .in1(bit_extender_2_out), .out(multiplexer_6_out), .sel(SignedExt));
  Multiplexer #(.select(1), .width(5), .disabled("Z"), .enable("false")) multiplexer_7 (
    .in0(rt_ID_WB), .in1(rd_ID_WB), .out(multiplexer_7_out), .sel(RegDst_WB));
  Multiplexer #(.select(1), .width(5), .disabled("Z"), .enable("false")) multiplexer_8 (
    .in0(multiplexer_7_out), .in1({5{1'b1}}), .out(multiplexer_8_out), .sel(JAL_WB));
  Multiplexer #(.select(1), .width(32), .disabled("Z"), .enable("false")) multiplexer_9 (
    .in0(multiplexer_10_out), .in1(adder_2_out), .out(RDin), .sel(JAL_WB));
  Multiplexer #(.select(1), .width(32), .disabled("Z"), .enable("false")) multiplexer_10 (
    .in0(RESULT_WB), .in1(MEMDATA_WB), .out(multiplexer_10_out), .sel(MemToBeg_WB));
  MIPS_Regifile mips_regifile_1 (
    .Din(RDin), .Clk(CLK), .R1(R1_ID_t), .R2(R2_ID_t), .WE(RegWrite), .W_num(multiplexer_8_out),
    .R1_num(R1_ID), .R2_num(R2_ID));
  Adder #(.width(32)) adder_2 (.a(32'h4), .b(WB_PC), .out(adder_2_out));  // open: cin, cout
  Counter #(.width(16), .max('hffff), .ongoal("wrap"), .trigger("rising"), .behavior("old")) counter_3 (
    .count(JMP_EX), .Q(\无条件分支数 ), .clk(CLK), .clr(RST));  // open: load, D, carry, preset
  Counter #(.width(16), .max('hffff), .ongoal("wrap"), .trigger("rising"), .behavior("old")) counter_4 (
    .count(\数据相关 ), .Q(\插入气泡数 ), .clk(CLK), .clr(RST));  // open: load, D, carry, preset
  or or_4 (or_4_out, JMP_EX, \是否跳转 );
  or or_5 (or_5_out, or_4_out, \数据相关 , RST);
  ID_EX id_ex_1 (
    .J_JAL_imm_ID({ID_IR[25:6], Func}), .rst(or_5_out), .JMP_ID(JMP), .JR_ID(JR), .Rt_ID(ID_IR[20:16]),
    .Rd_ID(ID_IR[15:11]), .RegDst(RegDst), .JAL(JAL), .RegWrite(RegWriteID), .MemToReg(MemToBeg),
    .MemWrite(MemWriteID), .ALU_OP(AluOP), .ALU_src(AluSrcB), .Bne(Bne), .Beq(Beq), .IR_ID({ID_IR, Func}),
    .PC_ID(ID_PC), .R1_ID(R1_ID_t), .R2_ID(R2_ID_t), .IMM_ID(multiplexer_6_out), .shamt__ID(ID_IR[10:6]),
    .enable(1'b1), .J_JAL_imm_EX(J_JAL[27:2]), .clk(CLK), .JMP_EX(JMP_EX), .JR_EX(JR_EX), .Rt_EX(rt_ID_EX),
    .Rd_EX(rd_ID_EX), .RegDst_EX(RegDst_EX), .JAL_EX(JAL_Ex), .RegWrite_EX(RegWrite_ex),
    .MemToReg_EX(MemToBeg_ex), .MemWrite_EX(MemWrite_ex), .ALU_OP_EX(AluOP_EX), .ALU_src_EX(AluSrcB_EX),
    .Bne_EX(Bne_EX), .Beq_EX(Beq_EX), .IR_EX(EX_IR), .PC_EX(EX_PC), .R1_EX(R1EX), .R2_EX(R2EX),
    .IMM_EX(IMMEX), .shamt_EX(shamtEX), .enable_EX(enableEX), .syscall(Syscall), .syscallex(Syscall_ex),
    .clear(1'b0), .SB(SB), .SB_EX(SB_EX), .equal_22_ex(equal_22_ex), .equal_22(equal_22), .bglz(BGTZ),
    .bglz_ex(BGTZ_EX));  // open: forward_To_R1, forward_to_r1_2, forward_To_R2, forward_to_r2_2, ERET, ERET_ex
  Multiplexer #(.select(1), .width(32), .disabled("Z"), .enable("false")) multiplexer_11 (
    .in0(R2EX), .in1(IMMEX), .out(multiplexer_11_out), .sel(AluSrcB_EX));
  Adder #(.width(32)) adder_3 (.a(EX_PC), .b(32'h4), .out({J_JAL[31:28], adder_3_out}));  // open: cin, cout
  Shifter #(.width(32), .shift("ll")) shifter_1 (.in(IMMEX), .\dist (5'b00010), .out(shifter_1_out));
  Multiplexer #(.select(1), .width(5), .disabled("Z"), .enable("false")) multiplexer_12 (
    .in0(rt_ID_MEM), .in1(rd_ID_MEM), .out(multiplexer_12_out), .sel(RegDst_MEM));
  Multiplexer #(.select(1), .width(5), .disabled("Z"), .enable("false")) multiplexer_13 (
    .in0(rt_ID_EX), .in1(rd_ID_EX), .out(multiplexer_13_out), .sel(RegDst_EX));
  or or_6 (\是否跳转 , and_5_out, and_6_out, and_7_out);
  and and_5 (and_5_out, Beq_EX, mips_alu_1_equal);
  not not_5 (not_5_out, mips_alu_1_equal);
  MIPS_ALU mips_alu_1 (
    .X(R1EX), .Y(multiplexer_11_out), .AluOP(AluOP_EX), .Equal(mips_alu_1_equal), .Result(RESULT),
    .shamt(shamtEX));  // open: Result_2
  Adder #(.width(32)) adder_4 (.a({J_JAL[31:28], adder_3_out}), .b(shifter_1_out), .out(Beq_Bne));  // open: cin, cout
  Multiplexer #(.select(1), .width(5), .disabled("Z"), .enable("false")) multiplexer_14 (
    .in0(multiplexer_13_out), .in1({5{1'b1}}), .out(multiplexer_14_out), .sel(JAL_Ex));
  Multiplexer #(.select(1), .width(5), .disabled("Z"), .enable("false")) multiplexer_15 (
    .in0(multiplexer_12_out), .in1({5{1'b1}}), .out(multiplexer_15_out), .sel(JAL_MEM));
  and and_6 (and_6_out, not_5_out, Bne_EX);
  Counter #(.width(16), .max('hffff), .ongoal("wrap"), .trigger("rising"), .behavior("old")) counter_5 (
    .count(\是否跳转 ), .Q(\条件分支成功数 ), .clk(CLK), .clr(RST));  // open: load, D, carry, preset
  and and_7 (and_7_out, BGTZ_EX, comparator_3_gt);
  EX_MEM ex_mem_1 (
    .Rt_ID(rt_ID_EX), .Rd_ID(rd_ID_EX), .RegDst(RegDst_EX), .JAL(JAL_Ex), .RegWrite(RegWrite_ex),
    .MemToReg(MemToBeg_ex), .MemWrite(MemWrite_ex), .ALU_OP(AluOP_EX), .ALU_src(AluSrcB_EX), .Bne(Bne_EX),
    .Beq(Beq_EX), .IR_ID(EX_IR), .PC_ID(EX_PC), .ALUresult_ID(RESULT), .R2_ID(R2EX), .enable(enableEX),
    .clk(CLK), .Rt_EX(rt_ID_MEM), .Rd_EX(rd_ID_MEM), .RegDst_EX(RegDst_MEM), .JAL_EX(JAL_MEM),
    .RegWrite_EX(RegWrite_MEM), .MemToReg_EX(MemToBeg_MEM), .MemWrite_EX(MemWrite), .ALU_OP_EX(AluOP_MEM),
    .ALU_src_EX(AluSrcB_MEM), .Bne_EX(Bne_MEM), .Beq_EX(Beq_MEM), .IR_EX(IR_PC_MEM), .PC_EX(M_PC),
    .ALU_result_EX(RESULT_MEM), .R2_EX(ex_mem_1_r2_ex), .enable_EX(ex_mem_1_enable_ex), .syscall(Syscall_ex),
    .sys_prime_call_EX(Syscall_mem), .SB(SB_EX), .SB_mem(SB_MEM), .equal_22(equal_22_ex),
    .equal_22_EX(equal_22_mem));  // open: clear, led, led_EX, bglz, bglz_mem, eret, eret_mem
  \数据相关检测  \u_数据相关检测_1  (
    .OP(ID_IR[31:26]), .Func(Func), .MEM_WriteReg(multiplexer_15_out), .EX_WriteReg(multiplexer_14_out),
    .MEM_RegWrite(RegWrite_MEM), .R2_ID(R2_ID), .EX_RegWrite(RegWrite_ex), .R1_ID(R1_ID), .stall(\数据相关 ));
  Comparator #(.width(32), .mode("twosComplement")) comparator_3 (
    .a(R1EX), .b({32{1'b0}}), .gt(comparator_3_gt));  // open: eq, lt
  assign bit_extender_3_out = {{3{1'b0}}, RESULT[1:0]};  // Bit_Extender bit_extender_3
  Demultiplexer #(.select(2), .width(8), .tristate("false"), .disabled("Z"), .enable("false")) demultiplexer_1 (
    .out0(demultiplexer_1_out0), .out1(demultiplexer_1_out1), .out2(demultiplexer_1_out2),
    .out3(demultiplexer_1_out3), .in({8{1'b1}}), .sel(RESULT[1:0]));
  RAM #(.addrWidth(10), .dataWidth(32), .bus("separate"), .Select("high")) ram_1 (
    .addr(RESULT_MEM[11:2]), .din(MDin), .data(MEMDATA_MEM), .str(MemWrite), .clk(CLK), .ld(1'b1), .clr(RST));  // open: sel
  assign and_8_out = ex_mem_1_r2_ex & 32'hff;  // AND_Gate and_8, 32 bits wide
  Multiplier #(.width(5)) multiplier_1 (
    .a(5'b01000), .b(bit_extender_3_out), .out(multiplier_1_out));  // open: cin, cout
  Shifter #(.width(32), .shift("ll")) shifter_2 (.in(and_8_out), .\dist (multiplier_1_out), .out(shifter_2_out));
  assign or_7_out = shifter_2_out | and_9_out;  // OR_Gate or_7, 32 bits wide
  assign and_9_out = MEMDATA_MEM & not_6_out;  // AND_Gate and_9, 32 bits wide
  assign not_6_out = ~{demultiplexer_1_out3, demultiplexer_1_out2, demultiplexer_1_out1, demultiplexer_1_out0};  // NOT_Gate not_6, 32 bits wide
  MEM_WB mem_wb_1 (
    .Rt_ID(rt_ID_MEM), .Rd_ID(rd_ID_MEM), .RegDst(RegDst_MEM), .JAL(JAL_MEM), .RegWrite(RegWrite_MEM),
    .MemToReg(MemToBeg_MEM), .IR_ID(IR_PC_MEM), .PC_ID(M_PC), .alureslut(RESULT_MEM), .MemData(MEMDATA_MEM),
    .enable(ex_mem_1_enable_ex), .clk(CLK), .Rt_EX(rt_ID_WB), .Rd_EX(rd_ID_WB), .RegDst_EX(RegDst_WB),
    .JAL_EX(JAL_WB), .RegWrite_EX(RegWrite), .MemToReg_EX(MemToBeg_WB), .IR_EX(IR_PC_WB), .PC_EX(WB_PC),
    .ALUresult(RESULT_WB), .MemData_2(MEMDATA_WB), .enable_EX(enable_WB), .syscall(Syscall_mem),
    .syscall_EX(Syscall_wb), .equal_22(equal_22_mem), .equal_22_EX(equal_22_wb), .SB_WB_2(SB_WB), .SB(SB_MEM));  // open: clear, pause_wb, pause, led, led_wb, eret, SB_WB
  Multiplexer #(.select(1), .width(32), .disabled("Z"), .enable("false")) multiplexer_16 (
    .in0(ex_mem_1_r2_ex), .in1(or_7_out), .out(MDin), .sel(SB_MEM));

  // Other names for the same wires on the sheet: ID_IR[5:0] = Func; IR_PC[31:0] = {ID_IR, Func};
  //   J_JAL_imm_ID[25:0] = {ID_IR[25:6], Func}; rd_ID[4:0] = ID_IR[15:11]; rt_ID[4:0] = ID_IR[20:16];
  //   rs_ID[4:0] = ID_IR[25:21]; OP[5:0] = ID_IR[31:26]; IR_PC_EX[31:0] = EX_IR; J_JAL_imm_ID_EX[25:0] = J_JAL[27:2];
  //   MEM_IR[31:0] = IR_PC_MEM; MEM_PC[31:0] = M_PC; MemWrite_MEM = MemWrite; PC[31:0] = IF_PC;
  //   RegWrite_WB = RegWrite; WB_IR[31:0] = IR_PC_WB

  // Notes on the sheet:
  //   中断源
  //   时空图监测，可删除
  //   控制位
  //   暂停节拍，不能为0
  //   中断等待指示
  //   戳工具置1进入计数暂停模式，ctrl+k时钟自动运行到对应节拍暂停
  //   ctrl+k关闭时钟连续运行，将控制位置零，进入单步调试模式调试
  //   用这个时钟源需要去掉电路中的其他时钟源
  //   数码管输出
  //   可计数暂停的时钟源
  //   指令存储器
  //   contents of rom_1 (hex, n*v repeats v):
  //   20090000 200b0020 20110000 20120001 a1310000 112020 20020022 c 2328820 21290001 216bffff 1560fff8
  //   200b0008 20090000 8d310000 112020 20020022 c 21290004 216bffff 1560fff9 2002000a c
  //   OP
  //   Func
  //   rs
  //   rt
  //   rd
  //   流水调试日志用
  //   JMP
  //   JR
  //   OP
  //   Func
  //   Beq
  //   Bne
  //   MemToReg
  //   MemWrite
  //   AluOP
  //   AluSrcB
  //   RegWrite
  //   JAL
  //   RegDst
  //   Syscall
  //   为方便自动评测，需要输出流水线各段保存的PC值，注意是PC不是PC+4，另外ID段寄存器写入信息，Mem段内存写入信息也要输出
endmodule

module \重定向流水线  (
  output RegWrite,
  output MemWrite,
  output [31:0] IF_PC,
  output [31:0] ID_PC,
  output [31:0] EX_PC,
  output [31:0] M_PC,
  output [31:0] WB_PC,
  output [31:0] RDin,
  output [31:0] MDin,
  output [31:0] LedData
);

  wire AluSrcB, AluSrcB_EX, AluSrcB_MEM, and_1_out, and_4_out, and_5_out, and_6_out, and_7_out, Beq, Beq_EX,
       Beq_MEM, BGTZ, BGTZ_EX, Bne, Bne_EX, Bne_MEM, CLK, comparator_2_gt, display, enable_WB, enableEX,
       equal_22, equal_22_mem, equal_22_wb, ex_mem_1_enable_ex, Go, IR1, IR2, IR3, JAL, JAL_Ex, JAL_MEM,
       JAL_WB, JMP, JMP_EX, JR, JR_EX, load_use, MemToBeg, MemToBeg_ex, MemToBeg_MEM, MemToBeg_WB,
       MemWrite_ex, MemWriteID, mips_alu_1_equal, not_1_out, not_2_out, not_3_out, not_4_out, not_5_out,
       or_1_out, or_2_out, or_3_out, or_4_out, or_5_out, pause, RegDst, RegDst_EX, RegDst_MEM, RegDst_WB,
       register_1_q, RegWrite_ex, RegWrite_MEM, RegWriteID, RST, SB, SB_EX, SB_MEM, SB_WB, SignedExt, SUBU,
       Syscall, Syscall_ex, Syscall_mem, Syscall_wb, W1, W2, W3, XOR, \数据相关 , \是否跳转 ;
  wire [1:0] bytechoose, forwardToR1, forwardToR1_EX, forwardToR2, forwardToR2_EX;
  wire [3:0] AluOP, AluOP_EX, AluOP_MEM;
  wire [4:0] bit_extender_3_out, multiplexer_7_out, multiplexer_8_out, multiplexer_11_out,
       multiplexer_12_out, multiplexer_13_out, multiplexer_14_out, multiplier_1_out, R1_ID, R2_ID, rd_ID_EX,
       rd_ID_MEM, rd_ID_WB, rt_ID_EX, rt_ID_MEM, rt_ID_WB, shamtEX;
  wire [5:0] Func;
  wire [7:0] demultiplexer_1_out0, demultiplexer_1_out1, demultiplexer_1_out2, demultiplexer_1_out3;
  wire [15:0] \LoadUse次数 , \总周期数 , \插入气泡数 , \无条件分支数 , \条件分支成功数 ;
  wire [27:0] adder_3_out;
  wire [31:0] adder_1_out, adder_2_out, and_8_out, and_9_out, Beq_Bne, bit_extender_1_out,
       bit_extender_2_out, EX_IR, ex_mem_1_r2_ex, IF_IR, IMMEX, IR_PC_MEM, IR_PC_WB, LedData_in, LedData_mem,
       MEMDATA_MEM, MEMDATA_WB, multiplexer_1_out, multiplexer_2_out, multiplexer_3_out, multiplexer_6_out,
       multiplexer_10_out, multiplexer_17_out, not_6_out, or_7_out, R1_ID_t, R1_USE, R1EX, R2_ID_t, R2_USE,
       R2EX, RESULT, RESULT_WB, shifter_1_out, shifter_2_out;
  wire [31:2] J_JAL, RESULT_MEM;
  wire [31:6] ID_IR;

  Multiplexer #(.select(1), .width(32), .disabled("Z"), .enable("false")) multiplexer_1 (
    .in0(multiplexer_3_out), .in1(multiplexer_2_out), .out(multiplexer_1_out), .sel(JMP_EX));
  Multiplexer #(.select(1), .width(32), .disabled("Z"), .enable("false")) multiplexer_2 (
    .in0({J_JAL, 2'b00}), .in1(R1EX), .out(multiplexer_2_out), .sel(JR_EX));
  Multiplexer #(.select(1), .width(32), .disabled("Z"), .enable("false")) multiplexer_3 (
    .in0(adder_1_out), .in1(Beq_Bne), .out(multiplexer_3_out), .sel(\是否跳转 ));
  Button \u_总复位  (.out(RST));
  Button _1 (.out(IR1));
  Button _2 (.out(IR2));
  Button _3 (.out(IR3));
  // Probe on \总周期数 
  Button \u_继续运行  (.out(Go));
  LED #(.active("true")) led_1 (.in(W1));
  LED #(.active("true")) led_2 (.in(W2));
  LED #(.active("true")) led_3 (.in(W3));
  // Probe on IF_PC[11:0]
  // Mips_Probe mips_probe_1: pin names not known; wires that end beside it: IF_IR
  Hex_Digit_Display hex_digit_display_1 (.value(LedData[31:28]));  // open: dp
  Hex_Digit_Display hex_digit_display_2 (.value(LedData[27:24]));  // open: dp
  // Probe on IF_PC[11:0]
  and and_1 (and_1_out, not_2_out, not_1_out);
  Register #(.width(32), .trigger("rising"), .Select("low")) PC (
    .D(multiplexer_1_out), .en(and_1_out), .Q(IF_PC), .clk(CLK), .clr(RST));
  Comparator #(.width(32), .mode("twosComplement")) comparator_1 (
    .a(R1_USE), .b(32'h22), .eq(equal_22));  // open: gt, lt
  Hex_Digit_Display hex_digit_display_3 (.value(LedData[19:16]));  // open: dp
  Hex_Digit_Display hex_digit_display_4 (.value(LedData[23:20]));  // open: dp
  // Probe on ID_PC[11:0]
  // Probe on ID_PC[11:0]
  // Mips_Probe mips_probe_2: pin names not known; wires that end beside it: {ID_IR, Func}
  Counter #(.width(16), .max('hffff), .ongoal("wrap"), .trigger("rising"), .behavior("old")) counter_1 (
    .count(not_2_out), .Q(\总周期数 ), .clk(CLK), .clr(RST));  // open: load, D, carry, preset
  Hex_Digit_Display hex_digit_display_5 (.value(LedData[11:8]));  // open: dp
  Hex_Digit_Display hex_digit_display_6 (.value(LedData[15:12]));  // open: dp
  not not_1 (not_1_out, load_use);
  not not_2 (not_2_out, register_1_q);
  Register #(.width(1), .trigger("rising"), .Select("low")) register_1 (
    .D(Syscall_wb), .en(pause), .Q(register_1_q), .clk(CLK), .clr(or_1_out));
  and and_2 (pause, Syscall_wb, not_3_out);
  not not_3 (not_3_out, equal_22_wb);
  and and_3 (display, equal_22, Syscall_ex);
  Hex_Digit_Display hex_digit_display_7 (.value(LedData[3:0]));  // open: dp
  Hex_Digit_Display hex_digit_display_8 (.value(LedData[7:4]));  // open: dp
  Clock #(.highDuration(1), .lowDuration(1)) clock_1 (.out(CLK));
  // Probe on EX_PC[11:0]
  // Probe on EX_PC[11:0]
  // Mips_Probe mips_probe_3: pin names not known; wires that end beside it: EX_IR
  or or_1 (or_1_out, Go, RST);
  ROM #(.addrWidth(10), .dataWidth(32), .Select("high")) rom_1 (.addr(IF_PC[11:2]), .data(IF_IR));
  not not_4 (not_4_out, load_use);
  // Probe on M_PC[11:0]
  // Probe on M_PC[11:0]
  // Mips_Probe mips_probe_4: pin names not known; wires that end beside it: IR_PC_MEM
  or or_2 (or_2_out, JMP_EX, \是否跳转 );
  and and_4 (and_4_out, not_4_out, not_2_out);
  // Probe on \总周期数 
  // Probe on \无条件分支数 
  // Probe on \条件分支成功数 
  // Probe on \插入气泡数 
  // Probe on \LoadUse次数 
  // Probe on WB_PC[11:0]
  // Mips_Probe mips_probe_5: pin names not known; wires that end beside it: IR_PC_WB
  or or_3 (or_3_out, RST, or_2_out);
  ps1 ps1_1 (
    .OP0(ID_IR[26]), .OP1(ID_IR[27]), .OP2(ID_IR[28]), .OP3(ID_IR[29]), .OP4(ID_IR[30]), .OP5(ID_IR[31]),
    .F0(Func[0]), .F1(Func[1]), .F2(Func[2]), .F3(Func[3]), .F4(Func[4]), .F5(Func[5]), .bgtz(BGTZ),
    .XOR(XOR), .SB(SB), .SUBU(SUBU));
  // Probe on IF_PC[11:0]
  // Probe on WB_PC[11:0]
  IF_ID if_id_1 (
    .IRin(IF_IR), .PCin(IF_PC), .IRout({ID_IR, Func}), .PCout(ID_PC), .rst(or_3_out), .enable(and_4_out),
    .clk(CLK), .clear(RST));  // open: enable_out
  Adder #(.width(32)) adder_1 (.a(IF_PC), .b(32'h4), .out(adder_1_out));  // open: cin, cout
  // Probe on ID_PC[11:0]
  // Probe on EX_PC[11:0]
  // Probe on M_PC[11:0]
  // Probe on WB_PC[11:0]
  assign bit_extender_1_out = {{16{1'b0}}, {ID_IR[15:6], Func}};  // Bit_Extender bit_extender_1
  assign bit_extender_2_out = {{16{ID_IR[15]}}, {ID_IR[15:6], Func}};  // Bit_Extender bit_extender_2
  \单周期硬布线控制器  \u_单周期硬布线控制器_1  (
    .Func(Func), .OP(ID_IR[31:26]), .ALU_OP(AluOP), .MemToReg(MemToBeg), .MemWrite(MemWriteID),
    .ALU_SRC(AluSrcB), .RegWrite(RegWriteID), .SysCALL(Syscall), .SignedExt(SignedExt), .RegDst(RegDst),
    .JR(JR), .JMP(JMP), .Beq(Beq), .JAL(JAL), .Bne(Bne));
  Multiplexer #(.select(1), .width(5), .disabled("Z"), .enable("false")) multiplexer_4 (
    .in0(ID_IR[25:21]), .in1(5'b00010), .out(R1_ID), .sel(Syscall));
  Multiplexer #(.select(1), .width(5), .disabled("Z"), .enable("false")) multiplexer_5 (
    .in0(ID_IR[20:16]), .in1(5'b00100), .out(R2_ID), .sel(Syscall));
  Multiplexer #(.select(1), .width(32), .disabled("Z"), .enable("false")) multiplexer_6 (
    .in0(bit_extender_1_out), .in1(bit_extender_2_out), .out(multiplexer_6_out), .sel(SignedExt));
  Register #(.width(32), .trigger("rising"), .Select("low")) register_2 (
    .D(R2_USE), .en(display), .Q(LedData_in), .clk(CLK), .clr(RST));
  Multiplexer #(.select(1), .width(5), .disabled("Z"), .enable("false")) multiplexer_7 (
    .in0(rt_ID_WB), .in1(rd_ID_WB), .out(multiplexer_7_out), .sel(RegDst_WB));
  Multiplexer #(.select(1), .width(5), .disabled("Z"), .enable("false")) multiplexer_8 (
    .in0(multiplexer_7_out), .in1({5{1'b1}}), .out(multiplexer_8_out), .sel(JAL_WB));
  Multiplexer #(.select(1), .width(32), .disabled("Z"), .enable("false")) multiplexer_9 (
    .in0(multiplexer_10_out), .in1(adder_2_out), .out(RDin), .sel(JAL_WB));
  Multiplexer #(.select(1), .width(32), .disabled("Z"), .enable("false")) multiplexer_10 (
    .in0(RESULT_WB), .in1(MEMDATA_WB), .out(multiplexer_10_out), .sel(MemToBeg_WB));
  MIPS_Regifile mips_regifile_1 (
    .Din(RDin), .Clk(CLK), .R1(R1_ID_t), .R2(R2_ID_t), .WE(RegWrite), .W_num(multiplexer_8_out),
    .R1_num(R1_ID), .R2_num(R2_ID));
  Adder #(.width(32)) adder_2 (.a(32'h4), .b(WB_PC), .out(adder_2_out));  // open: cin, cout
  Counter #(.width(16), .max('hffff), .ongoal("wrap"), .trigger("rising"), .behavior("old")) counter_2 (
    .count(JMP_EX), .Q(\无条件分支数 ), .clk(CLK), .clr(RST));  // open: load, D, carry, preset
  Counter #(.width(16), .max('hffff), .ongoal("wrap"), .trigger("rising"), .behavior("old")) counter_3 (
    .count(load_use), .Q(\插入气泡数 ), .clk(CLK), .clr(RST));  // open: load, D, carry, preset
  or or_4 (or_4_out, JMP_EX, \是否跳转 );
  or or_5 (or_5_out, or_4_out, load_use, RST);
  ID_EX id_ex_1 (
    .J_JAL_imm_ID({ID_IR[25:6], Func}), .rst(or_5_out), .JMP_ID(JMP), .JR_ID(JR), .Rt_ID(ID_IR[20:16]),
    .Rd_ID(ID_IR[15:11]), .RegDst(RegDst), .JAL(JAL), .RegWrite(RegWriteID), .MemToReg(MemToBeg),
    .MemWrite(MemWriteID), .ALU_OP(AluOP), .ALU_src(AluSrcB), .Bne(Bne), .Beq(Beq), .IR_ID({ID_IR, Func}),
    .PC_ID(ID_PC), .R1_ID(R1_ID_t), .R2_ID(R2_ID_t), .IMM_ID(multiplexer_6_out), .shamt__ID(ID_IR[10:6]),
    .enable(not_2_out), .J_JAL_imm_EX(J_JAL[27:2]), .clk(CLK), .JMP_EX(JMP_EX), .JR_EX(JR_EX),
    .Rt_EX(rt_ID_EX), .Rd_EX(rd_ID_EX), .RegDst_EX(RegDst_EX), .JAL_EX(JAL_Ex), .RegWrite_EX(RegWrite_ex),
    .MemToReg_EX(MemToBeg_ex), .MemWrite_EX(MemWrite_ex), .ALU_OP_EX(AluOP_EX), .ALU_src_EX(AluSrcB_EX),
    .Bne_EX(Bne_EX), .Beq_EX(Beq_EX), .IR_EX(EX_IR), .PC_EX(EX_PC), .R1_EX(R1EX), .R2_EX(R2EX),
    .IMM_EX(IMMEX), .shamt_EX(shamtEX), .enable_EX(enableEX), .syscall(Syscall), .syscallex(Syscall_ex),
    .clear(1'b0), .SB(SB), .SB_EX(SB_EX), .forward_To_R1(forwardToR1), .forward_to_r1_2(forwardToR1_EX),
    .forward_To_R2(forwardToR2), .forward_to_r2_2(forwardToR2_EX), .bglz(BGTZ), .bglz_ex(BGTZ_EX));  // open: equal_22_ex, equal_22, ERET, ERET_ex
  Adder #(.width(32)) adder_3 (.a(EX_PC), .b(32'h4), .out({J_JAL[31:28], adder_3_out}));  // open: cin, cout
  Shifter #(.width(32), .shift("ll")) shifter_1 (.in(IMMEX), .\dist (5'b00010), .out(shifter_1_out));
  Multiplexer #(.select(1), .width(5), .disabled("Z"), .enable("false")) multiplexer_11 (
    .in0(rt_ID_MEM), .in1(rd_ID_MEM), .out(multiplexer_11_out), .sel(RegDst_MEM));
  Multiplexer #(.select(1), .width(5), .disabled("Z"), .enable("false")) multiplexer_12 (
    .in0(rt_ID_EX), .in1(rd_ID_EX), .out(multiplexer_12_out), .sel(RegDst_EX));
  Adder #(.width(32)) adder_4 (.a({J_JAL[31:28], adder_3_out}), .b(shifter_1_out), .out(Beq_Bne));  // open: cin, cout
  Multiplexer #(.select(1), .width(5), .disabled("Z"), .enable("false")) multiplexer_13 (
    .in0(multiplexer_12_out), .in1({5{1'b1}}), .out(multiplexer_13_out), .sel(JAL_Ex));
  Multiplexer #(.select(1), .width(5), .disabled("Z"), .enable("false")) multiplexer_14 (
    .in0(multiplexer_11_out), .in1({5{1'b1}}), .out(multiplexer_14_out), .sel(JAL_MEM));
  Multiplexer #(.select(2), .width(32), .disabled("Z"), .enable("false")) multiplexer_15 (
    .in0(R1EX), .in1(MEMDATA_WB), .in2(RESULT_WB), .in3({RESULT_MEM, bytechoose}), .out(R1_USE),
    .sel(forwardToR1_EX));
  Multiplexer #(.select(2), .width(32), .disabled("Z"), .enable("false")) multiplexer_16 (
    .in0(R2EX), .in1(MEMDATA_WB), .in2(RESULT_WB), .in3({RESULT_MEM, bytechoose}), .out(R2_USE),
    .sel(forwardToR2_EX));
  \数据相关检测  \u_数据相关检测_1  (
    .OP(ID_IR[31:26]), .Func(Func), .MEM_WriteReg(multiplexer_14_out), .EX_WriteReg(multiplexer_13_out),
    .MEM_RegWrite(RegWrite_MEM), .R2_ID(R2_ID), .EX_RegWrite(RegWrite_ex), .R1_ID(R1_ID), .stall(\数据相关 ));
  \重定向检测  \u_重定向检测_1  (
    .OP(ID_IR[31:26]), .Func(Func), .MEM_memtoreg(MemToBeg_MEM), .EX_memtoreg(MemToBeg_ex),
    .MEM_WriteReg(multiplexer_14_out), .EX_WriteReg(multiplexer_13_out), .MEM_RegWrite(RegWrite_MEM),
    .R2_ID(R2_ID), .EX_RegWrite(RegWrite_ex), .R1_ID(R1_ID), .forwardToR1(forwardToR1), .loaduse(load_use),
    .forwardToR2(forwardToR2));
  Multiplexer #(.select(1), .width(32), .disabled("Z"), .enable("false")) multiplexer_17 (
    .in0(R2_USE), .in1(IMMEX), .out(multiplexer_17_out), .sel(AluSrcB_EX));
  or or_6 (\是否跳转 , and_5_out, and_6_out, and_7_out);
  and and_5 (and_5_out, Beq_EX, mips_alu_1_equal);
  and and_6 (and_6_out, not_5_out, Bne_EX);
  not not_5 (not_5_out, mips_alu_1_equal);
  MIPS_ALU mips_alu_1 (
    .X(R1_USE), .Y(multiplexer_17_out), .AluOP(AluOP_EX), .Equal(mips_alu_1_equal), .Result(RESULT),
    .shamt(shamtEX));  // open: Result_2
  Counter #(.width(16), .max('hffff), .ongoal("wrap"), .trigger("rising"), .behavior("old")) counter_4 (
    .count(\是否跳转 ), .Q(\条件分支成功数 ), .clk(CLK), .clr(RST));  // open: load, D, carry, preset
  and and_7 (and_7_out, BGTZ_EX, comparator_2_gt);
  EX_MEM ex_mem_1 (
    .Rt_ID(rt_ID_EX), .Rd_ID(rd_ID_EX), .RegDst(RegDst_EX), .JAL(JAL_Ex), .RegWrite(RegWrite_ex),
    .MemToReg(MemToBeg_ex), .MemWrite(MemWrite_ex), .ALU_OP(AluOP_EX), .ALU_src(AluSrcB_EX), .Bne(Bne_EX),
    .Beq(Beq_EX), .IR_ID(EX_IR), .PC_ID(EX_PC), .ALUresult_ID(RESULT), .R2_ID(R2_USE), .enable(enableEX),
    .clk(CLK), .Rt_EX(rt_ID_MEM), .Rd_EX(rd_ID_MEM), .RegDst_EX(RegDst_MEM), .JAL_EX(JAL_MEM),
    .RegWrite_EX(RegWrite_MEM), .MemToReg_EX(MemToBeg_MEM), .MemWrite_EX(MemWrite), .ALU_OP_EX(AluOP_MEM),
    .ALU_src_EX(AluSrcB_MEM), .Bne_EX(Bne_MEM), .Beq_EX(Beq_MEM), .IR_EX(IR_PC_MEM), .PC_EX(M_PC),
    .ALU_result_EX({RESULT_MEM, bytechoose}), .R2_EX(ex_mem_1_r2_ex), .enable_EX(ex_mem_1_enable_ex),
    .syscall(Syscall_ex), .sys_prime_call_EX(Syscall_mem), .SB(SB_EX), .SB_mem(SB_MEM), .led(LedData_in),
    .led_EX(LedData_mem), .equal_22(equal_22), .equal_22_EX(equal_22_mem));  // open: clear, bglz, bglz_mem, eret, eret_mem
  Comparator #(.width(32), .mode("twosComplement")) comparator_2 (
    .a(R1_USE), .b({32{1'b0}}), .gt(comparator_2_gt));  // open: eq, lt
  assign bit_extender_3_out = {{3{1'b0}}, RESULT[1:0]};  // Bit_Extender bit_extender_3
  Demultiplexer #(.select(2), .width(8), .tristate("false"), .disabled("Z"), .enable("false")) demultiplexer_1 (
    .out0(demultiplexer_1_out0), .out1(demultiplexer_1_out1), .out2(demultiplexer_1_out2),
    .out3(demultiplexer_1_out3), .in({8{1'b1}}), .sel(RESULT[1:0]));
  assign and_8_out = ex_mem_1_r2_ex & 32'hff;  // AND_Gate and_8, 32 bits wide
  Multiplier #(.width(5)) multiplier_1 (
    .a(5'b01000), .b(bit_extender_3_out), .out(multiplier_1_out));  // open: cin, cout
  RAM #(.addrWidth(10), .dataWidth(32), .bus("separate"), .Select("high")) ram_1 (
    .addr(RESULT_MEM[11:2]), .din(MDin), .data(MEMDATA_MEM), .str(MemWrite), .clk(CLK), .ld(1'b1), .clr(RST));  // open: sel
  Shifter #(.width(32), .shift("ll")) shifter_2 (.in(and_8_out), .\dist (multiplier_1_out), .out(shifter_2_out));
  assign or_7_out = shifter_2_out | and_9_out;  // OR_Gate or_7, 32 bits wide
  assign and_9_out = MEMDATA_MEM & not_6_out;  // AND_Gate and_9, 32 bits wide
  assign not_6_out = ~{demultiplexer_1_out3, demultiplexer_1_out2, demultiplexer_1_out1, demultiplexer_1_out0};  // NOT_Gate not_6, 32 bits wide
  Multiplexer #(.select(1), .width(32), .disabled("Z"), .enable("false")) multiplexer_18 (
    .in0(ex_mem_1_r2_ex), .in1(or_7_out), .out(MDin), .sel(SB_MEM));
  MEM_WB mem_wb_1 (
    .Rt_ID(rt_ID_MEM), .Rd_ID(rd_ID_MEM), .RegDst(RegDst_MEM), .JAL(JAL_MEM), .RegWrite(RegWrite_MEM),
    .MemToReg(MemToBeg_MEM), .IR_ID(IR_PC_MEM), .PC_ID(M_PC), .alureslut({RESULT_MEM, bytechoose}),
    .MemData(MEMDATA_MEM), .enable(ex_mem_1_enable_ex), .clk(CLK), .Rt_EX(rt_ID_WB), .Rd_EX(rd_ID_WB),
    .RegDst_EX(RegDst_WB), .JAL_EX(JAL_WB), .RegWrite_EX(RegWrite), .MemToReg_EX(MemToBeg_WB),
    .IR_EX(IR_PC_WB), .PC_EX(WB_PC), .ALUresult(RESULT_WB), .MemData_2(MEMDATA_WB), .enable_EX(enable_WB),
    .syscall(Syscall_mem), .syscall_EX(Syscall_wb), .led(LedData_mem), .led_wb(LedData),
    .equal_22(equal_22_mem), .equal_22_EX(equal_22_wb), .SB_WB_2(SB_WB), .SB(SB_MEM));  // open: clear, pause_wb, pause, eret, SB_WB

  // Other names for the same wires on the sheet: ID_IR[5:0] = Func; IR_PC[31:0] = {ID_IR, Func};
  //   J_JAL_imm_ID[25:0] = {ID_IR[25:6], Func}; rd_ID[4:0] = ID_IR[15:11]; rt_ID[4:0] = ID_IR[20:16];
  //   rs_ID[4:0] = ID_IR[25:21]; OP[5:0] = ID_IR[31:26]; IR_PC_EX[31:0] = EX_IR; J_JAL_imm_ID_EX[25:0] = J_JAL[27:2];
  //   MEM_IR[31:0] = IR_PC_MEM; MEM_PC[31:0] = M_PC; MemWrite_MEM = MemWrite; PC[31:0] = IF_PC;
  //   RegWrite_WB = RegWrite; RESULT_MEM[1:0] = bytechoose; WB_IR[31:0] = IR_PC_WB

  // Notes on the sheet:
  //   中断源
  //   时空图监测，可删除
  //   中断等待指示
  //   数码管输出
  //   指令存储器
  //   contents of rom_1 (hex, n*v repeats v):
  //   201d07d0 20100001 109fc0 139fc3 8021 2012000c 24160008 26100001 3210000f 20080008 20090001 139900
  //   2709825 132020 20020022 c 1094022 1500fff9 22100001 2018000f 2188024 108700 20080008 20090001 139902
  //   2709825 132021 20020022 c 1094022 1500fff9 108702 2c9b022 12c00001 8000c07 4020 1084027 84400
  //   3508ffff 82021 20020022 c 8000c01 afa20000 23bd0004 afa40000 23bd0004 afb00000 23bd0004 afb30000
  //   23bd0004 afb40000 23bd0004 afb50000 23bd0004 afb60000 23bd0004 20160001 20140003 20150001 168020
  //   108100 2149825 132020 20020022 c 1600fffa 295a022 1680fff7 23bdfffc 8fb60000 23bdfffc 8fb50000
  //   23bdfffc 8fb40000 23bdfffc 8fb30000 23bdfffc 8fb00000 23bdfffc 8fa40000 23bdfffc 8fa20000 42000018
  //   afa20000 23bd0004 afa40000 23bd0004 afb00000 23bd0004 afb30000 23bd0004 afb40000 23bd0004 afb50000
  //   23bd0004 afb60000 23bd0004 20160002 20140003 20150001 168020 108100 2149825 132020 20020022 c
  //   1600fffa 295a022 1680fff7 23bdfffc 8fb60000 23bdfffc 8fb50000 23bdfffc 8fb40000 23bdfffc 8fb30000
  //   23bdfffc 8fb00000 23bdfffc 8fa40000 23bdfffc 8fa20000 42000018 afa20000 23bd0004 afa40000 23bd0004
  //   afb00000 23bd0004 afb30000 23bd0004 afb40000 23bd0004 afb50000 23bd0004 afb60000 23bd0004 20160003
  //   20140003 20150001 168020 108100 2149825 132020 20020022 c 1600fffa 295a022 1680fff7 23bdfffc
  //   8fb60000 23bdfffc 8fb50000 23bdfffc 8fb40000 23bdfffc 8fb30000 23bdfffc 8fb00000 23bdfffc 8fa40000
  //   23bdfffc 8fa20000 42000018
  //   OP
  //   Func
  //   rs
  //   rt
  //   rd
  //   流水调试日志用
  //   JMP
  //   JR
  //   OP
  //   Func
  //   Beq
  //   Bne
  //   MemToReg
  //   MemWrite
  //   AluOP
  //   AluSrcB
  //   RegWrite
  //   JAL
  //   RegDst
  //   Syscall
  //   为方便自动评测，需要输出流水线各段保存的PC值，注意是PC不是PC+4，另外ID段寄存器写入信息，Mem段内存写入信息也要输出
endmodule
module \单周期MIPS_单级中断  (
  input  IR1,
  input  IR2,
  input  IR3,
  output RegWrite,
  output MemWrite,
  output [31:0] PC,
  output [31:0] IR,
  output [31:0] RDin,
  output [31:0] MDin,
  output [31:0] LedData
);

  wire and_1_out, and_5_out, and_9_out, and_10_out, BGTZ, CLK, comparator_2_eq, comparator_3_gt,
       decoder_1_out1, decoder_1_out2, decoder_1_out3, display, ERET, Go, IE, IR1_t, IR2_t, IR3_t, IRA, IRB,
       IRC, JAL, JMP, JR, MemToReg, mips_alu_1_equal, not_1_out, not_2_out, not_3_out, not_4_out, not_5_out,
       O_C, or_2_out, pause, RET1, RET2, RET3, RST, SB, SignedExt, SUBU, Syscall, W1, W2, W3, XOR, \中断位与1 ,
       \中断位与2 , \中断位与3 , \单周期硬布线控制器_1_alu_src , \单周期硬布线控制器_1_beq , \单周期硬布线控制器_1_bne , \单周期硬布线控制器_1_regdst ,
       \开中断 , \是否跳转 ;
  wire [1:0] bytechoose, priority_encoder_1_out, register_2_q;
  wire [3:0] \单周期硬布线控制器_1_alu_op ;
  wire [4:0] bit_extender_3_out, multiplexer_7_out, multiplexer_10_out, multiplexer_12_out,
       multiplexer_13_out, multiplier_1_out;
  wire [7:0] demultiplexer_1_out0, demultiplexer_1_out1, demultiplexer_1_out2, demultiplexer_1_out3;
  wire [15:0] \总周期数 , \无条件分支数 , \条件分支成功数 ;
  wire [27:0] adder_1_out_2;
  wire [31:0] adder_2_out, and_11_out, and_12_out, bit_extender_1_out, bit_extender_2_out, EPC,
       multiplexer_1_out, multiplexer_2_out, multiplexer_4_out, multiplexer_5_out, multiplexer_8_out,
       multiplexer_11_out, multiplexer_14_out, not_6_out, or_6_out, PC_4, R1, R2, ram_1_data, shifter_1_out,
       shifter_2_out, \中断程序入口地址 ;
  wire [31:2] mips_alu_1_result;
  wire [31:28] adder_1_out;

  Clock #(.highDuration(1), .lowDuration(1)) clock_1 (.out(CLK));
  Button _1 (.out(IRA));
  Button _2 (.out(IRB));
  Button _3 (.out(IRC));
  Multiplexer #(.select(1), .width(32), .disabled("Z"), .enable("false")) multiplexer_1 (
    .in0({adder_1_out, IR[25:0], 2'b00}), .in1(R2), .out(multiplexer_1_out), .sel(JR));
  Multiplexer #(.select(1), .width(32), .disabled("Z"), .enable("false")) multiplexer_2 (
    .in0({adder_1_out, adder_1_out_2}), .in1(adder_2_out), .out(multiplexer_2_out), .sel(\是否跳转 ));
  Button \u_继续运行  (.out(Go));
  LED #(.active("true")) led_1 (.in(W1));
  LED #(.active("true")) led_2 (.in(W2));
  LED #(.active("true")) led_3 (.in(W3));
  Multiplexer #(.select(1), .width(32), .disabled("Z"), .enable("false")) multiplexer_3 (
    .in0(multiplexer_2_out), .in1(multiplexer_1_out), .out(PC_4), .sel(JMP));
  Hex_Digit_Display hex_digit_display_1 (.value(LedData[31:28]));  // open: dp
  Counter #(.width(16), .max('hffff), .ongoal("wrap"), .trigger("rising"), .behavior("old")) counter_1 (
    .count(not_1_out), .Q(\总周期数 ), .clk(CLK), .clr(RST));  // open: load, D, carry, preset
  Multiplexer #(.select(1), .width(32), .disabled("Z"), .enable("false")) multiplexer_4 (
    .in0(PC_4), .in1(\中断程序入口地址 ), .out(multiplexer_4_out), .sel(O_C));
  Hex_Digit_Display hex_digit_display_2 (.value(LedData[27:24]));  // open: dp
  Hex_Digit_Display hex_digit_display_3 (.value(LedData[23:20]));  // open: dp
  Multiplexer #(.select(1), .width(32), .disabled("Z"), .enable("false")) multiplexer_5 (
    .in0(multiplexer_4_out), .in1(EPC), .out(multiplexer_5_out), .sel(ERET));
  \中断信号采样电路  \u_中断信号采样电路_1  (.clk(CLK), .\_1号中断信号 (IR1_t), .\中断等待指示灯 (W1), .\与中断屏蔽位与 (\中断位与1 ), .\同步清零信号 (RET1));
  \中断信号采样电路  \u_中断信号采样电路_2  (.clk(CLK), .\_1号中断信号 (IR2_t), .\中断等待指示灯 (W2), .\与中断屏蔽位与 (\中断位与2 ), .\同步清零信号 (RET2));
  \中断信号采样电路  \u_中断信号采样电路_3  (.clk(CLK), .\_1号中断信号 (IR3_t), .\中断等待指示灯 (W3), .\与中断屏蔽位与 (\中断位与3 ), .\同步清零信号 (RET3));
  Hex_Digit_Display hex_digit_display_4 (.value(LedData[15:12]));  // open: dp
  Hex_Digit_Display hex_digit_display_5 (.value(LedData[19:16]));  // open: dp
  not not_1 (not_1_out, and_1_out);
  and and_1 (and_1_out, not_2_out, pause);
  not not_2 (not_2_out, Go);
  Register #(.width(32), .trigger("rising"), .Select("low")) u_PC (
    .D(multiplexer_5_out), .en(not_1_out), .Q(PC), .clk(CLK), .clr(RST));
  Comparator #(.width(32), .mode("twosComplement")) comparator_1 (.a(IR), .b(32'h42000018), .eq(ERET));  // open: gt, lt
  Hex_Digit_Display hex_digit_display_6 (.value(LedData[7:4]));  // open: dp
  Hex_Digit_Display hex_digit_display_7 (.value(LedData[11:8]));  // open: dp
  // Mips_Probe mips_probe_1: pin names not known; wires that end beside it: IR
  Adder #(.width(32)) adder_1 (.a(PC), .b(32'h4), .out({adder_1_out, adder_1_out_2}));  // open: cin, cout
  Adder #(.width(32)) adder_2 (
    .a({adder_1_out, adder_1_out_2}), .b(shifter_1_out), .out(adder_2_out));  // open: cin, cout
  Hex_Digit_Display hex_digit_display_8 (.value(LedData[3:0]));  // open: dp
  // Probe on \总周期数 
  Comparator #(.width(32), .mode("twosComplement")) comparator_2 (
    .a(R1), .b(32'h22), .eq(comparator_2_eq));  // open: gt, lt
  ROM #(.addrWidth(10), .dataWidth(32), .Select("high")) rom_1 (.addr(PC[11:2]), .data(IR));
  or or_1 (IR1_t, IR1, IRA);
  and and_2 (pause, Syscall, not_3_out);
  not not_3 (not_3_out, comparator_2_eq);
  and and_3 (display, comparator_2_eq, Syscall);
  Register #(.width(32), .trigger("rising"), .Select("low")) register_1 (
    .D(R2), .en(display), .Q(LedData), .clk(CLK), .clr(RST));
  Priority_Encoder #(.select(2), .disabled("Z")) priority_encoder_1 (
    .in0(1'b0), .in1(\中断位与1 ), .in2(\中断位与2 ), .in3(\中断位与3 ), .out(priority_encoder_1_out), .gs(\开中断 ),
    .en_in(1'b1));  // open: en_out
  // Probe on IR
  ps1 ps1_1 (
    .OP0(IR[26]), .OP1(IR[27]), .OP2(IR[28]), .OP3(IR[29]), .OP4(IR[30]), .OP5(IR[31]), .F0(IR[0]),
    .F1(IR[1]), .F2(IR[2]), .F3(IR[3]), .F4(IR[4]), .F5(IR[5]), .bgtz(BGTZ), .XOR(XOR), .SB(SB), .SUBU(SUBU));
  or or_2 (or_2_out, O_C, ERET);
  or or_3 (IR2_t, IR2, IRB);
  Multiplexer #(.select(1), .width(32), .disabled("Z"), .enable("false")) multiplexer_6 (
    .in0(multiplexer_8_out), .in1({adder_1_out, adder_1_out_2}), .out(RDin), .sel(JAL));
  Register #(.width(32), .trigger("rising"), .Select("low")) \u_异常程序计数器  (
    .D(PC_4), .en(O_C), .Q(EPC), .clk(CLK), .clr(RST));
  Register #(.width(1), .trigger("rising"), .Select("low")) \u_中断使能寄存器  (
    .D(O_C), .en(or_2_out), .Q(IE), .clk(CLK), .clr(RST));
  or or_4 (IR3_t, IR3, IRC);
  \单周期硬布线控制器  \u_单周期硬布线控制器_1  (
    .Func(IR[5:0]), .OP(IR[31:26]), .ALU_OP(\单周期硬布线控制器_1_alu_op ), .MemToReg(MemToReg), .MemWrite(MemWrite),
    .ALU_SRC(\单周期硬布线控制器_1_alu_src ), .RegWrite(RegWrite), .SysCALL(Syscall), .SignedExt(SignedExt),
    .RegDst(\单周期硬布线控制器_1_regdst ), .JR(JR), .JMP(JMP), .Beq(\单周期硬布线控制器_1_beq ), .JAL(JAL),
    .Bne(\单周期硬布线控制器_1_bne ));
  Multiplexer #(.select(1), .width(5), .disabled("Z"), .enable("false")) multiplexer_7 (
    .in0(IR[25:21]), .in1(5'b00100), .out(multiplexer_7_out), .sel(Syscall));
  assign bit_extender_1_out = {{16{1'b0}}, IR[15:0]};  // Bit_Extender bit_extender_1
  assign bit_extender_2_out = {{16{IR[15]}}, IR[15:0]};  // Bit_Extender bit_extender_2
  Multiplexer #(.select(1), .width(32), .disabled("Z"), .enable("false")) multiplexer_8 (
    .in0({mips_alu_1_result, bytechoose}), .in1(ram_1_data), .out(multiplexer_8_out), .sel(MemToReg));
  Multiplexer #(.select(2), .width(32), .disabled("Z"), .enable("false")) multiplexer_9 (
    .in1(32'h30ac), .in2(32'h3150), .in3(32'h31f4), .out(\中断程序入口地址 ), .sel(priority_encoder_1_out));  // open: in0
  not not_4 (not_4_out, IE);
  // Probe on RDin
  Multiplexer #(.select(1), .width(5), .disabled("Z"), .enable("true")) multiplexer_10 (
    .in0(IR[20:16]), .in1(IR[15:11]), .out(multiplexer_10_out), .sel(\单周期硬布线控制器_1_regdst ));  // open: en
  Multiplexer #(.select(1), .width(32), .disabled("Z"), .enable("false")) multiplexer_11 (
    .in0(bit_extender_1_out), .in1(bit_extender_2_out), .out(multiplexer_11_out), .sel(SignedExt));
  Register #(.width(2), .trigger("rising"), .Select("low")) register_2 (
    .D(priority_encoder_1_out), .en(O_C), .Q(register_2_q), .clk(CLK), .clr(RST));
  and and_4 (O_C, not_4_out, \开中断 );
  Multiplexer #(.select(1), .width(5), .disabled("Z"), .enable("false")) multiplexer_12 (
    .in0(IR[20:16]), .in1(5'b00010), .out(multiplexer_12_out), .sel(Syscall));
  Multiplexer #(.select(1), .width(5), .disabled("Z"), .enable("false")) multiplexer_13 (
    .in0(multiplexer_10_out), .in1({5{1'b1}}), .out(multiplexer_13_out), .sel(JAL));
  Counter #(.width(16), .max('hffff), .ongoal("wrap"), .trigger("rising"), .behavior("old")) counter_2 (
    .count(JMP), .Q(\无条件分支数 ), .clk(CLK), .clr(RST));  // open: load, D, carry, preset
  Decoder #(.select(2), .tristate("false"), .disabled("Z"), .enable("false")) decoder_1 (
    .out1(decoder_1_out1), .out2(decoder_1_out2), .out3(decoder_1_out3), .sel(register_2_q));  // open: out0
  MIPS_Regifile mips_regifile_1 (
    .Din(RDin), .Clk(CLK), .R1(R1), .R2(R2), .WE(RegWrite), .W_num(multiplexer_13_out),
    .R1_num(multiplexer_12_out), .R2_num(multiplexer_7_out));
  or or_5 (\是否跳转 , and_5_out, and_9_out, and_10_out);
  and and_5 (and_5_out, \单周期硬布线控制器_1_beq , mips_alu_1_equal);
  Shifter #(.width(32), .shift("ll")) shifter_1 (.in(bit_extender_2_out), .\dist (5'b00010), .out(shifter_1_out));
  and and_6 (RET1, decoder_1_out1, ERET);
  and and_7 (RET2, decoder_1_out2, ERET);
  and and_8 (RET3, decoder_1_out3, ERET);
  and and_9 (and_9_out, not_5_out, \单周期硬布线控制器_1_bne );
  not not_5 (not_5_out, mips_alu_1_equal);
  Multiplexer #(.select(1), .width(32), .disabled("Z"), .enable("false")) multiplexer_14 (
    .in0(R1), .in1(multiplexer_11_out), .out(multiplexer_14_out), .sel(\单周期硬布线控制器_1_alu_src ));
  MIPS_ALU mips_alu_1 (
    .X(R2), .Y(multiplexer_14_out), .AluOP(\单周期硬布线控制器_1_alu_op ), .Equal(mips_alu_1_equal),
    .Result({mips_alu_1_result, bytechoose}), .shamt(IR[10:6]));  // open: Result_2
  Counter #(.width(16), .max('hffff), .ongoal("wrap"), .trigger("rising"), .behavior("old")) counter_3 (
    .count(\是否跳转 ), .Q(\条件分支成功数 ), .clk(CLK), .clr(RST));  // open: load, D, carry, preset
  and and_10 (and_10_out, BGTZ, comparator_3_gt);
  assign bit_extender_3_out = {{3{1'b0}}, bytechoose};  // Bit_Extender bit_extender_3
  Demultiplexer #(.select(2), .width(8), .tristate("false"), .disabled("Z"), .enable("false")) demultiplexer_1 (
    .out0(demultiplexer_1_out0), .out1(demultiplexer_1_out1), .out2(demultiplexer_1_out2),
    .out3(demultiplexer_1_out3), .in({8{1'b1}}), .sel(bytechoose));
  assign and_11_out = R1 & 32'hff;  // AND_Gate and_11, 32 bits wide
  Multiplier #(.width(5)) multiplier_1 (
    .a(5'b01000), .b(bit_extender_3_out), .out(multiplier_1_out));  // open: cin, cout
  Comparator #(.width(32), .mode("twosComplement")) comparator_3 (
    .a(R2), .b({32{1'b0}}), .gt(comparator_3_gt));  // open: eq, lt
  Shifter #(.width(32), .shift("ll")) shifter_2 (.in(and_11_out), .\dist (multiplier_1_out), .out(shifter_2_out));
  assign and_12_out = ram_1_data & not_6_out;  // AND_Gate and_12, 32 bits wide
  assign not_6_out = ~{demultiplexer_1_out3, demultiplexer_1_out2, demultiplexer_1_out1, demultiplexer_1_out0};  // NOT_Gate not_6, 32 bits wide
  Multiplexer #(.select(1), .width(32), .disabled("Z"), .enable("false")) multiplexer_15 (
    .in0(R1), .in1(or_6_out), .out(MDin), .sel(SB));
  assign or_6_out = shifter_2_out | and_12_out;  // OR_Gate or_6, 32 bits wide
  RAM #(.addrWidth(10), .dataWidth(32), .bus("separate"), .Select("high")) ram_1 (
    .addr(mips_alu_1_result[11:2]), .din(MDin), .data(ram_1_data), .str(MemWrite), .clk(CLK), .ld(1'b1),
    .clr(RST));  // open: sel

  // Other names for the same wires on the sheet: Func[5:0] = IR[5:0]; OP[5:0] = IR[31:26]; 指示灯1 = W1; 指示灯2 = W2;
  //   指示灯3 = W3

  // Notes on the sheet:
  //   J、JAL
  //   JR
  //   中断源
  //   中断等待指示
  //   总复位信号应将除ROM以外所有存储组件全部清零
  //   中断返回
  //   数码管输出
  //   beq和bne跳转的话，在pc+1的基础上加上偏移量
  //   中断请求信号
  //   数码管输出应该用寄存器锁存，否则显示数据只能一闪而过
  //   指令存储器
  //   contents of rom_1 (hex, n*v repeats v):
  //   201d07d0 20100001 109fc0 139fc3 8021 2012000c 24160008 26100001 3210000f 20080008 20090001 139900
  //   2709825 132020 20020022 c 1094022 1500fff9 22100001 2018000f 2188024 108700 20080008 20090001 139902
  //   2709825 132021 20020022 c 1094022 1500fff9 108702 2c9b022 12c00001 8000c07 4020 1084027 84400
  //   3508ffff 82021 20020022 c 8000c01 afa20000 23bd0004 afa40000 23bd0004 afb00000 23bd0004 afb30000
  //   23bd0004 afb40000 23bd0004 afb50000 23bd0004 afb60000 23bd0004 20160001 20140003 20150001 168020
  //   108100 2149825 132020 20020022 c 1600fffa 295a022 1680fff7 23bdfffc 8fb60000 23bdfffc 8fb50000
  //   23bdfffc 8fb40000 23bdfffc 8fb30000 23bdfffc 8fb00000 23bdfffc 8fa40000 23bdfffc 8fa20000 42000018
  //   afa20000 23bd0004 afa40000 23bd0004 afb00000 23bd0004 afb30000 23bd0004 afb40000 23bd0004 afb50000
  //   23bd0004 afb60000 23bd0004 20160002 20140003 20150001 168020 108100 2149825 132020 20020022 c
  //   1600fffa 295a022 1680fff7 23bdfffc 8fb60000 23bdfffc 8fb50000 23bdfffc 8fb40000 23bdfffc 8fb30000
  //   23bdfffc 8fb00000 23bdfffc 8fa40000 23bdfffc 8fa20000 42000018 afa20000 23bd0004 afa40000 23bd0004
  //   afb00000 23bd0004 afb30000 23bd0004 afb40000 23bd0004 afb50000 23bd0004 afb60000 23bd0004 20160003
  //   20140003 20150001 168020 108100 2149825 132020 20020022 c 1600fffa 295a022 1680fff7 23bdfffc
  //   8fb60000 23bdfffc 8fb50000 23bdfffc 8fb40000 23bdfffc 8fb30000 23bdfffc 8fb00000 23bdfffc 8fa40000
  //   23bdfffc 8fa20000 42000018
  //   OP
  //   Func
  //   rs
  //   指令字
  //   rt
  //   rd
  //   JMP
  //   JR
  //   OP
  //   Func
  //   开关中断
  //   Beq
  //   Bne
  //   MemToReg
  //   MemWrite
  //   AluOP
  //   AluSrcB
  //   RegWrite
  //   JAL
  //   RegDst
  //   Syscall
  //   ANDI、ORI
  //   ADDI、ADDIU、SLTI、LW、SW
  //   为方便自动评测，需要输出PC，IR，寄存器堆写如数据RDin
  //   RAM写使能MemWrite、RAM写入数据MDin等信号
  //   sw指令读入数据存储器中
endmodule

module \单周期MIPS_多级中断  (
  input  IR1,
  input  IR2,
  input  IR3,
  output RegWrite,
  output MemWrite,
  output [31:0] PC,
  output [31:0] IR,
  output [31:0] RDin,
  output [31:0] MDin,
  output [31:0] LedData
);

  wire add, and_1_out, and_2_out, and_3_out, and_4_out, and_8_out, and_9_out, and_10_out, and_11_out, BGTZ,
       CLK, clock_1_out, clock_2_out, comparator_1_eq, comparator_1_lt, comparator_5_eq, comparator_6_gt,
       comparator_7_eq, comparator_8_eq, comparator_9_eq, comparator_10_eq, comparator_11_eq, d_ff_1_q,
       demultiplexer_1_out1, demultiplexer_1_out2, demultiplexer_1_out3, demultiplexer_2_out1,
       demultiplexer_2_out2, demultiplexer_2_out3, demultiplexer_3_out1, demultiplexer_3_out2,
       demultiplexer_3_out3, display, ERET, Go, IE, IR1_t, IR2_t, IR3_t, IRA, IRB, IRC, JAL, JMP, JR,
       MemToReg, MFC0, mips_alu_1_equal, MTC0, nand_1_out, not_2_out, not_3_out, not_4_out, not_5_out, O_C,
       or_2_out, or_6_out, or_8_out, or_9_out, pause, priority_encoder_1_en_out, RST, SB, SignedExt, SUBU,
       Syscall, W1, W2, W3, XOR, \中断到来 , \单周期硬布线控制器_1_alu_src , \单周期硬布线控制器_1_beq , \单周期硬布线控制器_1_bne ,
       \单周期硬布线控制器_1_regdst , \开中断 , \是否跳转 ;
  wire [1:0] bytechoose, multiplexer_17_out, multiplexer_18_out, register_3_q, register_4_q, register_5_q,
       \上一个中断 , \执行中的中断 ;
  wire [2:0] multiplexer_6_out;
  wire [3:0] \单周期硬布线控制器_1_alu_op ;
  wire [4:0] bit_extender_3_out, multiplexer_10_out, multiplexer_12_out, multiplexer_14_out,
       multiplexer_15_out, multiplier_1_out;
  wire [7:0] demultiplexer_4_out0, demultiplexer_4_out1, demultiplexer_4_out2, demultiplexer_4_out3;
  wire [12:0] CNT_num;
  wire [15:0] \总周期数 , \无条件分支数 , \条件分支成功数 ;
  wire [27:0] adder_1_out_2;
  wire [31:0] adder_2_out, and_12_out, and_13_out, bit_extender_1_out, bit_extender_2_out, EPC, EPC_2_q,
       EPC_3_q, EPC_q, multiplexer_1_out, multiplexer_2_out, multiplexer_4_out, multiplexer_5_out,
       multiplexer_11_out, multiplexer_13_out, multiplexer_16_out, not_6_out, or_7_out, PC_4, R1, R2,
       ram_1_data, shifter_1_out, shifter_2_out, \中断程序入口地址 ;
  wire [31:2] mips_alu_1_result;
  wire [31:28] adder_1_out;

  D_Flip_Flop #(.trigger("high"), .Pre_Clr_Positions("LEGACY"), .NegatePresetClear("false"), .enable("true"), .NewFFLayout("false")) d_ff_1 (.Q(d_ff_1_q));  // open: clk, D, Qn, preset, en, reset
  // Probe on 13'hce
  Comparator #(.width(13), .mode("twosComplement")) comparator_1 (
    .a(CNT_num), .b(13'hce), .eq(comparator_1_eq), .lt(comparator_1_lt));  // open: gt
  Clock #(.highDuration(1), .lowDuration(1)) clock_1 (.out(clock_1_out));
  nand nand_1 (nand_1_out, d_ff_1_q, comparator_1_eq);
  Counter #(.width(13), .max('h1fff), .ongoal("stay"), .trigger("rising"), .behavior("old")) counter_1 (
    .count(comparator_1_lt), .Q(CNT_num), .clk(clock_1_out));  // open: load, D, carry, clr, preset
  Demultiplexer #(.select(2), .width(1), .tristate("false"), .disabled("Z"), .enable("false")) demultiplexer_1 (
    .out1(demultiplexer_1_out1), .out2(demultiplexer_1_out2), .out3(demultiplexer_1_out3), .in(\中断到来 ),
    .sel(\执行中的中断 ));  // open: out0
  Clock #(.highDuration(1), .lowDuration(1)) clock_2 (.out(clock_2_out));
  Button _1 ();  // open: out
  Button _2 ();  // open: out
  Button _3 ();  // open: out
  Multiplexer #(.select(1), .width(32), .disabled("Z"), .enable("false")) multiplexer_1 (
    .in0({adder_1_out, IR[25:0], 2'b00}), .in1(R2), .out(multiplexer_1_out), .sel(JR));
  Multiplexer #(.select(1), .width(32), .disabled("Z"), .enable("false")) multiplexer_2 (
    .in0({adder_1_out, adder_1_out_2}), .in1(adder_2_out), .out(multiplexer_2_out), .sel(\是否跳转 ));
  Comparator #(.width(11), .mode("twosComplement")) comparator_2 (
    .a(IR[31:21]), .b(11'h200), .eq(MFC0));  // open: gt, lt
  Button \u_继续运行  (.out(Go));
  LED #(.active("true")) led_1 (.in(W1));
  LED #(.active("true")) led_2 (.in(W2));
  LED #(.active("true")) led_3 (.in(W3));
  assign CLK = nand_1_out ? clock_1_out : 1'bz;  // Controlled_Buffer controlled_buffer_1
  Pull_Resistor #(.pull(1)) pull_resistor_1 (.node(CLK));
  Multiplexer #(.select(1), .width(32), .disabled("Z"), .enable("false")) multiplexer_3 (
    .in0(multiplexer_2_out), .in1(multiplexer_1_out), .out(PC_4), .sel(JMP));
  Hex_Digit_Display hex_digit_display_1 (.value(LedData[31:28]));  // open: dp
  Counter #(.width(16), .max('hffff), .ongoal("wrap"), .trigger("rising"), .behavior("old")) counter_2 (
    .count(add), .Q(\总周期数 ), .clk(CLK), .clr(RST));  // open: load, D, carry, preset
  Multiplexer #(.select(1), .width(32), .disabled("Z"), .enable("false")) multiplexer_4 (
    .in0(PC_4), .in1(\中断程序入口地址 ), .out(multiplexer_4_out), .sel(\中断到来 ));
  Register #(.width(32), .trigger("rising"), .Select("low")) u_EPC (
    .D(PC_4), .en(demultiplexer_1_out1), .Q(EPC_q), .clk(CLK));  // open: clr
  Register #(.width(32), .trigger("rising"), .Select("low")) EPC_2 (
    .D(PC_4), .en(demultiplexer_1_out2), .Q(EPC_2_q), .clk(CLK));  // open: clr
  Register #(.width(32), .trigger("rising"), .Select("low")) EPC_3 (
    .D(PC_4), .en(demultiplexer_1_out3), .Q(EPC_3_q), .clk(CLK));  // open: clr
  Hex_Digit_Display hex_digit_display_2 (.value(LedData[27:24]));  // open: dp
  Hex_Digit_Display hex_digit_display_3 (.value(LedData[23:20]));  // open: dp
  Multiplexer #(.select(1), .width(32), .disabled("Z"), .enable("false")) multiplexer_5 (
    .in0(multiplexer_4_out), .in1(EPC), .out(multiplexer_5_out), .sel(ERET));
  D_Flip_Flop #(.trigger("rising"), .Pre_Clr_Positions("LEGACY"), .NegatePresetClear("false"), .enable("true"), .NewFFLayout("false")) d_ff_2 (
    .clk(CLK), .D(1'b0), .Q(W1), .preset(IR1_t), .en(demultiplexer_2_out1));  // open: Qn, reset
  D_Flip_Flop #(.trigger("rising"), .Pre_Clr_Positions("LEGACY"), .NegatePresetClear("false"), .enable("true"), .NewFFLayout("false")) d_ff_3 (
    .clk(CLK), .D(1'b0), .Q(W2), .preset(IR2_t), .en(demultiplexer_2_out2));  // open: Qn, reset
  D_Flip_Flop #(.trigger("rising"), .Pre_Clr_Positions("LEGACY"), .NegatePresetClear("false"), .enable("true"), .NewFFLayout("false")) d_ff_4 (
    .clk(CLK), .D(1'b0), .Q(W3), .preset(IR3_t), .en(demultiplexer_2_out3));  // open: Qn, reset
  Hex_Digit_Display hex_digit_display_4 (.value(LedData[15:12]));  // open: dp
  Hex_Digit_Display hex_digit_display_5 (.value(LedData[19:16]));  // open: dp
  not not_1 (add, and_1_out);
  and and_1 (and_1_out, not_2_out, pause);
  not not_2 (not_2_out, Go);
  Register #(.width(32), .trigger("rising"), .Select("low")) u_PC (
    .D(multiplexer_5_out), .en(add), .Q(PC), .clk(CLK), .clr(RST));
  Comparator #(.width(11), .mode("twosComplement")) comparator_3 (
    .a(IR[31:21]), .b(11'h204), .eq(MTC0));  // open: gt, lt
  Comparator #(.width(32), .mode("twosComplement")) comparator_4 (.a(IR), .b(32'h42000018), .eq(ERET));  // open: gt, lt
  Multiplexer #(.select(2), .width(3), .disabled("Z"), .enable("false")) multiplexer_6 (
    .in0(3'b111), .in1(3'b110), .in2(3'b100), .in3(3'b000), .out(multiplexer_6_out), .sel(\上一个中断 ));
  Hex_Digit_Display hex_digit_display_6 (.value(LedData[11:8]));  // open: dp
  Hex_Digit_Display hex_digit_display_7 (.value(LedData[7:4]));  // open: dp
  // Mips_Probe mips_probe_1: pin names not known; wires that end beside it: IR
  Adder #(.width(32)) adder_1 (.a(PC), .b(32'h4), .out({adder_1_out, adder_1_out_2}));  // open: cin, cout
  Adder #(.width(32)) adder_2 (
    .a({adder_1_out, adder_1_out_2}), .b(shifter_1_out), .out(adder_2_out));  // open: cin, cout
  Demultiplexer #(.select(2), .width(1), .tristate("false"), .disabled("Z"), .enable("false")) demultiplexer_2 (
    .out1(demultiplexer_2_out1), .out2(demultiplexer_2_out2), .out3(demultiplexer_2_out3), .in(ERET),
    .sel(\上一个中断 ));  // open: out0
  Multiplexer #(.select(2), .width(32), .disabled("Z"), .enable("false")) multiplexer_7 (
    .in0(PC_4), .in1(EPC_q), .in2(EPC_2_q), .in3(EPC_3_q), .out(EPC), .sel(\上一个中断 ));
  Hex_Digit_Display hex_digit_display_8 (.value(LedData[3:0]));  // open: dp
  // Probe on \总周期数 
  assign \执行中的中断  = priority_encoder_1_en_out ? 2'b00 : 2'bz;  // Controlled_Buffer controlled_buffer_2
  and and_2 (and_2_out, W1, multiplexer_6_out[0]);
  // Probe on PC
  Comparator #(.width(32), .mode("twosComplement")) comparator_5 (
    .a(R1), .b(32'h22), .eq(comparator_5_eq));  // open: gt, lt
  ROM #(.addrWidth(10), .dataWidth(32), .Select("high")) rom_1 (.addr(PC[11:2]), .data(IR));
  and and_3 (and_3_out, multiplexer_6_out[1], W2);
  and and_4 (and_4_out, multiplexer_6_out[2], W3);
  or or_1 (IR1_t, IR1, IRA);
  and and_5 (pause, Syscall, not_3_out);
  not not_3 (not_3_out, comparator_5_eq);
  and and_6 (display, comparator_5_eq, Syscall);
  Register #(.width(32), .trigger("rising"), .Select("low")) register_1 (
    .D(R2), .en(display), .Q(LedData), .clk(CLK), .clr(RST));
  Priority_Encoder #(.select(2), .disabled("Z")) priority_encoder_1 (
    .in0(1'b0), .in1(and_2_out), .in2(and_3_out), .in3(and_4_out), .out(\执行中的中断 ), .gs(\开中断 ),
    .en_out(priority_encoder_1_en_out), .en_in(1'b1));
  // Probe on IR
  ps1 ps1_1 (
    .OP0(IR[26]), .OP1(IR[27]), .OP2(IR[28]), .OP3(IR[29]), .OP4(IR[30]), .OP5(IR[31]), .F0(IR[0]),
    .F1(IR[1]), .F2(IR[2]), .F3(IR[3]), .F4(IR[4]), .F5(IR[5]), .bgtz(BGTZ), .XOR(XOR), .SB(SB), .SUBU(SUBU));
  or or_2 (or_2_out, MFC0, MTC0, ERET);
  or or_3 (IR2_t, IR2, IRB);
  Multiplexer #(.select(1), .width(32), .disabled("Z"), .enable("false")) multiplexer_8 (
    .in0(multiplexer_11_out), .in1({adder_1_out, adder_1_out_2}), .out(RDin), .sel(JAL));
  Multiplexer #(.select(2), .width(32), .disabled("Z"), .enable("false")) multiplexer_9 (
    .in1(32'h30ac), .in2(32'h3158), .in3(32'h3204), .out(\中断程序入口地址 ), .sel(\执行中的中断 ));  // open: in0
  Register #(.width(1), .trigger("rising"), .Select("low")) \u_中断使能寄存器  (
    .D(1'b0), .en(or_2_out), .Q(IE), .clk(CLK), .clr(RST), .preset(\中断到来 ));  // open: cs
  or or_4 (IR3_t, IR3, IRC);
  \单周期硬布线控制器  \u_单周期硬布线控制器_1  (
    .Func(IR[5:0]), .OP(IR[31:26]), .ALU_OP(\单周期硬布线控制器_1_alu_op ), .MemToReg(MemToReg), .MemWrite(MemWrite),
    .ALU_SRC(\单周期硬布线控制器_1_alu_src ), .RegWrite(RegWrite), .SysCALL(Syscall), .SignedExt(SignedExt),
    .RegDst(\单周期硬布线控制器_1_regdst ), .JR(JR), .JMP(JMP), .Beq(\单周期硬布线控制器_1_beq ), .JAL(JAL),
    .Bne(\单周期硬布线控制器_1_bne ));
  Multiplexer #(.select(1), .width(5), .disabled("Z"), .enable("false")) multiplexer_10 (
    .in0(IR[25:21]), .in1(5'b00100), .out(multiplexer_10_out), .sel(Syscall));
  assign bit_extender_1_out = {{16{1'b0}}, IR[15:0]};  // Bit_Extender bit_extender_1
  assign bit_extender_2_out = {{16{IR[15]}}, IR[15:0]};  // Bit_Extender bit_extender_2
  Multiplexer #(.select(1), .width(32), .disabled("Z"), .enable("false")) multiplexer_11 (
    .in0({mips_alu_1_result, bytechoose}), .in1(ram_1_data), .out(multiplexer_11_out), .sel(MemToReg));
  // Probe on RDin
  Multiplexer #(.select(1), .width(5), .disabled("Z"), .enable("true")) multiplexer_12 (
    .in0(IR[20:16]), .in1(IR[15:11]), .out(multiplexer_12_out), .sel(\单周期硬布线控制器_1_regdst ));  // open: en
  Multiplexer #(.select(1), .width(32), .disabled("Z"), .enable("false")) multiplexer_13 (
    .in0(bit_extender_1_out), .in1(bit_extender_2_out), .out(multiplexer_13_out), .sel(SignedExt));
  Demultiplexer #(.select(2), .width(1), .tristate("false"), .disabled("Z"), .enable("false")) demultiplexer_3 (
    .out1(demultiplexer_3_out1), .out2(demultiplexer_3_out2), .out3(demultiplexer_3_out3), .in(\中断到来 ),
    .sel(\执行中的中断 ));  // open: out0
  not not_4 (not_4_out, IE);
  and and_7 (O_C, not_4_out, \开中断 );
  Multiplexer #(.select(1), .width(5), .disabled("Z"), .enable("false")) multiplexer_14 (
    .in0(IR[20:16]), .in1(5'b00010), .out(multiplexer_14_out), .sel(Syscall));
  Multiplexer #(.select(1), .width(5), .disabled("Z"), .enable("false")) multiplexer_15 (
    .in0(multiplexer_12_out), .in1({5{1'b1}}), .out(multiplexer_15_out), .sel(JAL));
  Counter #(.width(16), .max('hffff), .ongoal("wrap"), .trigger("rising"), .behavior("old")) counter_3 (
    .count(JMP), .Q(\无条件分支数 ), .clk(CLK), .clr(RST));  // open: load, D, carry, preset
  and and_8 (and_8_out, O_C, add);
  Register #(.width(1), .trigger("falling"), .Select("low")) register_2 (
    .D(and_8_out), .Q(\中断到来 ), .clk(CLK), .clr(RST));  // open: en
  MIPS_Regifile mips_regifile_1 (
    .Din(RDin), .Clk(CLK), .R1(R1), .R2(R2), .WE(RegWrite), .W_num(multiplexer_15_out),
    .R1_num(multiplexer_14_out), .R2_num(multiplexer_10_out));
  Register #(.width(2), .trigger("rising"), .Select("low")) register_3 (
    .D(\上一个中断 ), .en(demultiplexer_3_out1), .Q(register_3_q), .clk(CLK), .clr(RST));
  Register #(.width(2), .trigger("rising"), .Select("low")) register_4 (
    .D(\上一个中断 ), .en(demultiplexer_3_out2), .Q(register_4_q), .clk(CLK), .clr(RST));
  Register #(.width(2), .trigger("rising"), .Select("low")) register_5 (
    .D(\上一个中断 ), .en(demultiplexer_3_out3), .Q(register_5_q), .clk(CLK), .clr(RST));
  or or_5 (\是否跳转 , and_9_out, and_10_out, and_11_out);
  and and_9 (and_9_out, \单周期硬布线控制器_1_beq , mips_alu_1_equal);
  Shifter #(.width(32), .shift("ll")) shifter_1 (.in(bit_extender_2_out), .\dist (5'b00010), .out(shifter_1_out));
  and and_10 (and_10_out, not_5_out, \单周期硬布线控制器_1_bne );
  not not_5 (not_5_out, mips_alu_1_equal);
  Multiplexer #(.select(1), .width(32), .disabled("Z"), .enable("false")) multiplexer_16 (
    .in0(R1), .in1(multiplexer_13_out), .out(multiplexer_16_out), .sel(\单周期硬布线控制器_1_alu_src ));
  MIPS_ALU mips_alu_1 (
    .X(R2), .Y(multiplexer_16_out), .AluOP(\单周期硬布线控制器_1_alu_op ), .Equal(mips_alu_1_equal),
    .Result({mips_alu_1_result, bytechoose}), .shamt(IR[10:6]));  // open: Result_2
  Multiplexer #(.select(2), .width(2), .disabled("Z"), .enable("false")) multiplexer_17 (
    .in1(register_3_q), .in2(register_4_q), .in3(register_5_q), .out(multiplexer_17_out), .sel(\上一个中断 ));  // open: in0
  Counter #(.width(16), .max('hffff), .ongoal("wrap"), .trigger("rising"), .behavior("old")) counter_4 (
    .count(\是否跳转 ), .Q(\条件分支成功数 ), .clk(CLK), .clr(RST));  // open: load, D, carry, preset
  and and_11 (and_11_out, BGTZ, comparator_6_gt);
  assign bit_extender_3_out = {{3{1'b0}}, bytechoose};  // Bit_Extender bit_extender_3
  Demultiplexer #(.select(2), .width(8), .tristate("false"), .disabled("Z"), .enable("false")) demultiplexer_4 (
    .out0(demultiplexer_4_out0), .out1(demultiplexer_4_out1), .out2(demultiplexer_4_out2),
    .out3(demultiplexer_4_out3), .in({8{1'b1}}), .sel(bytechoose));
  Multiplexer #(.select(1), .width(2), .disabled("Z"), .enable("false")) multiplexer_18 (
    .in0(\执行中的中断 ), .in1(multiplexer_17_out), .out(multiplexer_18_out), .sel(ERET));
  assign and_12_out = R1 & 32'hff;  // AND_Gate and_12, 32 bits wide
  Multiplier #(.width(5)) multiplier_1 (
    .a(5'b01000), .b(bit_extender_3_out), .out(multiplier_1_out));  // open: cin, cout
  Comparator #(.width(32), .mode("twosComplement")) comparator_6 (
    .a(R2), .b({32{1'b0}}), .gt(comparator_6_gt));  // open: eq, lt
  Shifter #(.width(32), .shift("ll")) shifter_2 (.in(and_12_out), .\dist (multiplier_1_out), .out(shifter_2_out));
  assign and_13_out = ram_1_data & not_6_out;  // AND_Gate and_13, 32 bits wide
  assign not_6_out = ~{demultiplexer_4_out3, demultiplexer_4_out2, demultiplexer_4_out1, demultiplexer_4_out0};  // NOT_Gate not_6, 32 bits wide
  or or_6 (or_6_out, ERET, \中断到来 );
  Register #(.width(2), .trigger("rising"), .Select("low")) register_6 (
    .D(multiplexer_18_out), .en(or_6_out), .Q(\上一个中断 ), .clk(CLK));  // open: clr
  Multiplexer #(.select(1), .width(32), .disabled("Z"), .enable("false")) multiplexer_19 (
    .in0(R1), .in1(or_7_out), .out(MDin), .sel(SB));
  assign or_7_out = shifter_2_out | and_13_out;  // OR_Gate or_7, 32 bits wide
  RAM #(.addrWidth(10), .dataWidth(32), .bus("separate"), .Select("high")) ram_1 (
    .addr(mips_alu_1_result[11:2]), .din(MDin), .data(ram_1_data), .str(MemWrite), .clk(CLK), .ld(1'b1),
    .clr(RST));  // open: sel
  Comparator #(.width(16), .mode("twosComplement")) comparator_7 (
    .a(16'h258), .b(\总周期数 ), .eq(comparator_7_eq));  // open: gt, lt
  Comparator #(.width(16), .mode("twosComplement")) comparator_8 (
    .a(\总周期数 ), .b(16'h1), .eq(comparator_8_eq));  // open: gt, lt
  Comparator #(.width(16), .mode("twosComplement")) comparator_9 (
    .a(\总周期数 ), .b(16'h4), .eq(comparator_9_eq));  // open: gt, lt
  Comparator #(.width(16), .mode("twosComplement")) comparator_10 (
    .a(\总周期数 ), .b(16'h7), .eq(comparator_10_eq));  // open: gt, lt
  or or_8 (or_8_out, comparator_10_eq, comparator_11_eq);
  Comparator #(.width(16), .mode("twosComplement")) comparator_11 (
    .a(\总周期数 ), .b(16'h241), .eq(comparator_11_eq));  // open: gt, lt
  or or_9 (or_9_out, comparator_7_eq, comparator_8_eq);
  Pull_Resistor #(.pull(0)) pull_resistor_2 (.node(IRA));
  assign IRA = or_9_out ? ~CLK : 1'bz;  // Controlled_Inverter controlled_inverter_1
  Pull_Resistor #(.pull(0)) pull_resistor_3 (.node(IRB));
  assign IRB = comparator_9_eq ? ~CLK : 1'bz;  // Controlled_Inverter controlled_inverter_2
  Pull_Resistor #(.pull(0)) pull_resistor_4 (.node(IRC));
  assign IRC = or_8_out ? ~CLK : 1'bz;  // Controlled_Inverter controlled_inverter_3

  // Other names for the same wires on the sheet: Func[5:0] = IR[5:0]; OP[5:0] = IR[31:26]; 中断位与1 = W1; 中断位与2 = W2;
  //   中断位与3 = W3

  // Notes on the sheet:
  //   控制位
  //   暂停节拍，不能为0
  //   戳工具置1进入计数暂停模式，ctrl+k时钟自动运行到对应节拍暂停
  //   ctrl+k关闭时钟连续运行，将控制位置零，进入单步调试模式调试
  //   用这个时钟源需要去掉电路中的其他时钟源
  //   J、JAL
  //   JR
  //   中断源
  //   可计数暂停的时钟源
  //   中断等待指示
  //   总复位信号应将除ROM以外所有存储组件全部清零
  //   中断返回
  //   当ERET到来时选择对应的中断，将其设置为0
  //   数码管输出
  //   beq和bne跳转的话，在pc+1的基础上加上偏移量
  //   中断屏蔽字
  //   000表示优先级最高，111最低，110表示只有2、3中断可打断，100表示只有3号中断可以打断
  //   数码管输出应该用寄存器锁存，否则显示数据只能一闪而过
  //   指令存储器
  //   contents of rom_1 (hex, n*v repeats v):
  //   201d07d0 20100001 109fc0 139fc3 8021 2012000c 24160008 26100001 3210000f 20080008 20090001 139900
  //   2709825 132020 20020022 c 1094022 1500fff9 22100001 2018000f 2188024 108700 20080008 20090001 139902
  //   2709825 132021 20020022 c 1094022 1500fff9 108702 2c9b022 12c00001 8000c07 4020 1084027 84400
  //   3508ffff 82021 20020022 c 8000c01 afa20000 23bd0004 afa40000 23bd0004 afb00000 23bd0004 afb30000
  //   23bd0004 afb40000 23bd0004 afb50000 23bd0004 afb60000 23bd0004 40000000 20160001 20140003 20150001
  //   168020 108100 2149825 132020 20020022 c 1600fffa 295a022 1680fff7 40800000 23bdfffc 8fb60000
  //   23bdfffc 8fb50000 23bdfffc 8fb40000 23bdfffc 8fb30000 23bdfffc 8fb00000 23bdfffc 8fa40000 23bdfffc
  //   8fa20000 42000018 afa20000 23bd0004 afa40000 23bd0004 afb00000 23bd0004 afb30000 23bd0004 afb40000
  //   23bd0004 afb50000 23bd0004 afb60000 23bd0004 40000000 20160002 20140003 20150001 168020 108100
  //   2149825 132020 20020022 c 1600fffa 295a022 1680fff7 40800000 23bdfffc 8fb60000 23bdfffc 8fb50000
  //   23bdfffc 8fb40000 23bdfffc 8fb30000 23bdfffc 8fb00000 23bdfffc 8fa40000 23bdfffc 8fa20000 42000018
  //   afa20000 23bd0004 afa40000 23bd0004 afb00000 23bd0004 afb30000 23bd0004 afb40000 23bd0004 afb50000
  //   23bd0004 afb60000 23bd0004 40000000 20160003 20140003 20150001 168020 108100 2149825 132020 20020022
  //   c 1600fffa 295a022 1680fff7 40800000 23bdfffc 8fb60000 23bdfffc 8fb50000 23bdfffc 8fb40000 23bdfffc
  //   8fb30000 23bdfffc 8fb00000 23bdfffc 8fa40000 23bdfffc 8fa20000 42000018
  //   OP
  //   Func
  //   rs
  //   指令字
  //   rt
  //   rd
  //   JMP
  //   JR
  //   OP
  //   Func
  //   开关中断
  //   Beq
  //   Bne
  //   MemToReg
  //   MemWrite
  //   AluOP
  //   AluSrcB
  //   RegWrite
  //   JAL
  //   RegDst
  //   Syscall
  //   ANDI、ORI
  //   ADDI、ADDIU、SLTI、LW、SW
  //   为方便自动评测，需要输出PC，IR，寄存器堆写如数据RDin
  //   RAM写使能MemWrite、RAM写入数据MDin等信号
  //   sw指令读入数据存储器中
  //   多级中断信号产生
endmodule

module \中断按键参考电路  (
  input  \同步清零信号 ,
  output \与中断屏蔽位与 
);

  wire \_1号中断_out , and_1_out, clock_1_out, d_ff_1_q, or_1_out, or_2_out;

  Clock #(.highDuration(1), .lowDuration(1)) clock_1 (.out(clock_1_out));
  Button \_1号中断  (.out(\_1号中断_out ));
  LED #(.active("true")) \_1号中断等待指示灯  (.in(or_1_out));
  or or_1 (or_1_out, \与中断屏蔽位与 , d_ff_1_q);
  D_Flip_Flop #(.trigger("rising"), .Pre_Clr_Positions("LEGACY"), .NegatePresetClear("false"), .enable("true"), .NewFFLayout("false")) d_ff_1 (
    .clk(\_1号中断_out ), .D(1'b1), .Q(d_ff_1_q), .reset(\与中断屏蔽位与 ));  // open: Qn, preset, en
  or or_2 (or_2_out, d_ff_1_q, \与中断屏蔽位与 );
  and and_1 (and_1_out, or_2_out, ~\同步清零信号 );  // AND_Gate
  D_Flip_Flop #(.trigger("rising"), .Pre_Clr_Positions("LEGACY"), .NegatePresetClear("false"), .enable("true"), .NewFFLayout("false")) IR1 (
    .clk(clock_1_out), .D(and_1_out), .Q(\与中断屏蔽位与 ));  // open: Qn, preset, en, reset

  // Notes on the sheet:
  //   中断信号采样参考电路
  //   Reset 
endmodule

module \重定向流水线单极中断  (
  output RegWrite,
  output MemWrite,
  output [31:0] IF_PC,
  output [31:0] ID_PC,
  output [31:0] EX_PC,
  output [31:0] M_PC,
  output [31:0] WB_PC,
  output [31:0] RDin,
  output [31:0] MDin,
  output [31:0] LedData
);

  wire AluSrcB, AluSrcB_EX, AluSrcB_MEM, and_1_out, and_4_out, and_9_out, and_10_out, and_11_out, Beq,
       Beq_EX, Beq_MEM, BGTZ, BGTZ_EX, Bne, Bne_EX, Bne_MEM, CLK, clock_1_out, clock_2_out, comparator_3_eq,
       comparator_3_lt, comparator_4_gt, d_ff_1_q, decoder_1_out1, decoder_1_out2, decoder_1_out3, display,
       enable_WB, enableEX, equal_22, equal_22_mem, equal_22_wb, ERET, ERET_ex, ERET_mem, ERET_WB,
       ex_mem_1_enable_ex, Go, IE, IR1, IR2, IR3, JAL, JAL_Ex, JAL_MEM, JAL_WB, JMP, JMP_EX, JR, JR_EX,
       load_use, MemToBeg, MemToBeg_ex, MemToBeg_MEM, MemToBeg_WB, MemWrite_ex, MemWriteID, mips_alu_1_equal,
       nand_1_out, not_1_out, not_2_out, not_3_out, not_4_out, not_5_out, not_6_out, O_C, or_1_out, or_2_out,
       or_3_out, or_4_out, or_5_out, or_6_out, or_7_out, or_8_out, pause, RegDst, RegDst_EX, RegDst_MEM,
       RegDst_WB, register_1_q, RegWrite_ex, RegWrite_MEM, RegWriteID, RET1, RET2, RET3, RST, SB, SB_EX,
       SB_MEM, SB_WB, SignedExt, SUBU, Syscall, Syscall_ex, Syscall_mem, Syscall_wb, W1, W2, W3, XOR,
       \中断位与1 , \中断位与2 , \中断位与3 , \开中断 , \数据相关 , \是否跳转 ;
  wire [1:0] bytechoose, forwardToR1, forwardToR1_EX, forwardToR2, forwardToR2_EX, priority_encoder_1_out,
       register_3_q;
  wire [3:0] AluOP, AluOP_EX, AluOP_MEM;
  wire [4:0] bit_extender_3_out, multiplexer_9_out, multiplexer_10_out, multiplexer_14_out,
       multiplexer_15_out, multiplexer_16_out, multiplexer_17_out, multiplier_1_out, R1_ID, R2_ID, rd_ID_EX,
       rd_ID_MEM, rd_ID_WB, rt_ID_EX, rt_ID_MEM, rt_ID_WB, shamtEX;
  wire [5:0] Func;
  wire [7:0] demultiplexer_1_out0, demultiplexer_1_out1, demultiplexer_1_out2, demultiplexer_1_out3;
  wire [12:0] CNT_num;
  wire [15:0] \LoadUse次数 , \总周期数 , \插入气泡数 , \无条件分支数 , \条件分支成功数 ;
  wire [27:0] adder_3_out;
  wire [31:0] adder_1_out, adder_2_out, and_12_out, and_13_out, Beq_Bne, bit_extender_1_out,
       bit_extender_2_out, EPC, EX_IR, ex_mem_1_r2_ex, IF_IR, IMMEX, IR_PC_MEM, IR_PC_WB, LedData_in,
       LedData_mem, MEMDATA_MEM, MEMDATA_WB, multiplexer_1_out, multiplexer_2_out, multiplexer_3_out,
       multiplexer_4_out, multiplexer_5_out, multiplexer_7_out, multiplexer_12_out, multiplexer_20_out,
       not_7_out, or_10_out, R1_ID_t, R1_USE, R1EX, R2_ID_t, R2_USE, R2EX, RESULT, RESULT_WB, shifter_1_out,
       shifter_2_out, \中断程序入口地址 ;
  wire [31:2] J_JAL, RESULT_MEM;
  wire [31:6] ID_IR;

  Multiplexer #(.select(1), .width(32), .disabled("Z"), .enable("false")) multiplexer_1 (
    .in0(adder_1_out), .in1(Beq_Bne), .out(multiplexer_1_out), .sel(\是否跳转 ));
  Multiplexer #(.select(1), .width(32), .disabled("Z"), .enable("false")) multiplexer_2 (
    .in0(multiplexer_1_out), .in1(multiplexer_3_out), .out(multiplexer_2_out), .sel(JMP_EX));
  Multiplexer #(.select(1), .width(32), .disabled("Z"), .enable("false")) multiplexer_3 (
    .in0({J_JAL, 2'b00}), .in1(R1EX), .out(multiplexer_3_out), .sel(JR_EX));
  Button \u_总复位  (.out(RST));
  Button _1 (.out(IR1));
  Button _2 (.out(IR2));
  Button _3 (.out(IR3));
  // Probe on \总周期数 
  Multiplexer #(.select(1), .width(32), .disabled("Z"), .enable("false")) multiplexer_4 (
    .in0(multiplexer_2_out), .in1(\中断程序入口地址 ), .out(multiplexer_4_out), .sel(O_C));
  Button \u_继续运行  (.out(Go));
  LED #(.active("true")) led_1 (.in(W1));
  LED #(.active("true")) led_2 (.in(W2));
  LED #(.active("true")) led_3 (.in(W3));
  // Probe on IF_PC[11:0]
  // Mips_Probe mips_probe_1: pin names not known; wires that end beside it: IF_IR
  Multiplexer #(.select(1), .width(32), .disabled("Z"), .enable("false")) multiplexer_5 (
    .in0(multiplexer_4_out), .in1(EPC), .out(multiplexer_5_out), .sel(ERET_WB));
  Hex_Digit_Display hex_digit_display_1 (.value(LedData[27:24]));  // open: dp
  Hex_Digit_Display hex_digit_display_2 (.value(LedData[31:28]));  // open: dp
  // Probe on IF_PC[11:0]
  and and_1 (and_1_out, not_2_out, not_1_out);
  Hex_Digit_Display hex_digit_display_3 (.value(LedData[19:16]));  // open: dp
  Hex_Digit_Display hex_digit_display_4 (.value(LedData[23:20]));  // open: dp
  // Probe on ID_PC[11:0]
  // Mips_Probe mips_probe_2: pin names not known; wires that end beside it: {ID_IR, Func}
  Counter #(.width(16), .max('hffff), .ongoal("wrap"), .trigger("rising"), .behavior("old")) counter_1 (
    .count(not_2_out), .Q(\总周期数 ), .clk(CLK), .clr(RST));  // open: load, D, carry, preset
  Register #(.width(32), .trigger("rising"), .Select("low")) PC (
    .D(multiplexer_5_out), .en(and_1_out), .Q(IF_PC), .clk(CLK), .clr(RST));
  Comparator #(.width(32), .mode("twosComplement")) comparator_1 (
    .a(R1_USE), .b(32'h22), .eq(equal_22));  // open: gt, lt
  Hex_Digit_Display hex_digit_display_5 (.value(LedData[11:8]));  // open: dp
  Hex_Digit_Display hex_digit_display_6 (.value(LedData[15:12]));  // open: dp
  // Probe on ID_PC[11:0]
  not not_1 (not_1_out, load_use);
  not not_2 (not_2_out, register_1_q);
  Register #(.width(1), .trigger("rising"), .Select("low")) register_1 (
    .D(Syscall_wb), .en(pause), .Q(register_1_q), .clk(CLK), .clr(or_1_out));
  not not_3 (not_3_out, equal_22_wb);
  Hex_Digit_Display hex_digit_display_7 (.value(LedData[7:4]));  // open: dp
  Hex_Digit_Display hex_digit_display_8 (.value(LedData[3:0]));  // open: dp
  Clock #(.highDuration(1), .lowDuration(1)) clock_1 (.out(clock_1_out));
  // Probe on EX_PC[11:0]
  // Probe on EX_PC[11:0]
  // Mips_Probe mips_probe_3: pin names not known; wires that end beside it: clock_1_out, EX_IR, CLK
  and and_2 (pause, Syscall_wb, not_3_out);
  and and_3 (display, equal_22, Syscall_ex);
  ROM #(.addrWidth(10), .dataWidth(32), .Select("high")) rom_1 (.addr(IF_PC[11:2]), .data(IF_IR));
  not not_4 (not_4_out, load_use);
  or or_1 (or_1_out, Go, RST);
  \中断信号采样电路  \u_中断信号采样电路_1  (.clk(CLK), .\_1号中断信号 (IR1), .\中断等待指示灯 (W1), .\与中断屏蔽位与 (\中断位与1 ), .\同步清零信号 (RET1));
  \中断信号采样电路  \u_中断信号采样电路_2  (.clk(CLK), .\_1号中断信号 (IR2), .\中断等待指示灯 (W2), .\与中断屏蔽位与 (\中断位与2 ), .\同步清零信号 (RET2));
  \中断信号采样电路  \u_中断信号采样电路_3  (.clk(CLK), .\_1号中断信号 (IR3), .\中断等待指示灯 (W3), .\与中断屏蔽位与 (\中断位与3 ), .\同步清零信号 (RET3));
  // Probe on M_PC[11:0]
  // Probe on M_PC[11:0]
  // Mips_Probe mips_probe_4: pin names not known; wires that end beside it: IR_PC_MEM
  or or_2 (or_2_out, ERET_WB, O_C);
  or or_3 (or_3_out, JMP_EX, \是否跳转 );
  and and_4 (and_4_out, not_4_out, not_2_out);
  Comparator #(.width(32), .mode("twosComplement")) comparator_2 (
    .a({ID_IR, Func}), .b(32'h42000018), .eq(ERET));  // open: gt, lt
  // Probe on \总周期数 
  // Probe on \无条件分支数 
  // Probe on \条件分支成功数 
  // Probe on \插入气泡数 
  // Probe on \LoadUse次数 
  // Probe on WB_PC[11:0]
  // Mips_Probe mips_probe_5: pin names not known; wires that end beside it: IR_PC_WB
  or or_4 (or_4_out, or_2_out, RST, or_3_out);
  ps1 ps1_1 (
    .OP0(ID_IR[26]), .OP1(ID_IR[27]), .OP2(ID_IR[28]), .OP3(ID_IR[29]), .OP4(ID_IR[30]), .OP5(ID_IR[31]),
    .F0(Func[0]), .F1(Func[1]), .F2(Func[2]), .F3(Func[3]), .F4(Func[4]), .F5(Func[5]), .bgtz(BGTZ),
    .XOR(XOR), .SB(SB), .SUBU(SUBU));
  // Probe on IF_PC[11:0]
  // Probe on WB_PC[11:0]
  IF_ID if_id_1 (
    .IRin(IF_IR), .PCin(IF_PC), .IRout({ID_IR, Func}), .PCout(ID_PC), .rst(or_4_out), .enable(and_4_out),
    .clk(CLK), .clear(RST));  // open: enable_out
  // Probe on EX_PC[11:0]
  // Probe on ID_PC[11:0]
  Adder #(.width(32)) adder_1 (.a(IF_PC), .b(32'h4), .out(adder_1_out));  // open: cin, cout
  // Probe on M_PC[11:0]
  assign bit_extender_1_out = {{16{1'b0}}, {ID_IR[15:6], Func}};  // Bit_Extender bit_extender_1
  assign bit_extender_2_out = {{16{ID_IR[15]}}, {ID_IR[15:6], Func}};  // Bit_Extender bit_extender_2
  Priority_Encoder #(.select(2), .disabled("Z")) priority_encoder_1 (
    .in0(1'b0), .in1(\中断位与1 ), .in2(\中断位与2 ), .in3(\中断位与3 ), .out(priority_encoder_1_out), .gs(\开中断 ),
    .en_in(1'b1));  // open: en_out
  // Probe on WB_PC[11:0]
  \单周期硬布线控制器  \u_单周期硬布线控制器_1  (
    .Func(Func), .OP(ID_IR[31:26]), .ALU_OP(AluOP), .MemToReg(MemToBeg), .MemWrite(MemWriteID),
    .ALU_SRC(AluSrcB), .RegWrite(RegWriteID), .SysCALL(Syscall), .SignedExt(SignedExt), .RegDst(RegDst),
    .JR(JR), .JMP(JMP), .Beq(Beq), .JAL(JAL), .Bne(Bne));
  Multiplexer #(.select(1), .width(5), .disabled("Z"), .enable("false")) multiplexer_6 (
    .in0(ID_IR[25:21]), .in1(5'b00010), .out(R1_ID), .sel(Syscall));
  Multiplexer #(.select(1), .width(32), .disabled("Z"), .enable("false")) multiplexer_7 (
    .in0(bit_extender_1_out), .in1(bit_extender_2_out), .out(multiplexer_7_out), .sel(SignedExt));
  Register #(.width(32), .trigger("rising"), .Select("low")) register_2 (
    .D(R2_USE), .en(display), .Q(LedData_in), .clk(CLK), .clr(RST));
  or or_5 (or_5_out, O_C, ERET_WB);
  Multiplexer #(.select(1), .width(5), .disabled("Z"), .enable("false")) multiplexer_8 (
    .in0(ID_IR[20:16]), .in1(5'b00100), .out(R2_ID), .sel(Syscall));
  Multiplexer #(.select(1), .width(5), .disabled("Z"), .enable("false")) multiplexer_9 (
    .in0(rt_ID_WB), .in1(rd_ID_WB), .out(multiplexer_9_out), .sel(RegDst_WB));
  Register #(.width(32), .trigger("rising"), .Select("low")) \u_异常程序计数器  (
    .D(EX_PC), .en(O_C), .Q(EPC), .clk(CLK), .clr(RST));
  Register #(.width(1), .trigger("rising"), .Select("low")) \u_中断使能寄存器  (
    .D(O_C), .en(or_5_out), .Q(IE), .clk(CLK), .clr(RST));
  Multiplexer #(.select(1), .width(5), .disabled("Z"), .enable("false")) multiplexer_10 (
    .in0(multiplexer_9_out), .in1({5{1'b1}}), .out(multiplexer_10_out), .sel(JAL_WB));
  Multiplexer #(.select(1), .width(32), .disabled("Z"), .enable("false")) multiplexer_11 (
    .in0(multiplexer_12_out), .in1(adder_2_out), .out(RDin), .sel(JAL_WB));
  Multiplexer #(.select(1), .width(32), .disabled("Z"), .enable("false")) multiplexer_12 (
    .in0(RESULT_WB), .in1(MEMDATA_WB), .out(multiplexer_12_out), .sel(MemToBeg_WB));
  Multiplexer #(.select(2), .width(32), .disabled("Z"), .enable("false")) multiplexer_13 (
    .in1(32'h30ac), .in2(32'h3150), .in3(32'h31f4), .out(\中断程序入口地址 ), .sel(priority_encoder_1_out));  // open: in0
  MIPS_Regifile mips_regifile_1 (
    .Din(RDin), .Clk(CLK), .R1(R1_ID_t), .R2(R2_ID_t), .WE(RegWrite), .W_num(multiplexer_10_out),
    .R1_num(R1_ID), .R2_num(R2_ID));
  not not_5 (not_5_out, IE);
  and and_5 (O_C, not_5_out, \开中断 );
  Register #(.width(2), .trigger("rising"), .Select("low")) register_3 (
    .D(priority_encoder_1_out), .en(O_C), .Q(register_3_q), .clk(CLK), .clr(RST));
  or or_6 (or_6_out, ERET_WB, O_C);
  or or_7 (or_7_out, JMP_EX, \是否跳转 );
  Adder #(.width(32)) adder_2 (.a(32'h4), .b(WB_PC), .out(adder_2_out));  // open: cin, cout
  Counter #(.width(16), .max('hffff), .ongoal("wrap"), .trigger("rising"), .behavior("old")) counter_2 (
    .count(JMP_EX), .Q(\无条件分支数 ), .clk(CLK), .clr(RST));  // open: load, D, carry, preset
  Counter #(.width(16), .max('hffff), .ongoal("wrap"), .trigger("rising"), .behavior("old")) counter_3 (
    .count(load_use), .Q(\插入气泡数 ), .clk(CLK), .clr(RST));  // open: load, D, carry, preset
  Decoder #(.select(2), .tristate("false"), .disabled("Z"), .enable("false")) decoder_1 (
    .out1(decoder_1_out1), .out2(decoder_1_out2), .out3(decoder_1_out3), .sel(register_3_q));  // open: out0
  or or_8 (or_8_out, or_6_out, or_7_out, RST, load_use);
  ID_EX id_ex_1 (
    .J_JAL_imm_ID({ID_IR[25:6], Func}), .rst(or_8_out), .JMP_ID(JMP), .JR_ID(JR), .Rt_ID(ID_IR[20:16]),
    .Rd_ID(ID_IR[15:11]), .RegDst(RegDst), .JAL(JAL), .RegWrite(RegWriteID), .MemToReg(MemToBeg),
    .MemWrite(MemWriteID), .ALU_OP(AluOP), .ALU_src(AluSrcB), .Bne(Bne), .Beq(Beq), .IR_ID({ID_IR, Func}),
    .PC_ID(ID_PC), .R1_ID(R1_ID_t), .R2_ID(R2_ID_t), .IMM_ID(multiplexer_7_out), .shamt__ID(ID_IR[10:6]),
    .enable(not_2_out), .J_JAL_imm_EX(J_JAL[27:2]), .clk(CLK), .JMP_EX(JMP_EX), .JR_EX(JR_EX),
    .Rt_EX(rt_ID_EX), .Rd_EX(rd_ID_EX), .RegDst_EX(RegDst_EX), .JAL_EX(JAL_Ex), .RegWrite_EX(RegWrite_ex),
    .MemToReg_EX(MemToBeg_ex), .MemWrite_EX(MemWrite_ex), .ALU_OP_EX(AluOP_EX), .ALU_src_EX(AluSrcB_EX),
    .Bne_EX(Bne_EX), .Beq_EX(Beq_EX), .IR_EX(EX_IR), .PC_EX(EX_PC), .R1_EX(R1EX), .R2_EX(R2EX),
    .IMM_EX(IMMEX), .shamt_EX(shamtEX), .enable_EX(enableEX), .syscall(Syscall), .syscallex(Syscall_ex),
    .clear(1'b0), .SB(SB), .SB_EX(SB_EX), .forward_To_R1(forwardToR1), .forward_to_r1_2(forwardToR1_EX),
    .forward_To_R2(forwardToR2), .forward_to_r2_2(forwardToR2_EX), .bglz(BGTZ), .bglz_ex(BGTZ_EX),
    .ERET(ERET), .ERET_ex(ERET_ex));  // open: equal_22_ex, equal_22
  and and_6 (RET1, decoder_1_out1, ERET_WB);
  and and_7 (RET2, decoder_1_out2, ERET_WB);
  and and_8 (RET3, decoder_1_out3, ERET_WB);
  Adder #(.width(32)) adder_3 (.a(EX_PC), .b(32'h4), .out({J_JAL[31:28], adder_3_out}));  // open: cin, cout
  Shifter #(.width(32), .shift("ll")) shifter_1 (.in(IMMEX), .\dist (5'b00010), .out(shifter_1_out));
  Multiplexer #(.select(1), .width(5), .disabled("Z"), .enable("false")) multiplexer_14 (
    .in0(rt_ID_EX), .in1(rd_ID_EX), .out(multiplexer_14_out), .sel(RegDst_EX));
  Multiplexer #(.select(1), .width(5), .disabled("Z"), .enable("false")) multiplexer_15 (
    .in0(rt_ID_MEM), .in1(rd_ID_MEM), .out(multiplexer_15_out), .sel(RegDst_MEM));
  Adder #(.width(32)) adder_4 (.a({J_JAL[31:28], adder_3_out}), .b(shifter_1_out), .out(Beq_Bne));  // open: cin, cout
  Multiplexer #(.select(1), .width(5), .disabled("Z"), .enable("false")) multiplexer_16 (
    .in0(multiplexer_14_out), .in1({5{1'b1}}), .out(multiplexer_16_out), .sel(JAL_Ex));
  Multiplexer #(.select(1), .width(5), .disabled("Z"), .enable("false")) multiplexer_17 (
    .in0(multiplexer_15_out), .in1({5{1'b1}}), .out(multiplexer_17_out), .sel(JAL_MEM));
  Multiplexer #(.select(2), .width(32), .disabled("Z"), .enable("false")) multiplexer_18 (
    .in0(R1EX), .in1(MEMDATA_WB), .in2(RESULT_WB), .in3({RESULT_MEM, bytechoose}), .out(R1_USE),
    .sel(forwardToR1_EX));
  Multiplexer #(.select(2), .width(32), .disabled("Z"), .enable("false")) multiplexer_19 (
    .in0(R2EX), .in1(MEMDATA_WB), .in2(RESULT_WB), .in3({RESULT_MEM, bytechoose}), .out(R2_USE),
    .sel(forwardToR2_EX));
  D_Flip_Flop #(.trigger("high"), .Pre_Clr_Positions("LEGACY"), .NegatePresetClear("false"), .enable("true"), .NewFFLayout("false")) d_ff_1 (.Q(d_ff_1_q));  // open: clk, D, Qn, preset, en, reset
  // Probe on 13'h8f9
  Clock #(.highDuration(1), .lowDuration(1)) clock_2 (.out(clock_2_out));
  \数据相关检测  \u_数据相关检测_1  (
    .OP(ID_IR[31:26]), .Func(Func), .MEM_WriteReg(multiplexer_17_out), .EX_WriteReg(multiplexer_16_out),
    .MEM_RegWrite(RegWrite_MEM), .R2_ID(R2_ID), .EX_RegWrite(RegWrite_ex), .R1_ID(R1_ID), .stall(\数据相关 ));
  Multiplexer #(.select(1), .width(32), .disabled("Z"), .enable("false")) multiplexer_20 (
    .in0(R2_USE), .in1(IMMEX), .out(multiplexer_20_out), .sel(AluSrcB_EX));
  Comparator #(.width(13), .mode("twosComplement")) comparator_3 (
    .a(CNT_num), .b(13'h8f9), .eq(comparator_3_eq), .lt(comparator_3_lt));  // open: gt
  \重定向检测  \u_重定向检测_1  (
    .OP(ID_IR[31:26]), .Func(Func), .MEM_memtoreg(MemToBeg_MEM), .EX_memtoreg(MemToBeg_ex),
    .MEM_WriteReg(multiplexer_17_out), .EX_WriteReg(multiplexer_16_out), .MEM_RegWrite(RegWrite_MEM),
    .R2_ID(R2_ID), .EX_RegWrite(RegWrite_ex), .R1_ID(R1_ID), .forwardToR1(forwardToR1), .loaduse(load_use),
    .forwardToR2(forwardToR2));
  and and_9 (and_9_out, Beq_EX, mips_alu_1_equal);
  nand nand_1 (nand_1_out, d_ff_1_q, comparator_3_eq);
  Counter #(.width(13), .max('h1fff), .ongoal("stay"), .trigger("rising"), .behavior("old")) counter_4 (
    .count(comparator_3_lt), .Q(CNT_num), .clk(clock_2_out));  // open: load, D, carry, clr, preset
  or or_9 (\是否跳转 , and_9_out, and_10_out, and_11_out);
  and and_10 (and_10_out, not_6_out, Bne_EX);
  not not_6 (not_6_out, mips_alu_1_equal);
  MIPS_ALU mips_alu_1 (
    .X(R1_USE), .Y(multiplexer_20_out), .AluOP(AluOP_EX), .Equal(mips_alu_1_equal), .Result(RESULT),
    .shamt(shamtEX));  // open: Result_2
  assign CLK = nand_1_out ? clock_2_out : 1'bz;  // Controlled_Buffer controlled_buffer_1
  Pull_Resistor #(.pull(1)) pull_resistor_1 (.node(CLK));
  Counter #(.width(16), .max('hffff), .ongoal("wrap"), .trigger("rising"), .behavior("old")) counter_5 (
    .count(\是否跳转 ), .Q(\条件分支成功数 ), .clk(CLK), .clr(RST));  // open: load, D, carry, preset
  and and_11 (and_11_out, BGTZ_EX, comparator_4_gt);
  EX_MEM ex_mem_1 (
    .Rt_ID(rt_ID_EX), .Rd_ID(rd_ID_EX), .RegDst(RegDst_EX), .JAL(JAL_Ex), .RegWrite(RegWrite_ex),
    .MemToReg(MemToBeg_ex), .MemWrite(MemWrite_ex), .ALU_OP(AluOP_EX), .ALU_src(AluSrcB_EX), .Bne(Bne_EX),
    .Beq(Beq_EX), .IR_ID(EX_IR), .PC_ID(EX_PC), .ALUresult_ID(RESULT), .R2_ID(R2_USE), .enable(enableEX),
    .clk(CLK), .Rt_EX(rt_ID_MEM), .Rd_EX(rd_ID_MEM), .RegDst_EX(RegDst_MEM), .JAL_EX(JAL_MEM),
    .RegWrite_EX(RegWrite_MEM), .MemToReg_EX(MemToBeg_MEM), .MemWrite_EX(MemWrite), .ALU_OP_EX(AluOP_MEM),
    .ALU_src_EX(AluSrcB_MEM), .Bne_EX(Bne_MEM), .Beq_EX(Beq_MEM), .IR_EX(IR_PC_MEM), .PC_EX(M_PC),
    .ALU_result_EX({RESULT_MEM, bytechoose}), .R2_EX(ex_mem_1_r2_ex), .enable_EX(ex_mem_1_enable_ex),
    .syscall(Syscall_ex), .sys_prime_call_EX(Syscall_mem), .SB(SB_EX), .SB_mem(SB_MEM), .led(LedData_in),
    .led_EX(LedData_mem), .equal_22(equal_22), .equal_22_EX(equal_22_mem), .eret(ERET_ex), .eret_mem(ERET_mem));  // open: clear, bglz, bglz_mem
  Comparator #(.width(32), .mode("twosComplement")) comparator_4 (
    .a(R1_USE), .b({32{1'b0}}), .gt(comparator_4_gt));  // open: eq, lt
  assign bit_extender_3_out = {{3{1'b0}}, RESULT[1:0]};  // Bit_Extender bit_extender_3
  Demultiplexer #(.select(2), .width(8), .tristate("false"), .disabled("Z"), .enable("false")) demultiplexer_1 (
    .out0(demultiplexer_1_out0), .out1(demultiplexer_1_out1), .out2(demultiplexer_1_out2),
    .out3(demultiplexer_1_out3), .in({8{1'b1}}), .sel(RESULT[1:0]));
  assign and_12_out = ex_mem_1_r2_ex & 32'hff;  // AND_Gate and_12, 32 bits wide
  Multiplier #(.width(5)) multiplier_1 (
    .a(5'b01000), .b(bit_extender_3_out), .out(multiplier_1_out));  // open: cin, cout
  RAM #(.addrWidth(10), .dataWidth(32), .bus("separate"), .Select("high")) ram_1 (
    .addr(RESULT_MEM[11:2]), .din(MDin), .data(MEMDATA_MEM), .str(MemWrite), .clk(CLK), .ld(1'b1), .clr(RST));  // open: sel
  Shifter #(.width(32), .shift("ll")) shifter_2 (.in(and_12_out), .\dist (multiplier_1_out), .out(shifter_2_out));
  assign and_13_out = MEMDATA_MEM & not_7_out;  // AND_Gate and_13, 32 bits wide
  assign not_7_out = ~{demultiplexer_1_out3, demultiplexer_1_out2, demultiplexer_1_out1, demultiplexer_1_out0};  // NOT_Gate not_7, 32 bits wide
  Multiplexer #(.select(1), .width(32), .disabled("Z"), .enable("false")) multiplexer_21 (
    .in0(ex_mem_1_r2_ex), .in1(or_10_out), .out(MDin), .sel(SB_MEM));
  assign or_10_out = shifter_2_out | and_13_out;  // OR_Gate or_10, 32 bits wide
  MEM_WB mem_wb_1 (
    .Rt_ID(rt_ID_MEM), .Rd_ID(rd_ID_MEM), .RegDst(RegDst_MEM), .JAL(JAL_MEM), .RegWrite(RegWrite_MEM),
    .MemToReg(MemToBeg_MEM), .IR_ID(IR_PC_MEM), .PC_ID(M_PC), .alureslut({RESULT_MEM, bytechoose}),
    .MemData(MEMDATA_MEM), .enable(ex_mem_1_enable_ex), .clk(CLK), .Rt_EX(rt_ID_WB), .Rd_EX(rd_ID_WB),
    .RegDst_EX(RegDst_WB), .JAL_EX(JAL_WB), .RegWrite_EX(RegWrite), .MemToReg_EX(MemToBeg_WB),
    .IR_EX(IR_PC_WB), .PC_EX(WB_PC), .ALUresult(RESULT_WB), .MemData_2(MEMDATA_WB), .enable_EX(enable_WB),
    .syscall(Syscall_mem), .syscall_EX(Syscall_wb), .led(LedData_mem), .led_wb(LedData),
    .equal_22(equal_22_mem), .equal_22_EX(equal_22_wb), .SB_WB_2(SB_WB), .SB(SB_MEM), .eret(ERET_mem),
    .SB_WB(ERET_WB));  // open: clear, pause_wb, pause

  // Other names for the same wires on the sheet: ID_IR[5:0] = Func; IR_PC[31:0] = {ID_IR, Func};
  //   J_JAL_imm_ID[25:0] = {ID_IR[25:6], Func}; rd_ID[4:0] = ID_IR[15:11]; rt_ID[4:0] = ID_IR[20:16];
  //   rs_ID[4:0] = ID_IR[25:21]; OP[5:0] = ID_IR[31:26]; IR_PC_EX[31:0] = EX_IR; J_JAL_imm_ID_EX[25:0] = J_JAL[27:2];
  //   MEM_IR[31:0] = IR_PC_MEM; MEM_PC[31:0] = M_PC; MemWrite_MEM = MemWrite; PC[31:0] = IF_PC;
  //   RegWrite_WB = RegWrite; RESULT_MEM[1:0] = bytechoose; WB_IR[31:0] = IR_PC_WB; 指示灯1 = W1; 指示灯2 = W2; 指示灯3 = W3

  // Notes on the sheet:
  //   中断源
  //   时空图监测，可删除
  //   中断等待指示
  //   数码管输出
  //   指令存储器
  //   contents of rom_1 (hex, n*v repeats v):
  //   201d07d0 20100001 109fc0 139fc3 8021 2012000c 24160008 26100001 3210000f 20080008 20090001 139900
  //   2709825 132020 20020022 c 1094022 1500fff9 22100001 2018000f 2188024 108700 20080008 20090001 139902
  //   2709825 132021 20020022 c 1094022 1500fff9 108702 2c9b022 12c00001 8000c07 4020 1084027 84400
  //   3508ffff 82021 20020022 c 8000c01 afa20000 23bd0004 afa40000 23bd0004 afb00000 23bd0004 afb30000
  //   23bd0004 afb40000 23bd0004 afb50000 23bd0004 afb60000 23bd0004 20160001 20140003 20150001 168020
  //   108100 2149825 132020 20020022 c 1600fffa 295a022 1680fff7 23bdfffc 8fb60000 23bdfffc 8fb50000
  //   23bdfffc 8fb40000 23bdfffc 8fb30000 23bdfffc 8fb00000 23bdfffc 8fa40000 23bdfffc 8fa20000 42000018
  //   afa20000 23bd0004 afa40000 23bd0004 afb00000 23bd0004 afb30000 23bd0004 afb40000 23bd0004 afb50000
  //   23bd0004 afb60000 23bd0004 20160002 20140003 20150001 168020 108100 2149825 132020 20020022 c
  //   1600fffa 295a022 1680fff7 23bdfffc 8fb60000 23bdfffc 8fb50000 23bdfffc 8fb40000 23bdfffc 8fb30000
  //   23bdfffc 8fb00000 23bdfffc 8fa40000 23bdfffc 8fa20000 42000018 afa20000 23bd0004 afa40000 23bd0004
  //   afb00000 23bd0004 afb30000 23bd0004 afb40000 23bd0004 afb50000 23bd0004 afb60000 23bd0004 20160003
  //   20140003 20150001 168020 108100 2149825 132020 20020022 c 1600fffa 295a022 1680fff7 23bdfffc
  //   8fb60000 23bdfffc 8fb50000 23bdfffc 8fb40000 23bdfffc 8fb30000 23bdfffc 8fb00000 23bdfffc 8fa40000
  //   23bdfffc 8fa20000 42000018
  //   中断返回
  //   中断请求信号
  //   在EX段执行处理中断，在EX段的指令不让执行，在EX段前的两个指令让其执行，所以eret移到wb段，然后EX段后的两个指令不让执行，在IF/ID和ID/EX中拆入两个气泡
  //   OP
  //   Func
  //   rs
  //   rt
  //   rd
  //   流水调试日志用
  //   JMP
  //   JR
  //   OP
  //   Func
  //   Beq
  //   Bne
  //   MemToReg
  //   MemWrite
  //   AluOP
  //   AluSrcB
  //   RegWrite
  //   JAL
  //   RegDst
  //   Syscall
  //   开关中断
  //   为方便自动评测，需要输出流水线各段保存的PC值，注意是PC不是PC+4，另外ID段寄存器写入信息，Mem段内存写入信息也要输出
  //   控制位
  //   暂停节拍，不能为0
  //   戳工具置1进入计数暂停模式，ctrl+k时钟自动运行到对应节拍暂停
  //   ctrl+k关闭时钟连续运行，将控制位置零，进入单步调试模式调试
  //   用这个时钟源需要去掉电路中的其他时钟源
  //   可计数暂停的时钟源
endmodule

module ps1 (
  input  OP0,
  input  OP1,
  input  OP2,
  input  OP3,
  input  OP4,
  input  OP5,
  input  F0,
  input  F1,
  input  F2,
  input  F3,
  input  F4,
  input  F5,
  output bgtz,
  output XOR,
  output SB,
  output SUBU
);

  wire and_2_out, and_3_out, and_5_out, and_6_out, not_1_out, not_2_out, not_3_out, not_4_out, not_5_out,
       not_6_out, not_7_out, not_8_out, not_9_out, not_10_out, not_11_out, not_12_out, not_13_out,
       not_14_out, not_15_out, not_16_out, not_17_out, not_18_out, not_19_out, not_20_out, not_21_out,
       not_22_out, not_23_out, not_24_out, not_25_out;

  not not_1 (not_1_out, OP3);
  not not_2 (not_2_out, OP4);
  not not_3 (not_3_out, OP5);
  not not_4 (not_4_out, OP0);
  not not_5 (not_5_out, OP1);
  not not_6 (not_6_out, OP2);
  not not_7 (not_7_out, OP3);
  not not_8 (not_8_out, OP4);
  not not_9 (not_9_out, OP5);
  not not_10 (not_10_out, F0);
  not not_11 (not_11_out, F3);
  not not_12 (not_12_out, F4);
  not not_13 (not_13_out, OP0);
  not not_14 (not_14_out, OP1);
  not not_15 (not_15_out, OP2);
  not not_16 (not_16_out, OP4);
  not not_17 (not_17_out, OP0);
  not not_18 (not_18_out, OP1);
  not not_19 (not_19_out, OP2);
  not not_20 (not_20_out, OP3);
  not not_21 (not_21_out, OP4);
  not not_22 (not_22_out, OP5);
  not not_23 (not_23_out, F2);
  not not_24 (not_24_out, F3);
  not not_25 (not_25_out, F4);
  and and_1 (bgtz, OP0, OP1, OP2, not_1_out, not_2_out, not_3_out);
  and and_2 (and_2_out, not_4_out, not_5_out, not_6_out, not_7_out, not_8_out, not_9_out);
  and and_3 (and_3_out, not_10_out, F1, F2, not_11_out, not_12_out, F5);
  and and_4 (SB, not_13_out, not_14_out, not_15_out, OP3, not_16_out, OP5);
  and and_5 (and_5_out, not_17_out, not_18_out, not_19_out, not_20_out, not_21_out, not_22_out);
  and and_6 (and_6_out, F0, F1, not_23_out, not_24_out, not_25_out, F5);
  or or_1 (XOR, and_2_out, and_3_out);
  or or_2 (SUBU, and_5_out, and_6_out);
endmodule

module IF_ID (
  input  [31:0] IRin,
  input  [31:0] PCin,
  input  enable,
  input  rst,
  input  clear,
  input  clk,
  output [31:0] IRout,
  output [31:0] PCout,
  output enable_out
);

  wire [31:0] multiplexer_1_out, multiplexer_2_out;

  Multiplexer #(.select(1), .width(32), .disabled("Z"), .enable("false")) multiplexer_1 (
    .in0(IRin), .in1({32{1'b0}}), .out(multiplexer_1_out), .sel(rst));
  Multiplexer #(.select(1), .width(32), .disabled("Z"), .enable("false")) multiplexer_2 (
    .in0(PCin), .in1({32{1'b0}}), .out(multiplexer_2_out), .sel(rst));
  Register #(.width(32), .trigger("rising"), .Select("low")) register_1 (
    .D(multiplexer_1_out), .en(enable), .Q(IRout), .clk(clk), .clr(clear));
  Register #(.width(32), .trigger("rising"), .Select("low")) register_2 (
    .D(multiplexer_2_out), .en(enable), .Q(PCout), .clk(clk), .clr(clear));
  Register #(.width(1), .trigger("rising"), .Select("low")) register_3 (
    .D(enable), .Q(enable_out), .clk(clk), .clr(clear));  // open: en
endmodule

module ID_EX (
  input  ERET,
  input  bglz,
  input  equal_22,
  input  [1:0] forward_To_R1,
  input  [1:0] forward_To_R2,
  input  SB,
  input  syscall,
  input  [25:0] J_JAL_imm_ID,
  input  rst,
  input  clk,
  input  JMP_ID,
  input  JR_ID,
  input  [4:0] Rt_ID,
  input  [4:0] Rd_ID,
  input  RegDst,
  input  JAL,
  input  RegWrite,
  input  MemToReg,
  input  MemWrite,
  input  [3:0] ALU_OP,
  input  ALU_src,
  input  Bne,
  input  Beq,
  input  [31:0] IR_ID,
  input  [31:0] PC_ID,
  input  [31:0] R1_ID,
  input  [31:0] R2_ID,
  input  [31:0] IMM_ID,
  input  [4:0] shamt__ID,
  input  enable,
  input  clear,
  output ERET_ex,
  output bglz_ex,
  output equal_22_ex,
  output [1:0] forward_to_r1_2,
  output [1:0] forward_to_r2_2,
  output SB_EX,
  output syscallex,
  output [25:0] J_JAL_imm_EX,
  output JMP_EX,
  output JR_EX,
  output [4:0] Rt_EX,
  output [4:0] Rd_EX,
  output RegDst_EX,
  output JAL_EX,
  output RegWrite_EX,
  output MemToReg_EX,
  output MemWrite_EX,
  output [3:0] ALU_OP_EX,
  output ALU_src_EX,
  output Bne_EX,
  output Beq_EX,
  output [31:0] IR_EX,
  output [31:0] PC_EX,
  output [31:0] R1_EX,
  output [31:0] R2_EX,
  output [31:0] IMM_EX,
  output [4:0] shamt_EX,
  output enable_EX
);

  wire multiplexer_1_out, multiplexer_2_out, multiplexer_3_out, multiplexer_5_out, multiplexer_6_out,
       multiplexer_7_out, multiplexer_8_out, multiplexer_9_out, multiplexer_10_out, multiplexer_13_out,
       multiplexer_14_out, multiplexer_16_out, multiplexer_17_out, multiplexer_20_out, multiplexer_21_out;
  wire [1:0] multiplexer_11_out, multiplexer_12_out;
  wire [3:0] multiplexer_4_out;
  wire [4:0] multiplexer_18_out, multiplexer_19_out, multiplexer_27_out;
  wire [25:0] multiplexer_15_out;
  wire [31:0] multiplexer_22_out, multiplexer_23_out, multiplexer_24_out, multiplexer_25_out,
       multiplexer_26_out;

  Multiplexer #(.select(1), .width(1), .disabled("Z"), .enable("false")) multiplexer_1 (
    .in0(RegWrite), .in1(1'b0), .out(multiplexer_1_out), .sel(rst));
  Multiplexer #(.select(1), .width(1), .disabled("Z"), .enable("false")) multiplexer_2 (
    .in0(MemToReg), .in1(1'b0), .out(multiplexer_2_out), .sel(rst));
  Multiplexer #(.select(1), .width(1), .disabled("Z"), .enable("false")) multiplexer_3 (
    .in0(MemWrite), .in1(1'b0), .out(multiplexer_3_out), .sel(rst));
  Multiplexer #(.select(1), .width(4), .disabled("Z"), .enable("false")) multiplexer_4 (
    .in0(ALU_OP), .in1(4'b0000), .out(multiplexer_4_out), .sel(rst));
  Multiplexer #(.select(1), .width(1), .disabled("Z"), .enable("false")) multiplexer_5 (
    .in0(ALU_src), .in1(1'b0), .out(multiplexer_5_out), .sel(rst));
  Multiplexer #(.select(1), .width(1), .disabled("Z"), .enable("false")) multiplexer_6 (
    .in0(Bne), .in1(1'b0), .out(multiplexer_6_out), .sel(rst));
  Multiplexer #(.select(1), .width(1), .disabled("Z"), .enable("false")) multiplexer_7 (
    .in0(Beq), .in1(1'b0), .out(multiplexer_7_out), .sel(rst));
  Multiplexer #(.select(1), .width(1), .disabled("Z"), .enable("false")) multiplexer_8 (
    .in0(ERET), .in1(1'b0), .out(multiplexer_8_out), .sel(rst));
  Multiplexer #(.select(1), .width(1), .disabled("Z"), .enable("false")) multiplexer_9 (
    .in0(bglz), .in1(1'b0), .out(multiplexer_9_out), .sel(rst));
  Multiplexer #(.select(1), .width(1), .disabled("Z"), .enable("false")) multiplexer_10 (
    .in0(equal_22), .in1(1'b0), .out(multiplexer_10_out), .sel(rst));
  Multiplexer #(.select(1), .width(2), .disabled("Z"), .enable("false")) multiplexer_11 (
    .in0(forward_To_R1), .in1(2'b00), .out(multiplexer_11_out), .sel(rst));
  Multiplexer #(.select(1), .width(2), .disabled("Z"), .enable("false")) multiplexer_12 (
    .in0(forward_To_R2), .in1(2'b00), .out(multiplexer_12_out), .sel(rst));
  Multiplexer #(.select(1), .width(1), .disabled("Z"), .enable("false")) multiplexer_13 (
    .in0(SB), .in1(1'b0), .out(multiplexer_13_out), .sel(rst));
  Multiplexer #(.select(1), .width(1), .disabled("Z"), .enable("false")) multiplexer_14 (
    .in0(syscall), .in1(1'b0), .out(multiplexer_14_out), .sel(rst));
  Multiplexer #(.select(1), .width(26), .disabled("Z"), .enable("false")) multiplexer_15 (
    .in0(J_JAL_imm_ID), .in1({26{1'b0}}), .out(multiplexer_15_out), .sel(rst));
  Multiplexer #(.select(1), .width(1), .disabled("Z"), .enable("false")) multiplexer_16 (
    .in0(JMP_ID), .in1(1'b0), .out(multiplexer_16_out), .sel(rst));
  Multiplexer #(.select(1), .width(1), .disabled("Z"), .enable("false")) multiplexer_17 (
    .in0(JR_ID), .in1(1'b0), .out(multiplexer_17_out), .sel(rst));
  Multiplexer #(.select(1), .width(5), .disabled("Z"), .enable("false")) multiplexer_18 (
    .in0(Rt_ID), .in1({5{1'b0}}), .out(multiplexer_18_out), .sel(rst));
  Multiplexer #(.select(1), .width(5), .disabled("Z"), .enable("false")) multiplexer_19 (
    .in0(Rd_ID), .in1({5{1'b0}}), .out(multiplexer_19_out), .sel(rst));
  Multiplexer #(.select(1), .width(1), .disabled("Z"), .enable("false")) multiplexer_20 (
    .in0(RegDst), .in1(1'b0), .out(multiplexer_20_out), .sel(rst));
  Multiplexer #(.select(1), .width(1), .disabled("Z"), .enable("false")) multiplexer_21 (
    .in0(JAL), .in1(1'b0), .out(multiplexer_21_out), .sel(rst));
  Multiplexer #(.select(1), .width(32), .disabled("Z"), .enable("false")) multiplexer_22 (
    .in0(IR_ID), .in1({32{1'b0}}), .out(multiplexer_22_out), .sel(rst));
  Multiplexer #(.select(1), .width(32), .disabled("Z"), .enable("false")) multiplexer_23 (
    .in0(PC_ID), .in1({32{1'b0}}), .out(multiplexer_23_out), .sel(rst));
  Multiplexer #(.select(1), .width(32), .disabled("Z"), .enable("false")) multiplexer_24 (
    .in0(R1_ID), .in1({32{1'b0}}), .out(multiplexer_24_out), .sel(rst));
  Multiplexer #(.select(1), .width(32), .disabled("Z"), .enable("false")) multiplexer_25 (
    .in0(R2_ID), .in1({32{1'b0}}), .out(multiplexer_25_out), .sel(rst));
  Multiplexer #(.select(1), .width(32), .disabled("Z"), .enable("false")) multiplexer_26 (
    .in0(IMM_ID), .in1({32{1'b0}}), .out(multiplexer_26_out), .sel(rst));
  Multiplexer #(.select(1), .width(5), .disabled("Z"), .enable("false")) multiplexer_27 (
    .in0(shamt__ID), .in1({5{1'b0}}), .out(multiplexer_27_out), .sel(rst));
  Register #(.width(26), .trigger("rising"), .Select("low")) register_1 (
    .D(multiplexer_15_out), .en(enable), .Q(J_JAL_imm_EX), .clk(clk), .clr(clear));
  Register #(.width(1), .trigger("rising"), .Select("low")) register_2 (
    .D(multiplexer_16_out), .en(enable), .Q(JMP_EX), .clk(clk), .clr(clear));
  Register #(.width(1), .trigger("rising"), .Select("low")) register_3 (
    .D(multiplexer_17_out), .en(enable), .Q(JR_EX), .clk(clk), .clr(clear));
  Register #(.width(5), .trigger("rising"), .Select("low")) register_4 (
    .D(multiplexer_18_out), .en(enable), .Q(Rt_EX), .clk(clk), .clr(clear));
  Register #(.width(5), .trigger("rising"), .Select("low")) register_5 (
    .D(multiplexer_19_out), .en(enable), .Q(Rd_EX), .clk(clk), .clr(clear));
  Register #(.width(1), .trigger("rising"), .Select("low")) register_6 (
    .D(multiplexer_20_out), .en(enable), .Q(RegDst_EX), .clk(clk), .clr(clear));
  Register #(.width(1), .trigger("rising"), .Select("low")) register_7 (
    .D(multiplexer_21_out), .en(enable), .Q(JAL_EX), .clk(clk), .clr(clear));
  Register #(.width(1), .trigger("rising"), .Select("low")) register_8 (
    .D(multiplexer_1_out), .en(enable), .Q(RegWrite_EX), .clk(clk), .clr(clear));
  Register #(.width(1), .trigger("rising"), .Select("low")) register_9 (
    .D(multiplexer_2_out), .en(enable), .Q(MemToReg_EX), .clk(clk), .clr(clear));
  Register #(.width(1), .trigger("rising"), .Select("low")) register_10 (
    .D(multiplexer_3_out), .en(enable), .Q(MemWrite_EX), .clk(clk));  // open: clr
  Register #(.width(4), .trigger("rising"), .Select("low")) register_11 (
    .D(multiplexer_4_out), .en(enable), .Q(ALU_OP_EX), .clk(clk), .clr(clear));
  Register #(.width(1), .trigger("rising"), .Select("low")) register_12 (
    .D(multiplexer_5_out), .en(enable), .Q(ALU_src_EX), .clk(clk), .clr(clear));
  Register #(.width(1), .trigger("rising"), .Select("low")) register_13 (
    .D(multiplexer_6_out), .en(enable), .Q(Bne_EX), .clk(clk), .clr(clear));
  Register #(.width(1), .trigger("rising"), .Select("low")) register_14 (
    .D(multiplexer_7_out), .en(enable), .Q(Beq_EX), .clk(clk), .clr(clear));
  Register #(.width(32), .trigger("rising"), .Select("low")) register_15 (
    .D(multiplexer_22_out), .en(enable), .Q(IR_EX), .clk(clk), .clr(clear));
  Register #(.width(32), .trigger("rising"), .Select("low")) register_16 (
    .D(multiplexer_23_out), .en(enable), .Q(PC_EX), .clk(clk), .clr(clear));
  Register #(.width(32), .trigger("rising"), .Select("low")) register_17 (
    .D(multiplexer_24_out), .en(enable), .Q(R1_EX), .clk(clk), .clr(clear));
  Register #(.width(32), .trigger("rising"), .Select("low")) register_18 (
    .D(multiplexer_25_out), .en(enable), .Q(R2_EX), .clk(clk), .clr(clear));
  Register #(.width(32), .trigger("rising"), .Select("low")) register_19 (
    .D(multiplexer_26_out), .en(enable), .Q(IMM_EX), .clk(clk), .clr(clear));
  Register #(.width(5), .trigger("rising"), .Select("low")) register_20 (
    .D(multiplexer_27_out), .en(enable), .Q(shamt_EX), .clk(clk), .clr(clear));
  Register #(.width(1), .trigger("rising"), .Select("low")) register_21 (
    .D(enable), .Q(enable_EX), .clk(clk), .clr(clear));  // open: en
  Register #(.width(1), .trigger("rising"), .Select("low")) register_22 (
    .D(multiplexer_8_out), .en(enable), .Q(ERET_ex), .clk(clk), .clr(clear));
  Register #(.width(1), .trigger("rising"), .Select("low")) register_23 (
    .D(multiplexer_9_out), .en(enable), .Q(bglz_ex), .clk(clk), .clr(clear));
  Register #(.width(1), .trigger("rising"), .Select("low")) register_24 (
    .D(multiplexer_10_out), .en(enable), .Q(equal_22_ex), .clk(clk), .clr(clear));
  Register #(.width(2), .trigger("rising"), .Select("low")) register_25 (
    .D(multiplexer_11_out), .en(enable), .Q(forward_to_r1_2), .clk(clk), .clr(clear));
  Register #(.width(2), .trigger("rising"), .Select("low")) register_26 (
    .D(multiplexer_12_out), .en(enable), .Q(forward_to_r2_2), .clk(clk), .clr(clear));
  Register #(.width(1), .trigger("rising"), .Select("low")) register_27 (
    .D(multiplexer_13_out), .en(enable), .Q(SB_EX), .clk(clk), .clr(clear));
  Register #(.width(1), .trigger("rising"), .Select("low")) register_28 (
    .D(multiplexer_14_out), .en(enable), .Q(syscallex), .clk(clk), .clr(clear));

  // Notes on the sheet:
  //   MEM
endmodule

module EX_MEM (
  input  clk,
  input  eret,
  input  bglz,
  input  SB,
  input  syscall,
  input  equal_22,
  input  [4:0] Rt_ID,
  input  [4:0] Rd_ID,
  input  RegDst,
  input  JAL,
  input  RegWrite,
  input  MemToReg,
  input  MemWrite,
  input  [3:0] ALU_OP,
  input  ALU_src,
  input  Bne,
  input  Beq,
  input  [31:0] IR_ID,
  input  [31:0] PC_ID,
  input  [31:0] ALUresult_ID,
  input  [31:0] R2_ID,
  input  [31:0] led,
  input  enable,
  input  clear,
  output eret_mem,
  output bglz_mem,
  output SB_mem,
  output sys_prime_call_EX,
  output equal_22_EX,
  output [4:0] Rt_EX,
  output [4:0] Rd_EX,
  output RegDst_EX,
  output JAL_EX,
  output RegWrite_EX,
  output MemToReg_EX,
  output MemWrite_EX,
  output [3:0] ALU_OP_EX,
  output ALU_src_EX,
  output Bne_EX,
  output Beq_EX,
  output [31:0] IR_EX,
  output [31:0] PC_EX,
  output [31:0] ALU_result_EX,
  output [31:0] R2_EX,
  output [31:0] led_EX,
  output enable_EX
);

  Register #(.width(1), .trigger("rising"), .Select("low")) register_1 (
    .D(eret), .en(enable), .Q(eret_mem), .clk(clk), .clr(clear));
  Register #(.width(1), .trigger("rising"), .Select("low")) register_2 (
    .D(bglz), .en(enable), .Q(bglz_mem), .clk(clk), .clr(clear));
  Register #(.width(1), .trigger("rising"), .Select("low")) register_3 (
    .D(SB), .en(enable), .Q(SB_mem), .clk(clk), .clr(clear));
  Register #(.width(1), .trigger("rising"), .Select("low")) register_4 (
    .D(syscall), .en(enable), .Q(sys_prime_call_EX), .clk(clk), .clr(clear));
  Register #(.width(1), .trigger("rising"), .Select("low")) register_5 (
    .D(equal_22), .en(enable), .Q(equal_22_EX), .clk(clk), .clr(clear));
  Register #(.width(1), .trigger("rising"), .Select("low")) register_6 (
    .D(RegWrite), .en(enable), .Q(RegWrite_EX), .clk(clk), .clr(clear));
  Register #(.width(1), .trigger("rising"), .Select("low")) register_7 (
    .D(MemToReg), .en(enable), .Q(MemToReg_EX), .clk(clk), .clr(clear));
  Register #(.width(1), .trigger("rising"), .Select("low")) register_8 (
    .D(MemWrite), .en(enable), .Q(MemWrite_EX), .clk(clk), .clr(clear));
  Register #(.width(4), .trigger("rising"), .Select("low")) register_9 (
    .D(ALU_OP), .en(enable), .Q(ALU_OP_EX), .clk(clk), .clr(clear));
  Register #(.width(1), .trigger("rising"), .Select("low")) register_10 (
    .D(ALU_src), .en(enable), .Q(ALU_src_EX), .clk(clk), .clr(clear));
  Register #(.width(1), .trigger("rising"), .Select("low")) register_11 (
    .D(Bne), .en(enable), .Q(Bne_EX), .clk(clk), .clr(clear));
  Register #(.width(1), .trigger("rising"), .Select("low")) register_12 (
    .D(Beq), .en(enable), .Q(Beq_EX), .clk(clk), .clr(clear));
  Register #(.width(32), .trigger("rising"), .Select("low")) register_13 (
    .D(IR_ID), .en(enable), .Q(IR_EX), .clk(clk), .clr(clear));
  Register #(.width(32), .trigger("rising"), .Select("low")) register_14 (
    .D(PC_ID), .en(enable), .Q(PC_EX), .clk(clk), .clr(clear));
  Register #(.width(32), .trigger("rising"), .Select("low")) register_15 (
    .D(ALUresult_ID), .en(enable), .Q(ALU_result_EX), .clk(clk), .clr(clear));
  Register #(.width(32), .trigger("rising"), .Select("low")) register_16 (
    .D(R2_ID), .en(enable), .Q(R2_EX), .clk(clk), .clr(clear));
  Register #(.width(32), .trigger("rising"), .Select("low")) register_17 (
    .D(led), .en(enable), .Q(led_EX), .clk(clk), .clr(clear));
  Register #(.width(5), .trigger("rising"), .Select("low")) register_18 (
    .D(Rt_ID), .en(enable), .Q(Rt_EX), .clk(clk), .clr(clear));
  Register #(.width(5), .trigger("rising"), .Select("low")) register_19 (
    .D(Rd_ID), .en(enable), .Q(Rd_EX), .clk(clk), .clr(clear));
  Register #(.width(1), .trigger("rising"), .Select("low")) register_20 (
    .D(RegDst), .en(enable), .Q(RegDst_EX), .clk(clk), .clr(clear));
  Register #(.width(1), .trigger("rising"), .Select("low")) register_21 (
    .D(JAL), .en(enable), .Q(JAL_EX), .clk(clk), .clr(clear));
  Register #(.width(1), .trigger("rising"), .Select("low")) register_22 (
    .D(enable), .Q(enable_EX), .clk(clk), .clr(clear));  // open: en

  // Notes on the sheet:
  //   MEM
endmodule

module MEM_WB (
  input  clk,
  input  eret,
  input  SB,
  input  equal_22,
  input  syscall,
  input  [4:0] Rt_ID,
  input  [4:0] Rd_ID,
  input  RegDst,
  input  JAL,
  input  RegWrite,
  input  MemToReg,
  input  pause,
  input  [31:0] IR_ID,
  input  [31:0] PC_ID,
  input  [31:0] alureslut,
  input  [31:0] MemData,
  input  [31:0] led,
  input  enable,
  input  clear,
  output SB_WB,
  output SB_WB_2,
  output equal_22_EX,
  output syscall_EX,
  output [4:0] Rt_EX,
  output [4:0] Rd_EX,
  output RegDst_EX,
  output JAL_EX,
  output RegWrite_EX,
  output MemToReg_EX,
  output pause_wb,
  output [31:0] IR_EX,
  output [31:0] PC_EX,
  output [31:0] ALUresult,
  output [31:0] MemData_2,
  output [31:0] led_wb,
  output enable_EX
);

  Register #(.width(1), .trigger("rising"), .Select("low")) register_1 (
    .D(RegWrite), .en(enable), .Q(RegWrite_EX), .clk(clk), .clr(clear));
  Register #(.width(1), .trigger("rising"), .Select("low")) register_2 (
    .D(MemToReg), .en(enable), .Q(MemToReg_EX), .clk(clk), .clr(clear));
  Register #(.width(1), .trigger("rising"), .Select("low")) register_3 (
    .D(pause), .en(enable), .Q(pause_wb), .clk(clk), .clr(clear));
  Register #(.width(32), .trigger("rising"), .Select("low")) register_4 (
    .D(IR_ID), .en(enable), .Q(IR_EX), .clk(clk), .clr(clear));
  Register #(.width(32), .trigger("rising"), .Select("low")) register_5 (
    .D(PC_ID), .en(enable), .Q(PC_EX), .clk(clk), .clr(clear));
  Register #(.width(32), .trigger("rising"), .Select("low")) register_6 (
    .D(alureslut), .en(enable), .Q(ALUresult), .clk(clk), .clr(clear));
  Register #(.width(32), .trigger("rising"), .Select("low")) register_7 (
    .D(MemData), .en(enable), .Q(MemData_2), .clk(clk), .clr(clear));
  Register #(.width(32), .trigger("rising"), .Select("low")) register_8 (
    .D(led), .en(enable), .Q(led_wb), .clk(clk), .clr(clear));
  Register #(.width(1), .trigger("rising"), .Select("low")) register_9 (
    .D(eret), .en(enable), .Q(SB_WB), .clk(clk), .clr(clear));
  Register #(.width(1), .trigger("rising"), .Select("low")) register_10 (
    .D(SB), .en(enable), .Q(SB_WB_2), .clk(clk), .clr(clear));
  Register #(.width(1), .trigger("rising"), .Select("low")) register_11 (
    .D(equal_22), .en(enable), .Q(equal_22_EX), .clk(clk), .clr(clear));
  Register #(.width(1), .trigger("rising"), .Select("low")) register_12 (
    .D(syscall), .en(enable), .Q(syscall_EX), .clk(clk), .clr(clear));
  Register #(.width(5), .trigger("rising"), .Select("low")) register_13 (
    .D(Rt_ID), .en(enable), .Q(Rt_EX), .clk(clk), .clr(clear));
  Register #(.width(5), .trigger("rising"), .Select("low")) register_14 (
    .D(Rd_ID), .en(enable), .Q(Rd_EX), .clk(clk), .clr(clear));
  Register #(.width(1), .trigger("rising"), .Select("low")) register_15 (
    .D(RegDst), .en(enable), .Q(RegDst_EX), .clk(clk), .clr(clear));
  Register #(.width(1), .trigger("rising"), .Select("low")) register_16 (
    .D(JAL), .en(enable), .Q(JAL_EX), .clk(clk), .clr(clear));
  Register #(.width(1), .trigger("rising"), .Select("low")) register_17 (
    .D(enable), .Q(enable_EX), .clk(clk), .clr(clear));  // open: en
endmodule

module \源寄存器使用情况  (
  input  OP0,
  input  OP1,
  input  OP2,
  input  OP3,
  input  OP4,
  input  OP5,
  input  F0,
  input  F1,
  input  F2,
  input  F3,
  input  F4,
  input  F5,
  output R1_used,
  output R2_used
);

  wire and_1_out, and_2_out, and_3_out, and_4_out, and_5_out, and_6_out, and_7_out, and_8_out, and_9_out,
       and_10_out, and_11_out, and_12_out, and_13_out, and_14_out, and_15_out, and_16_out, and_17_out,
       and_18_out, and_19_out, and_20_out, and_21_out, and_22_out, and_23_out, and_24_out, and_25_out,
       and_26_out, and_27_out, and_28_out, and_29_out, and_30_out, and_31_out, and_32_out, and_33_out,
       and_34_out, and_35_out, and_36_out, and_37_out, not_1_out, not_2_out, not_3_out, not_4_out, not_5_out,
       not_6_out, not_7_out, not_8_out, not_9_out, not_10_out, not_11_out, not_12_out, not_13_out,
       not_14_out, not_15_out, not_16_out, not_17_out, not_18_out, not_19_out, not_20_out, not_21_out,
       not_22_out, not_23_out, not_24_out, not_25_out, not_26_out, not_27_out, not_28_out, not_29_out,
       not_30_out, not_31_out, not_32_out, not_33_out, not_34_out, not_35_out, not_36_out, not_37_out,
       not_38_out, not_39_out, not_40_out, not_41_out, not_42_out, not_43_out, not_44_out, not_45_out,
       not_46_out, not_47_out, not_48_out, not_49_out, not_50_out, not_51_out, not_52_out, not_53_out,
       not_54_out, not_55_out, not_56_out, not_57_out, not_58_out, not_59_out, not_60_out, not_61_out,
       not_62_out, not_63_out, not_64_out, not_65_out, not_66_out, not_67_out, not_68_out, not_69_out,
       not_70_out, not_71_out, not_72_out, not_73_out, not_74_out, not_75_out, not_76_out, not_77_out,
       not_78_out, not_79_out, not_80_out, not_81_out, not_82_out, not_83_out, not_84_out, not_85_out,
       not_86_out, not_87_out, not_88_out, not_89_out, not_90_out, not_91_out, not_92_out, not_93_out,
       not_94_out, not_95_out, not_96_out, not_97_out, not_98_out, not_99_out, not_100_out, not_101_out,
       not_102_out, not_103_out, not_104_out, not_105_out, not_106_out, not_107_out, not_108_out,
       not_109_out, not_110_out, not_111_out, not_112_out, not_113_out, not_114_out, not_115_out,
       not_116_out, not_117_out, not_118_out, not_119_out, not_120_out, not_121_out, not_122_out,
       not_123_out, not_124_out, not_125_out, not_126_out, not_127_out, not_128_out, not_129_out,
       not_130_out, not_131_out, not_132_out, not_133_out, not_134_out, not_135_out, not_136_out,
       not_137_out, not_138_out, not_139_out, not_140_out, not_141_out, not_142_out, not_143_out,
       not_144_out, not_145_out, not_146_out, not_147_out, not_148_out, not_149_out, not_150_out,
       not_151_out, not_152_out, not_153_out, not_154_out, not_155_out, not_156_out, not_157_out,
       not_158_out, not_159_out, not_160_out, not_161_out, not_162_out, not_163_out, not_164_out,
       not_165_out, not_166_out, not_167_out, not_168_out, not_169_out, not_170_out, not_171_out,
       not_172_out, not_173_out, not_174_out, not_175_out, not_176_out, not_177_out, not_178_out,
       not_179_out, not_180_out, not_181_out, not_182_out, not_183_out, not_184_out, not_185_out,
       not_186_out, not_187_out, not_188_out, not_189_out, not_190_out, not_191_out, not_192_out,
       not_193_out, not_194_out, not_195_out, not_196_out, not_197_out, not_198_out, not_199_out,
       not_200_out, not_201_out, not_202_out, not_203_out, not_204_out, not_205_out, not_206_out,
       not_207_out, not_208_out, not_209_out, not_210_out, not_211_out, not_212_out, not_213_out,
       not_214_out, not_215_out, not_216_out, not_217_out, not_218_out, not_219_out, not_220_out,
       not_221_out, not_222_out, not_223_out, not_224_out, not_225_out, not_226_out, not_227_out,
       not_228_out, not_229_out, not_230_out, not_231_out, not_232_out, not_233_out, not_234_out,
       not_235_out, not_236_out, not_237_out, not_238_out, not_239_out, not_240_out, not_241_out,
       not_242_out, not_243_out, not_244_out, not_245_out, not_246_out, not_247_out, not_248_out,
       not_249_out, not_250_out, not_251_out, not_252_out, not_253_out, not_254_out, not_255_out,
       not_256_out, not_257_out, not_258_out, not_259_out, not_260_out, not_261_out, not_262_out,
       not_263_out, not_264_out, not_265_out, not_266_out, not_267_out, not_268_out, not_269_out,
       not_270_out, not_271_out, not_272_out, not_273_out, not_274_out, not_275_out, not_276_out,
       not_277_out, not_278_out, not_279_out, not_280_out, not_281_out, not_282_out, not_283_out;

  not not_1 (not_1_out, OP5);
  not not_2 (not_2_out, OP4);
  not not_3 (not_3_out, OP3);
  not not_4 (not_4_out, OP2);
  not not_5 (not_5_out, OP1);
  not not_6 (not_6_out, OP0);
  not not_7 (not_7_out, F5);
  not not_8 (not_8_out, F4);
  not not_9 (not_9_out, F3);
  not not_10 (not_10_out, F2);
  not not_11 (not_11_out, OP5);
  not not_12 (not_12_out, OP4);
  not not_13 (not_13_out, OP3);
  not not_14 (not_14_out, OP2);
  not not_15 (not_15_out, OP1);
  not not_16 (not_16_out, OP0);
  not not_17 (not_17_out, F5);
  not not_18 (not_18_out, F4);
  not not_19 (not_19_out, F3);
  not not_20 (not_20_out, F2);
  not not_21 (not_21_out, F0);
  not not_22 (not_22_out, OP5);
  not not_23 (not_23_out, OP4);
  not not_24 (not_24_out, OP3);
  not not_25 (not_25_out, OP2);
  not not_26 (not_26_out, OP1);
  not not_27 (not_27_out, OP0);
  not not_28 (not_28_out, F4);
  not not_29 (not_29_out, F3);
  not not_30 (not_30_out, F2);
  not not_31 (not_31_out, F1);
  not not_32 (not_32_out, F0);
  not not_33 (not_33_out, OP5);
  not not_34 (not_34_out, OP4);
  not not_35 (not_35_out, OP3);
  not not_36 (not_36_out, OP2);
  not not_37 (not_37_out, OP1);
  not not_38 (not_38_out, OP0);
  not not_39 (not_39_out, F4);
  not not_40 (not_40_out, F3);
  not not_41 (not_41_out, F2);
  not not_42 (not_42_out, F1);
  not not_43 (not_43_out, OP5);
  not not_44 (not_44_out, OP4);
  not not_45 (not_45_out, OP3);
  not not_46 (not_46_out, OP2);
  not not_47 (not_47_out, OP1);
  not not_48 (not_48_out, OP0);
  not not_49 (not_49_out, F4);
  not not_50 (not_50_out, F3);
  not not_51 (not_51_out, F2);
  not not_52 (not_52_out, F0);
  not not_53 (not_53_out, OP5);
  not not_54 (not_54_out, OP4);
  not not_55 (not_55_out, OP3);
  not not_56 (not_56_out, OP2);
  not not_57 (not_57_out, OP1);
  not not_58 (not_58_out, OP0);
  not not_59 (not_59_out, F4);
  not not_60 (not_60_out, F3);
  not not_61 (not_61_out, F1);
  not not_62 (not_62_out, F0);
  not not_63 (not_63_out, OP5);
  not not_64 (not_64_out, OP4);
  not not_65 (not_65_out, OP3);
  not not_66 (not_66_out, OP2);
  not not_67 (not_67_out, OP1);
  not not_68 (not_68_out, OP0);
  not not_69 (not_69_out, F4);
  not not_70 (not_70_out, F3);
  not not_71 (not_71_out, F1);
  not not_72 (not_72_out, OP5);
  not not_73 (not_73_out, OP4);
  not not_74 (not_74_out, OP3);
  not not_75 (not_75_out, OP2);
  not not_76 (not_76_out, OP1);
  not not_77 (not_77_out, OP0);
  not not_78 (not_78_out, F4);
  not not_79 (not_79_out, F3);
  not not_80 (not_80_out, OP5);
  not not_81 (not_81_out, OP4);
  not not_82 (not_82_out, OP3);
  not not_83 (not_83_out, OP2);
  not not_84 (not_84_out, OP1);
  not not_85 (not_85_out, OP0);
  not not_86 (not_86_out, F4);
  not not_87 (not_87_out, F2);
  not not_88 (not_88_out, F0);
  not not_89 (not_89_out, OP5);
  not not_90 (not_90_out, OP4);
  not not_91 (not_91_out, OP3);
  not not_92 (not_92_out, OP2);
  not not_93 (not_93_out, OP1);
  not not_94 (not_94_out, OP0);
  not not_95 (not_95_out, F4);
  not not_96 (not_96_out, F2);
  not not_97 (not_97_out, OP5);
  not not_98 (not_98_out, OP4);
  not not_99 (not_99_out, OP3);
  not not_100 (not_100_out, OP2);
  not not_101 (not_101_out, OP1);
  not not_102 (not_102_out, OP0);
  not not_103 (not_103_out, F5);
  not not_104 (not_104_out, F4);
  not not_105 (not_105_out, F2);
  not not_106 (not_106_out, F1);
  not not_107 (not_107_out, F0);
  not not_108 (not_108_out, OP5);
  not not_109 (not_109_out, OP4);
  not not_110 (not_110_out, OP3);
  not not_111 (not_111_out, OP2);
  not not_112 (not_112_out, OP1);
  not not_113 (not_113_out, OP0);
  not not_114 (not_114_out, F5);
  not not_115 (not_115_out, F4);
  not not_116 (not_116_out, F1);
  not not_117 (not_117_out, F0);
  not not_118 (not_118_out, OP5);
  not not_119 (not_119_out, OP4);
  not not_120 (not_120_out, OP3);
  not not_121 (not_121_out, OP1);
  not not_122 (not_122_out, OP0);
  not not_123 (not_123_out, OP5);
  not not_124 (not_124_out, OP4);
  not not_125 (not_125_out, OP3);
  not not_126 (not_126_out, OP1);
  not not_127 (not_127_out, OP5);
  not not_128 (not_128_out, OP4);
  not not_129 (not_129_out, OP2);
  not not_130 (not_130_out, OP1);
  not not_131 (not_131_out, OP0);
  not not_132 (not_132_out, OP5);
  not not_133 (not_133_out, OP4);
  not not_134 (not_134_out, OP1);
  not not_135 (not_135_out, OP0);
  not not_136 (not_136_out, OP5);
  not not_137 (not_137_out, OP4);
  not not_138 (not_138_out, OP2);
  not not_139 (not_139_out, OP1);
  not not_140 (not_140_out, OP5);
  not not_141 (not_141_out, OP4);
  not not_142 (not_142_out, OP2);
  not not_143 (not_143_out, OP0);
  not not_144 (not_144_out, OP5);
  not not_145 (not_145_out, OP4);
  not not_146 (not_146_out, OP1);
  not not_147 (not_147_out, OP4);
  not not_148 (not_148_out, OP3);
  not not_149 (not_149_out, OP2);
  not not_150 (not_150_out, OP4);
  not not_151 (not_151_out, OP2);
  not not_152 (not_152_out, OP5);
  not not_153 (not_153_out, OP4);
  not not_154 (not_154_out, OP3);
  not not_155 (not_155_out, OP2);
  not not_156 (not_156_out, OP1);
  not not_157 (not_157_out, OP0);
  not not_158 (not_158_out, F5);
  not not_159 (not_159_out, F4);
  not not_160 (not_160_out, F3);
  not not_161 (not_161_out, F2);
  not not_162 (not_162_out, F1);
  not not_163 (not_163_out, F0);
  not not_164 (not_164_out, OP5);
  not not_165 (not_165_out, OP4);
  not not_166 (not_166_out, OP3);
  not not_167 (not_167_out, OP2);
  not not_168 (not_168_out, OP1);
  not not_169 (not_169_out, OP0);
  not not_170 (not_170_out, F5);
  not not_171 (not_171_out, F4);
  not not_172 (not_172_out, F3);
  not not_173 (not_173_out, F2);
  not not_174 (not_174_out, OP5);
  not not_175 (not_175_out, OP4);
  not not_176 (not_176_out, OP3);
  not not_177 (not_177_out, OP2);
  not not_178 (not_178_out, OP1);
  not not_179 (not_179_out, OP0);
  not not_180 (not_180_out, F5);
  not not_181 (not_181_out, F4);
  not not_182 (not_182_out, F3);
  not not_183 (not_183_out, F2);
  not not_184 (not_184_out, F0);
  not not_185 (not_185_out, OP5);
  not not_186 (not_186_out, OP4);
  not not_187 (not_187_out, OP3);
  not not_188 (not_188_out, OP2);
  not not_189 (not_189_out, OP1);
  not not_190 (not_190_out, OP0);
  not not_191 (not_191_out, F4);
  not not_192 (not_192_out, F3);
  not not_193 (not_193_out, F2);
  not not_194 (not_194_out, F1);
  not not_195 (not_195_out, F0);
  not not_196 (not_196_out, OP5);
  not not_197 (not_197_out, OP4);
  not not_198 (not_198_out, OP3);
  not not_199 (not_199_out, OP2);
  not not_200 (not_200_out, OP1);
  not not_201 (not_201_out, OP0);
  not not_202 (not_202_out, F4);
  not not_203 (not_203_out, F3);
  not not_204 (not_204_out, F2);
  not not_205 (not_205_out, F1);
  not not_206 (not_206_out, OP5);
  not not_207 (not_207_out, OP4);
  not not_208 (not_208_out, OP3);
  not not_209 (not_209_out, OP2);
  not not_210 (not_210_out, OP1);
  not not_211 (not_211_out, OP0);
  not not_212 (not_212_out, F4);
  not not_213 (not_213_out, F3);
  not not_214 (not_214_out, F2);
  not not_215 (not_215_out, F0);
  not not_216 (not_216_out, OP5);
  not not_217 (not_217_out, OP4);
  not not_218 (not_218_out, OP3);
  not not_219 (not_219_out, OP2);
  not not_220 (not_220_out, OP1);
  not not_221 (not_221_out, OP0);
  not not_222 (not_222_out, F4);
  not not_223 (not_223_out, F3);
  not not_224 (not_224_out, F1);
  not not_225 (not_225_out, F0);
  not not_226 (not_226_out, OP5);
  not not_227 (not_227_out, OP4);
  not not_228 (not_228_out, OP3);
  not not_229 (not_229_out, OP2);
  not not_230 (not_230_out, OP1);
  not not_231 (not_231_out, OP0);
  not not_232 (not_232_out, F4);
  not not_233 (not_233_out, F3);
  not not_234 (not_234_out, F1);
  not not_235 (not_235_out, OP5);
  not not_236 (not_236_out, OP4);
  not not_237 (not_237_out, OP3);
  not not_238 (not_238_out, OP2);
  not not_239 (not_239_out, OP1);
  not not_240 (not_240_out, OP0);
  not not_241 (not_241_out, F4);
  not not_242 (not_242_out, F3);
  not not_243 (not_243_out, OP5);
  not not_244 (not_244_out, OP4);
  not not_245 (not_245_out, OP3);
  not not_246 (not_246_out, OP2);
  not not_247 (not_247_out, OP1);
  not not_248 (not_248_out, OP0);
  not not_249 (not_249_out, F4);
  not not_250 (not_250_out, F2);
  not not_251 (not_251_out, F0);
  not not_252 (not_252_out, OP5);
  not not_253 (not_253_out, OP4);
  not not_254 (not_254_out, OP3);
  not not_255 (not_255_out, OP2);
  not not_256 (not_256_out, OP1);
  not not_257 (not_257_out, OP0);
  not not_258 (not_258_out, F4);
  not not_259 (not_259_out, F2);
  not not_260 (not_260_out, OP5);
  not not_261 (not_261_out, OP4);
  not not_262 (not_262_out, OP3);
  not not_263 (not_263_out, OP2);
  not not_264 (not_264_out, OP1);
  not not_265 (not_265_out, OP0);
  not not_266 (not_266_out, F5);
  not not_267 (not_267_out, F4);
  not not_268 (not_268_out, F1);
  not not_269 (not_269_out, F0);
  not not_270 (not_270_out, OP5);
  not not_271 (not_271_out, OP4);
  not not_272 (not_272_out, OP3);
  not not_273 (not_273_out, OP1);
  not not_274 (not_274_out, OP0);
  not not_275 (not_275_out, OP5);
  not not_276 (not_276_out, OP4);
  not not_277 (not_277_out, OP3);
  not not_278 (not_278_out, OP1);
  not not_279 (not_279_out, OP4);
  not not_280 (not_280_out, OP3);
  not not_281 (not_281_out, OP2);
  not not_282 (not_282_out, OP4);
  not not_283 (not_283_out, OP2);
  and and_1 (and_1_out, not_1_out, not_2_out, not_3_out, not_4_out, not_5_out, not_6_out, not_7_out, not_8_out, not_9_out, not_10_out, F1, F0);
  and and_2 (and_2_out, not_11_out, not_12_out, not_13_out, not_14_out, not_15_out, not_16_out, not_17_out, not_18_out, not_19_out, not_20_out, F1, not_21_out);
  and and_3 (and_3_out, not_22_out, not_23_out, not_24_out, not_25_out, not_26_out, not_27_out, F5, not_28_out, not_29_out, not_30_out, not_31_out, not_32_out);
  and and_4 (and_4_out, not_33_out, not_34_out, not_35_out, not_36_out, not_37_out, not_38_out, F5, not_39_out, not_40_out, not_41_out, not_42_out, F0);
  and and_5 (and_5_out, not_43_out, not_44_out, not_45_out, not_46_out, not_47_out, not_48_out, F5, not_49_out, not_50_out, not_51_out, F1, not_52_out);
  and and_6 (and_6_out, not_53_out, not_54_out, not_55_out, not_56_out, not_57_out, not_58_out, F5, not_59_out, not_60_out, F2, not_61_out, not_62_out);
  and and_7 (and_7_out, not_63_out, not_64_out, not_65_out, not_66_out, not_67_out, not_68_out, F5, not_69_out, not_70_out, F2, not_71_out, F0);
  and and_8 (and_8_out, not_72_out, not_73_out, not_74_out, not_75_out, not_76_out, not_77_out, F5, not_78_out, not_79_out, F2, F1, F0);
  and and_9 (and_9_out, not_80_out, not_81_out, not_82_out, not_83_out, not_84_out, not_85_out, F5, not_86_out, F3, not_87_out, F1, not_88_out);
  and and_10 (and_10_out, not_89_out, not_90_out, not_91_out, not_92_out, not_93_out, not_94_out, F5, not_95_out, F3, not_96_out, F1, F0);
  and and_11 (and_11_out, not_97_out, not_98_out, not_99_out, not_100_out, not_101_out, not_102_out, not_103_out, not_104_out, F3, not_105_out, not_106_out, not_107_out);
  and and_12 (and_12_out, not_108_out, not_109_out, not_110_out, not_111_out, not_112_out, not_113_out, not_114_out, not_115_out, F3, F2, not_116_out, not_117_out);
  and and_13 (and_13_out, not_118_out, not_119_out, not_120_out, OP2, not_121_out, not_122_out);
  and and_14 (and_14_out, not_123_out, not_124_out, not_125_out, OP2, not_126_out, OP0);
  and and_15 (and_15_out, not_127_out, not_128_out, OP3, not_129_out, not_130_out, not_131_out);
  and and_16 (and_16_out, not_132_out, not_133_out, OP3, OP2, not_134_out, not_135_out);
  and and_17 (and_17_out, not_136_out, not_137_out, OP3, not_138_out, not_139_out, OP0);
  and and_18 (and_18_out, not_140_out, not_141_out, OP3, not_142_out, OP1, not_143_out);
  and and_19 (and_19_out, not_144_out, not_145_out, OP3, OP2, not_146_out, OP0);
  and and_20 (and_20_out, OP5, not_147_out, not_148_out, not_149_out, OP1, OP0);
  and and_21 (and_21_out, OP5, not_150_out, OP3, not_151_out, OP1, OP0);
  and and_22 (and_22_out, not_152_out, not_153_out, not_154_out, not_155_out, not_156_out, not_157_out, not_158_out, not_159_out, not_160_out, not_161_out, not_162_out, not_163_out);
  and and_23 (and_23_out, not_164_out, not_165_out, not_166_out, not_167_out, not_168_out, not_169_out, not_170_out, not_171_out, not_172_out, not_173_out, F1, F0);
  and and_24 (and_24_out, not_174_out, not_175_out, not_176_out, not_177_out, not_178_out, not_179_out, not_180_out, not_181_out, not_182_out, not_183_out, F1, not_184_out);
  and and_25 (and_25_out, not_185_out, not_186_out, not_187_out, not_188_out, not_189_out, not_190_out, F5, not_191_out, not_192_out, not_193_out, not_194_out, not_195_out);
  and and_26 (and_26_out, not_196_out, not_197_out, not_198_out, not_199_out, not_200_out, not_201_out, F5, not_202_out, not_203_out, not_204_out, not_205_out, F0);
  and and_27 (and_27_out, not_206_out, not_207_out, not_208_out, not_209_out, not_210_out, not_211_out, F5, not_212_out, not_213_out, not_214_out, F1, not_215_out);
  and and_28 (and_28_out, not_216_out, not_217_out, not_218_out, not_219_out, not_220_out, not_221_out, F5, not_222_out, not_223_out, F2, not_224_out, not_225_out);
  and and_29 (and_29_out, not_226_out, not_227_out, not_228_out, not_229_out, not_230_out, not_231_out, F5, not_232_out, not_233_out, F2, not_234_out, F0);
  and and_30 (and_30_out, not_235_out, not_236_out, not_237_out, not_238_out, not_239_out, not_240_out, F5, not_241_out, not_242_out, F2, F1, F0);
  and and_31 (and_31_out, not_243_out, not_244_out, not_245_out, not_246_out, not_247_out, not_248_out, F5, not_249_out, F3, not_250_out, F1, not_251_out);
  and and_32 (and_32_out, not_252_out, not_253_out, not_254_out, not_255_out, not_256_out, not_257_out, F5, not_258_out, F3, not_259_out, F1, F0);
  and and_33 (and_33_out, not_260_out, not_261_out, not_262_out, not_263_out, not_264_out, not_265_out, not_266_out, not_267_out, F3, F2, not_268_out, not_269_out);
  and and_34 (and_34_out, not_270_out, not_271_out, not_272_out, OP2, not_273_out, not_274_out);
  and and_35 (and_35_out, not_275_out, not_276_out, not_277_out, OP2, not_278_out, OP0);
  and and_36 (and_36_out, OP5, not_279_out, not_280_out, not_281_out, OP1, OP0);
  and and_37 (and_37_out, OP5, not_282_out, OP3, not_283_out, OP1, OP0);
  or or_1 (R1_used, and_1_out, and_2_out, and_3_out, and_4_out, and_5_out, and_6_out, and_7_out, and_8_out, and_9_out, and_10_out, and_11_out, and_12_out, and_13_out, and_14_out, and_15_out, and_16_out, and_17_out, and_18_out, and_19_out, and_20_out, and_21_out);
  or or_2 (R2_used, and_22_out, and_23_out, and_24_out, and_25_out, and_26_out, and_27_out, and_28_out, and_29_out, and_30_out, and_31_out, and_32_out, and_33_out, and_34_out, and_35_out, and_36_out, and_37_out);
endmodule

module \数据相关检测  (
  input  [5:0] OP,
  input  [5:0] Func,
  input  [4:0] MEM_WriteReg,
  input  [4:0] EX_WriteReg,
  input  MEM_RegWrite,
  input  [4:0] R2_ID,
  input  EX_RegWrite,
  input  [4:0] R1_ID,
  output stall
);

  wire and_1_out, and_2_out, and_3_out, and_4_out, and_5_out, and_6_out, and_7_out, and_8_out,
       comparator_1_eq, comparator_2_eq, comparator_3_eq, comparator_4_eq, comparator_5_eq, comparator_6_eq,
       not_1_out, not_2_out, or_1_out, or_2_out, R1_used, R2_used;

  \源寄存器使用情况  \u_源寄存器使用情况_1  (
    .OP0(OP[0]), .OP1(OP[1]), .OP2(OP[2]), .OP3(OP[3]), .OP4(OP[4]), .OP5(OP[5]), .F0(Func[0]), .F1(Func[1]),
    .F2(Func[2]), .F3(Func[3]), .F4(Func[4]), .F5(Func[5]), .R1_used(R1_used), .R2_used(R2_used));
  Comparator #(.width(5), .mode("twosComplement")) comparator_1 (
    .a(EX_WriteReg), .b(R1_ID), .eq(comparator_1_eq));  // open: gt, lt
  Comparator #(.width(5), .mode("twosComplement")) comparator_2 (
    .a(MEM_WriteReg), .b(R1_ID), .eq(comparator_2_eq));  // open: gt, lt
  Comparator #(.width(5), .mode("twosComplement")) comparator_3 (
    .a(EX_WriteReg), .b(R2_ID), .eq(comparator_3_eq));  // open: gt, lt
  Comparator #(.width(5), .mode("twosComplement")) comparator_4 (
    .a(MEM_WriteReg), .b(R2_ID), .eq(comparator_4_eq));  // open: gt, lt
  and and_1 (and_1_out, EX_RegWrite, comparator_1_eq);
  and and_2 (and_2_out, EX_RegWrite, comparator_3_eq);
  Comparator #(.width(5), .mode("twosComplement")) comparator_5 (
    .a(R2_ID), .b({5{1'b0}}), .eq(comparator_5_eq));  // open: gt, lt
  Comparator #(.width(5), .mode("twosComplement")) comparator_6 (
    .a(R1_ID), .b({5{1'b0}}), .eq(comparator_6_eq));  // open: gt, lt
  and and_3 (and_3_out, MEM_RegWrite, comparator_2_eq);
  and and_4 (and_4_out, MEM_RegWrite, comparator_4_eq);
  not not_1 (not_1_out, comparator_5_eq);
  not not_2 (not_2_out, comparator_6_eq);
  or or_1 (or_1_out, and_1_out, and_3_out);
  or or_2 (or_2_out, and_2_out, and_4_out);
  and and_5 (and_5_out, R1_used, or_1_out);
  and and_6 (and_6_out, R2_used, or_2_out);
  and and_7 (and_7_out, and_6_out, not_1_out);
  and and_8 (and_8_out, not_2_out, and_5_out);
  or or_3 (stall, and_8_out, and_7_out);
endmodule
module \封装正确性测试  (
);

  wire IR1, IR2, IR3, MemW, RegW;
  wire [31:0] EX_PC, ID_PC, IF_PC, IR, LED, MDin, MDinr, MEM_PC, PC, RDin, RDinr, WB_PC;

  \单周期MIPS  \u_单周期mips_1  (
    .RegWrite(RegW), .MemWrite(MemW), .PC(PC), .IR(IR), .RDin(RDin), .MDin(MDin), .LedData(LED));  // open: IR1, IR2, IR3
  \气泡流水线  \u_气泡流水线_1  (
    .RegWrite(RegW), .MemWrite(MemW), .IF_PC(IF_PC), .ID_PC(ID_PC), .EX_PC(EX_PC), .M_PC(MEM_PC),
    .WB_PC(WB_PC), .RDin(RDinr), .MDin(MDinr), .LedData(LED));
  \单周期MIPS_单级中断  \u_单周期mips_单级中断_1  (
    .IR1(IR1), .IR2(IR2), .IR3(IR3), .RegWrite(RegW), .MemWrite(MemW), .PC(PC), .IR(IR), .RDin(RDin),
    .MDin(MDin), .LedData(LED));
  \理想流水线  \u_理想流水线_1  (
    .RegWrite(RegW), .MemWrite(MemW), .IF_PC(IF_PC), .ID_PC(ID_PC), .EX_PC(EX_PC), .M_PC(MEM_PC),
    .WB_PC(WB_PC), .RDin(RDinr), .MDin(MDinr), .LedData(LED));
  \气泡流水线  \u_气泡流水线_2  (
    .RegWrite(RegW), .MemWrite(MemW), .IF_PC(IF_PC), .ID_PC(ID_PC), .EX_PC(EX_PC), .M_PC(MEM_PC),
    .WB_PC(WB_PC), .RDin(RDinr), .MDin(MDinr), .LedData(LED));
  \单周期MIPS_多级中断  \u_单周期mips_多级中断_1  (
    .IR1(IR1), .IR2(IR2), .IR3(IR3), .RegWrite(RegW), .MemWrite(MemW), .PC(PC), .IR(IR), .RDin(RDin),
    .MDin(MDin), .LedData(LED));

  // Notes on the sheet:
  //   单周期封装测试
  //   气泡流水封装测试
  //   单周期+单级中断封装测试
  //   请检查上面封装有无位宽不匹配，引脚标签是否和连接的标签相对应，否则无法在educoder平台上正确测试
  //   理想流水封装测试
  //   重定向流水封装测试
  //   单周期+多级中断封装测试
endmodule

module \重定向检测  (
  input  [5:0] OP,
  input  [5:0] Func,
  input  MEM_memtoreg,
  input  EX_memtoreg,
  input  [4:0] MEM_WriteReg,
  input  [4:0] EX_WriteReg,
  input  MEM_RegWrite,
  input  [4:0] R2_ID,
  input  EX_RegWrite,
  input  [4:0] R1_ID,
  output [1:0] forwardToR1,
  output loaduse,
  output [1:0] forwardToR2
);

  wire and_1_out, and_2_out, and_3_out, and_4_out, comparator_1_eq, comparator_2_eq, comparator_3_eq,
       comparator_4_eq, comparator_5_eq, comparator_6_eq, comparator_7_eq, comparator_8_eq, not_1_out,
       not_2_out, not_3_out, not_4_out, R1_loaduse, R1_memdata, R1_used, R2_loaduse, R2_memdata, R2_used;
  wire [1:0] multiplexer_1_out, multiplexer_2_out, multiplexer_3_out, multiplexer_4_out;

  \源寄存器使用情况  \u_源寄存器使用情况_1  (
    .OP0(OP[0]), .OP1(OP[1]), .OP2(OP[2]), .OP3(OP[3]), .OP4(OP[4]), .OP5(OP[5]), .F0(Func[0]), .F1(Func[1]),
    .F2(Func[2]), .F3(Func[3]), .F4(Func[4]), .F5(Func[5]), .R1_used(R1_used), .R2_used(R2_used));
  Comparator #(.width(5), .mode("twosComplement")) comparator_1 (
    .a(R1_ID), .b({5{1'b0}}), .eq(comparator_1_eq));  // open: gt, lt
  Comparator #(.width(5), .mode("twosComplement")) comparator_2 (
    .a(R1_ID), .b(EX_WriteReg), .eq(comparator_2_eq));  // open: gt, lt
  Comparator #(.width(5), .mode("twosComplement")) comparator_3 (
    .a(R1_ID), .b({5{1'b0}}), .eq(comparator_3_eq));  // open: gt, lt
  Comparator #(.width(5), .mode("twosComplement")) comparator_4 (
    .a(R1_ID), .b(MEM_WriteReg), .eq(comparator_4_eq));  // open: gt, lt
  not not_1 (not_1_out, comparator_5_eq);
  Comparator #(.width(5), .mode("twosComplement")) comparator_5 (
    .a(R2_ID), .b({5{1'b0}}), .eq(comparator_5_eq));  // open: gt, lt
  Comparator #(.width(5), .mode("twosComplement")) comparator_6 (
    .a(R2_ID), .b(EX_WriteReg), .eq(comparator_6_eq));  // open: gt, lt
  not not_2 (not_2_out, comparator_7_eq);
  Comparator #(.width(5), .mode("twosComplement")) comparator_7 (
    .a(R2_ID), .b({5{1'b0}}), .eq(comparator_7_eq));  // open: gt, lt
  Comparator #(.width(5), .mode("twosComplement")) comparator_8 (
    .a(R2_ID), .b(MEM_WriteReg), .eq(comparator_8_eq));  // open: gt, lt
  not not_3 (not_3_out, comparator_1_eq);
  not not_4 (not_4_out, comparator_3_eq);
  and and_1 (and_1_out, not_1_out, comparator_6_eq, R2_used, EX_RegWrite);
  and and_2 (and_2_out, not_3_out, comparator_2_eq, R1_used, EX_RegWrite);
  and and_3 (and_3_out, not_4_out, comparator_4_eq, R1_used, MEM_RegWrite);
  and and_4 (and_4_out, not_2_out, comparator_8_eq, R2_used, MEM_RegWrite);
  Multiplexer #(.select(1), .width(2), .disabled("Z"), .enable("false")) multiplexer_1 (
    .in0(2'b00), .in1(2'b10), .out(multiplexer_1_out), .sel(and_4_out));
  Multiplexer #(.select(1), .width(2), .disabled("Z"), .enable("false")) multiplexer_2 (
    .in0(2'b00), .in1(2'b10), .out(multiplexer_2_out), .sel(and_3_out));
  and and_5 (R1_loaduse, and_2_out, EX_memtoreg);
  and and_6 (R1_memdata, and_3_out, MEM_memtoreg);
  and and_7 (R2_loaduse, and_1_out, EX_memtoreg);
  Multiplexer #(.select(1), .width(2), .disabled("Z"), .enable("false")) multiplexer_3 (
    .in0(multiplexer_1_out), .in1(2'b01), .out(multiplexer_3_out), .sel(R2_memdata));
  and and_8 (R2_memdata, and_4_out, MEM_memtoreg);
  Multiplexer #(.select(1), .width(2), .disabled("Z"), .enable("false")) multiplexer_4 (
    .in0(multiplexer_2_out), .in1(2'b01), .out(multiplexer_4_out), .sel(R1_memdata));
  or or_1 (loaduse, R1_loaduse, R2_loaduse);
  Multiplexer #(.select(1), .width(2), .disabled("Z"), .enable("false")) multiplexer_5 (
    .in0(multiplexer_3_out), .in1(2'b11), .out(forwardToR2), .sel(and_1_out));
  Multiplexer #(.select(1), .width(2), .disabled("Z"), .enable("false")) multiplexer_6 (
    .in0(multiplexer_4_out), .in1(2'b11), .out(forwardToR1), .sel(and_2_out));
endmodule

module \中断信号采样电路  (
  input  clk,
  input  \_1号中断信号 ,
  input  \同步清零信号 ,
  output \与中断屏蔽位与 ,
  output \中断等待指示灯 
);

  wire and_1_out, d_ff_1_q, or_2_out;

  or or_1 (\中断等待指示灯 , \与中断屏蔽位与 , d_ff_1_q);
  D_Flip_Flop #(.trigger("rising"), .Pre_Clr_Positions("LEGACY"), .NegatePresetClear("false"), .enable("true"), .NewFFLayout("false")) d_ff_1 (
    .clk(\_1号中断信号 ), .D(1'b1), .Q(d_ff_1_q), .reset(\与中断屏蔽位与 ));  // open: Qn, preset, en
  or or_2 (or_2_out, d_ff_1_q, \与中断屏蔽位与 );
  and and_1 (and_1_out, or_2_out, ~\同步清零信号 );  // AND_Gate
  D_Flip_Flop #(.trigger("rising"), .Pre_Clr_Positions("LEGACY"), .NegatePresetClear("false"), .enable("true"), .NewFFLayout("false")) IR1 (
    .clk(clk), .D(and_1_out), .Q(\与中断屏蔽位与 ));  // open: Qn, preset, en, reset

  // Notes on the sheet:
  //   中断信号采样参考电路
  //   Reset 
endmodule
